// Logisim project 2402CS11_Lab10_anjneyLawaniya.circ as structural Verilog: 12 circuits, main circuit main
module main (
  input  in_1
);

  wire ALUSrcD, ALUSrcE, BranchD, brnchStl, clear, clk, clkA, clkB, clock_1_out, comparator_1_eq, FlushD,
       FlushE, FrwdAD, FrwdBD, isBranch, JalD, jalE, jalM, jalW, jrD, JumpD, lwStl, memClear, MemToRegD,
       MemToRegE, MemToRegM, MemToRegW, MemWriteD, MemWriteE, MemWriteM, or_1_out, regClear, RegWriteD,
       RegWriteE, RegWriteM, RegWriteW, stallD, stallF;
  wire [1:0] FrwdAE, FrwdBE, RegDstD, RegDstE;
  wire [2:0] ALUCtrlD, ALUCtrlE;
  wire [4:0] DstE, DstM, DstW, rdD, rdE, rsD, rsE, rtD, rtE;
  wire [5:0] instructionsplitter_1_func, instructionsplitter_1_opcode;
  wire [15:0] instructionsplitter_1_out_4;
  wire [23:0] shifter_1_out, shifter_3_out;
  wire [25:0] instructionsplitter_1_out_5;
  wire [31:0] ALUResE, ALUResM, ALUResW, BrnchTrgD, if_id_1_out_7, immD, immE, jAddD, jaddressmaker_1_out_3,
       jrFrwdAdd, multiplexer_1_out, multiplexer_2_out, multiplexer_3_out, multiplexer_7_out,
       multiplexer_9_out, multiplexer_11_out, multiplexer_13_out, n32x32regfile_1_out_8,
       n32x32regfile_1_out_9, PC_4D, PC_4E, PC_4F, PC_4M, PC_4W, ReadDataM, ReadDataW, register_1_q, ResW,
       rom_1_data, rsValD, rsValE, rtValD, rtValE, shifter_2_out, WriteDataE, WriteDataM;

  Clock clock_1 (.out(clock_1_out));
  Button button_1 ();  // open: out
  or or_1 (or_1_out, JumpD, jrD, JalD);
  Multiplexer #(.width(32)) multiplexer_1 (
    .in0(PC_4F), .in1(BrnchTrgD), .out(multiplexer_1_out), .sel(isBranch));  // open: en
  Multiplexer #(.width(32)) multiplexer_2 (
    .in0(multiplexer_1_out), .in1(jAddD), .out(multiplexer_2_out), .sel(or_1_out));  // open: en
  or or_2 (clk, clock_1_out, clkA, clkB);
  Multiplexer #(.width(32)) multiplexer_3 (
    .in0(multiplexer_2_out), .in1(register_1_q), .out(multiplexer_3_out), .sel(stallF));  // open: en
  Register #(.width(32)) register_1 (.D(multiplexer_3_out), .Q(register_1_q), .clk(clk), .clr(clear));  // open: en
  Button button_2 (.out(regClear));
  Button button_3 (.out(memClear));
  Button button_4 (.out(clear));
  Shifter #(.width(24), .shift("lr")) shifter_1 (.in(register_1_q[23:0]), .\dist (5'b00010), .out(shifter_1_out));
  Adder #(.width(32)) adder_1 (.a(register_1_q), .b(32'h4), .out(PC_4F));  // open: cin, cout
  LED led_1 (.in(clk));
  IF_ID if_id_1 (
    .in_1(rom_1_data), .in_2(PC_4F), .out_7(if_id_1_out_7), .out_8(PC_4D), .stall(stallD), .clk(clk),
    .clear(clear), .FlushD(FlushD));
  ROM #(.addrWidth(24), .dataWidth(32)) rom_1 (.addr(shifter_1_out), .data(rom_1_data));  // open: sel
  InstructionSplitter instructionsplitter_1 (
    .in_1(if_id_1_out_7), .Func(instructionsplitter_1_func), .out_4(instructionsplitter_1_out_4),
    .out_5(instructionsplitter_1_out_5), .rd(rdD), .rt(rtD), .rs(rsD), .opCode(instructionsplitter_1_opcode));  // open: shamt
  Shifter #(.width(32)) shifter_2 (.in(immD), .\dist (5'b00010), .out(shifter_2_out));
  Control_Unit control_unit_1 (
    .OpCode(instructionsplitter_1_opcode), .jr(jrD), .Funct(instructionsplitter_1_func),
    .RegWrite(RegWriteD), .ALUSrc(ALUSrcD), .Branch(BranchD), .MemWrite(MemWriteD), .MemToReg(MemToRegD),
    .Jump(JumpD), .Jal(JalD), .ALU_Control(ALUCtrlD), .RegDst(RegDstD));
  jAddressMaker jaddressmaker_1 (.in_1(PC_4D), .in_2(instructionsplitter_1_out_5), .out_3(jaddressmaker_1_out_3));
  Adder #(.width(32)) adder_2 (.a(PC_4D), .b(shifter_2_out), .out(BrnchTrgD));  // open: cin, cout
  Comparator #(.width(32)) comparator_1 (.a(rsValD), .b(rtValD), .eq(comparator_1_eq));  // open: gt, lt
  _32X32RegFile u_32x32regfile_1 (
    .Read_B(rtD), .Read_A(rsD), .in_3(RegWriteW), .Selection(DstW), .out_8(n32x32regfile_1_out_8),
    .out_9(n32x32regfile_1_out_9), .in_7(ResW), .in_5(regClear), .in_6(clk));
  assign immD = {{16{instructionsplitter_1_out_4[15]}}, instructionsplitter_1_out_4};  // Bit_Extender bit_extender_1
  Multiplexer #(.width(32)) multiplexer_4 (
    .in0(jaddressmaker_1_out_3), .in1(jrFrwdAdd), .out(jAddD), .sel(jrD));  // open: en
  and and_1 (isBranch, BranchD, comparator_1_eq);
  Multiplexer #(.width(32)) multiplexer_5 (
    .in0(n32x32regfile_1_out_8), .in1(ALUResM), .out(rsValD), .sel(FrwdAD));  // open: en
  Multiplexer #(.width(32)) multiplexer_6 (
    .in0(n32x32regfile_1_out_9), .in1(ALUResM), .out(rtValD), .sel(FrwdBD));  // open: en
  Hazard_Unit_Og hazard_unit_og_1 (
    .rsD(rsD), .rtD(rtD), .rsE(rsE), .rtE(rtE), .DestinationE(DstE), .DestinationM(DstM),
    .DestinationW(DstW), .RegWriteM(RegWriteM), .RegWriteW(RegWriteW), .MemToRegE(MemToRegE),
    .BranchD(BranchD), .RegWriteE(RegWriteE), .MemToRegM(MemToRegM), .ForwardBE(FrwdBE), .ForwardAE(FrwdAE),
    .ForwardAD(FrwdAD), .ForwardBD(FrwdBD), .branchStall(brnchStl), .lwStall(lwStl), .StallF(stallF),
    .StallD(stallD), .FlushE(FlushE), .isBranch(isBranch), .jD(JumpD), .jrD(jrD), .jalD(JalD), .FlushD(FlushD));
  ID_EX id_ex_1 (
    .RegWriteD(RegWriteD), .in_2(PC_4D), .in_3(rsValD), .RegDstD(RegDstD), .rsD(rsD), .ALUSrcD(ALUSrcD),
    .in_7(rtValD), .rtD(rtD), .BranchD(BranchD), .rdD(rdD), .MemWriteD(MemWriteD), .MemToRegD(MemToRegD),
    .JumpD(JumpD), .JalD(JalD), .in_16(immD), .JrD(jrD), .in_18(jAddD), .ALUCtrlD(ALUCtrlD),
    .RegWriteE(RegWriteE), .out_25(PC_4E), .out_26(rsValE), .RegDstE(RegDstE), .rsE(rsE), .ALUSrcE(ALUSrcE),
    .out_30(rtValE), .rtE(rtE), .rdE(rdE), .JalE(jalE), .out_39(immE), .ALUICtrlE(ALUCtrlE), .stall(1'b0),
    .clk(clk), .FlushE(FlushE), .clear(clear), .MemWriteE(MemWriteE), .MemToRegE(MemToRegE));  // open: in_13, BranchE, out_36, JumpE, JrE, out_41
  Multiplexer #(.select(2), .width(32)) multiplexer_7 (
    .in0(rsValE), .in1(ResW), .in2(ALUResM), .in3(ReadDataM), .out(multiplexer_7_out), .sel(FrwdAE));  // open: en
  Multiplexer #(.select(2), .width(32)) multiplexer_8 (
    .in0(rtValE), .in1(ResW), .in2(ALUResM), .in3(ReadDataM), .out(WriteDataE), .sel(FrwdBE));  // open: en
  Multiplexer #(.width(32)) multiplexer_9 (
    .in0(WriteDataE), .in1(immE), .out(multiplexer_9_out), .sel(ALUSrcE));  // open: en
  Button button_5 (.out(clkA));
  Multiplexer #(.width(32)) multiplexer_10 (
    .in0(multiplexer_11_out), .in1(PC_4M), .out(jrFrwdAdd), .sel(jalM));  // open: en
  Multiplexer #(.width(32)) multiplexer_11 (
    .in0(rsValD), .in1(PC_4W), .out(multiplexer_11_out), .sel(jalW));  // open: en
  ALU alu_1 (.in_1(multiplexer_7_out), .in_2(multiplexer_9_out), .out_5(ALUResE), .OpCode(ALUCtrlE));  // open: isZero
  Multiplexer #(.select(2), .width(5)) multiplexer_12 (
    .in0(rtE), .in1(rdE), .in2({5{1'b1}}), .out(DstE), .sel(RegDstE));  // open: in3, en
  LED led_2 (.in(clk));
  EX_MEM ex_mem_1 (
    .in_3(PC_4E), .DestinationE(DstE), .in_6(WriteDataE), .MemWriteE(MemWriteE), .in_8(ALUResE),
    .RegWriteE(RegWriteE), .MemToRegE(MemToRegE), .JalE(jalE), .out_21(PC_4M), .DestinationM(DstM),
    .out_24(WriteDataM), .MemWriteM(MemWriteM), .out_26(ALUResM), .RegWriteM(RegWriteM),
    .MemToRegM(MemToRegM), .JalM(jalM), .stall(1'b0), .clk(clk), .clear(clear));  // open: in_1, in_2, in_4, ZeroBitE, jE, jrE, BranchE, out_19, out_20, out_22, ZeroBitM, jM, jrM, BranchM
  Shifter #(.width(24), .shift("lr")) shifter_3 (.in(ALUResM[23:0]), .\dist (5'b00010), .out(shifter_3_out));
  LED led_3 (.in(clk));
  RAM #(.addrWidth(24), .dataWidth(32), .bus("separate")) ram_1 (
    .addr(shifter_3_out), .din(WriteDataM), .data(ReadDataM), .str(MemWriteM), .ld(MemToRegM), .clr(memClear));  // open: sel, clk
  MEM_WB mem_wb_1 (
    .in_2(ALUResM), .in_3(ReadDataM), .in_5(PC_4M), .JalM(jalM), .RegWriteM(RegWriteM), .DestinationM(DstM),
    .MemToRegtM(MemToRegM), .out_16(ALUResW), .out_17(ReadDataW), .out_19(PC_4W), .JalW(jalW),
    .RegWriteW(RegWriteW), .DestinationW(DstW), .MemToRegtW(MemToRegW), .stall(1'b0), .clk(clk), .clear(clear));  // open: in_1, jM, in_6, JrM, out_15, jW, out_20, JrW
  Button button_6 (.out(clkB));
  Multiplexer #(.width(32)) multiplexer_13 (
    .in0(ALUResW), .in1(PC_4W), .out(multiplexer_13_out), .sel(jalW));  // open: en
  Multiplexer #(.width(32)) multiplexer_14 (
    .in0(multiplexer_13_out), .in1(ReadDataW), .out(ResW), .sel(MemToRegW));  // open: en

  // Notes on the sheet:
  //   clk
  //   RegClear
  //   MemClear
  //   clear
  //   clkA
  //   clkB
endmodule

module Control_Unit (
  input  [5:0] OpCode,
  input  [5:0] Funct,
  output RegWrite,
  output [1:0] RegDst,
  output ALUSrc,
  output Branch,
  output jr,
  output MemWrite,
  output MemToReg,
  output Jump,
  output Jal,
  output [2:0] ALU_Control
);

  wire and_3_out, and_4_out, comparator_1_eq, comparator_2_eq, not_1_out, not_2_out, not_3_out, not_4_out,
       not_5_out, not_6_out, not_7_out, not_8_out, not_9_out, not_10_out;
  wire [1:1] and_7_out;

  Comparator #(.width(6)) comparator_1 (.a(OpCode), .b({6{1'b0}}), .eq(comparator_1_eq));  // open: gt, lt
  and and_1 (jr, comparator_1_eq, comparator_2_eq);
  Comparator #(.width(6)) comparator_2 (.a(Funct), .b(6'b001000), .eq(comparator_2_eq));  // open: gt, lt
  not not_1 (not_1_out, OpCode[2]);
  not not_2 (not_2_out, OpCode[1]);
  not not_3 (not_3_out, OpCode[3]);
  not not_4 (not_4_out, OpCode[3]);
  not not_5 (not_5_out, OpCode[2]);
  not not_6 (not_6_out, OpCode[1]);
  or or_1 (ALUSrc, OpCode[3], OpCode[5]);
  and and_2 (MemWrite, OpCode[5], OpCode[3]);
  not not_7 (not_7_out, OpCode[3]);
  not not_8 (not_8_out, OpCode[3]);
  not not_9 (not_9_out, OpCode[2]);
  not not_10 (not_10_out, OpCode[1]);
  and and_3 (and_3_out, not_1_out, not_2_out);
  and and_4 (and_4_out, not_3_out, OpCode[0]);
  and and_5 (RegDst[0], not_4_out, not_5_out, not_6_out);
  and and_6 (MemToReg, OpCode[5], not_7_out);
  and and_7 (and_7_out[1], not_8_out, not_9_out, not_10_out);
  or or_2 (RegWrite, and_3_out, and_4_out);
  Comparator #(.width(6), .mode("unsigned")) comparator_3 (.a(6'b000010), .b(OpCode), .eq(Jump));  // open: gt, lt
  Comparator #(.width(6)) comparator_4 (.a(OpCode), .b(6'b000011), .eq(Jal));  // open: gt, lt
  ALU_Decoder_Truly alu_decoder_truly_1 (.ALUOp({and_7_out[1], OpCode[2]}), .Funct(Funct), .ALUControl(ALU_Control));

  assign Branch = OpCode[2];
  assign RegDst[1] = Jal;

  // Notes on the sheet:
  //   00 -> rt
  //   01 -> rd
  //   10 -> $ra
endmodule

module ALU_Decoder_Truly (
  input  [1:0] ALUOp,
  input  [5:0] Funct,
  output [2:0] ALUControl
);

  wire and_1_out, and_2_out, and_3_out, not_1_out, not_2_out;

  and and_1 (and_1_out, ALUOp[1], Funct[1]);
  not not_1 (not_1_out, ALUOp[1]);
  not not_2 (not_2_out, Funct[2]);
  and and_2 (and_2_out, ALUOp[1], Funct[0]);
  and and_3 (and_3_out, ALUOp[1], Funct[3]);
  or or_1 (ALUControl[2], ALUOp[0], and_1_out);
  or or_2 (ALUControl[1], not_1_out, not_2_out);
  or or_3 (ALUControl[0], and_2_out, and_3_out);
endmodule

module IF_ID (
  input  [31:0] in_1,
  input  [31:0] in_2,
  input  FlushD,
  input  stall,
  input  clk,
  input  clear,
  output [31:0] out_7,
  output [31:0] out_8
);

  wire not_1_out;
  wire [31:0] multiplexer_1_out;

  Multiplexer #(.width(32)) multiplexer_1 (
    .in0(in_1), .in1({32{1'b0}}), .out(multiplexer_1_out), .sel(FlushD));  // open: en
  not not_1 (not_1_out, stall);
  Register #(.width(32)) register_1 (.D(multiplexer_1_out), .en(not_1_out), .Q(out_7), .clk(clk), .clr(clear));
  Register #(.width(32)) register_2 (.D(in_2), .en(not_1_out), .Q(out_8), .clk(clk), .clr(clear));

  // Notes on the sheet:
  //   InstID
  //   PC+4IF
  //   PC
  //   InstD
  //   PC+4D
endmodule

module ID_EX (
  input  RegWriteD,
  input  [31:0] in_2,
  input  [31:0] in_3,
  input  [1:0] RegDstD,
  input  [4:0] rsD,
  input  ALUSrcD,
  input  [31:0] in_7,
  input  [4:0] rtD,
  input  BranchD,
  input  [4:0] rdD,
  input  MemWriteD,
  input  MemToRegD,
  input  [31:0] in_13,
  input  JumpD,
  input  JalD,
  input  [31:0] in_16,
  input  JrD,
  input  [31:0] in_18,
  input  [2:0] ALUCtrlD,
  input  clk,
  input  stall,
  input  clear,
  input  FlushE,
  output RegWriteE,
  output [31:0] out_25,
  output [31:0] out_26,
  output [1:0] RegDstE,
  output [4:0] rsE,
  output ALUSrcE,
  output [31:0] out_30,
  output [4:0] rtE,
  output BranchE,
  output [4:0] rdE,
  output MemWriteE,
  output MemToRegE,
  output [31:0] out_36,
  output JumpE,
  output JalE,
  output [31:0] out_39,
  output JrE,
  output [31:0] out_41,
  output [2:0] ALUICtrlE
);

  wire and_1_out, and_2_out, and_3_out, not_1_out, NotFlush;

  and and_1 (and_1_out, NotFlush, MemWriteD);
  and and_2 (and_2_out, NotFlush, RegWriteD);
  Register #(.width(1)) register_1 (.D(and_2_out), .en(not_1_out), .Q(RegWriteE), .clk(clk), .clr(clear));
  Register #(.width(2)) register_2 (.D(RegDstD), .en(not_1_out), .Q(RegDstE), .clk(clk), .clr(clear));
  Register #(.width(1)) register_3 (.D(ALUSrcD), .en(not_1_out), .Q(ALUSrcE), .clk(clk), .clr(clear));
  Register #(.width(1)) register_4 (.D(BranchD), .en(not_1_out), .Q(BranchE), .clk(clk), .clr(clear));
  Register #(.width(1)) register_5 (.D(and_1_out), .en(not_1_out), .Q(MemWriteE), .clk(clk), .clr(clear));
  and and_3 (and_3_out, NotFlush, MemToRegD);
  Register #(.width(1)) register_6 (.D(and_3_out), .en(not_1_out), .Q(MemToRegE), .clk(clk), .clr(clear));
  Register #(.width(1)) register_7 (.D(JumpD), .en(not_1_out), .Q(JumpE), .clk(clk), .clr(clear));
  Register #(.width(1)) register_8 (.D(JalD), .en(not_1_out), .Q(JalE), .clk(clk), .clr(clear));
  Register #(.width(1)) register_9 (.D(JrD), .en(not_1_out), .Q(JrE), .clk(clk), .clr(clear));
  Register #(.width(3)) register_10 (.D(ALUCtrlD), .en(not_1_out), .Q(ALUICtrlE), .clk(clk), .clr(clear));
  not not_1 (not_1_out, stall);
  Register #(.width(32)) register_11 (.D(in_2), .en(not_1_out), .Q(out_25), .clk(clk), .clr(clear));
  Register #(.width(5)) register_12 (.D(rsD), .en(not_1_out), .Q(rsE), .clk(clk), .clr(clear));
  Register #(.width(5)) register_13 (.D(rtD), .en(not_1_out), .Q(rtE), .clk(clk), .clr(clear));
  Register #(.width(5)) register_14 (.D(rdD), .en(not_1_out), .Q(rdE), .clk(clk), .clr(clear));
  Register #(.width(32)) register_15 (.D(in_13), .en(not_1_out), .Q(out_36), .clk(clk), .clr(clear));
  Register #(.width(32)) register_16 (.D(in_16), .en(not_1_out), .Q(out_39), .clk(clk), .clr(clear));
  Register #(.width(32)) register_17 (.D(in_18), .en(not_1_out), .Q(out_41), .clk(clk), .clr(clear));
  not not_2 (NotFlush, FlushE);
  Register #(.width(32)) register_18 (.D(in_3), .en(not_1_out), .Q(out_26), .clk(clk), .clr(clear));
  Register #(.width(32)) register_19 (.D(in_7), .en(not_1_out), .Q(out_30), .clk(clk), .clr(clear));

  // Notes on the sheet:
  //   jAddD
  //   PC+4D
  //   shamtD
  //   immD
  //   PC+4E
  //   shamtE
  //   immE
  //   jAddE
  //   rsValD
  //   rtValD
  //   rsValE
  //   rtValE
endmodule

module EX_MEM (
  input  [31:0] in_1,
  input  [31:0] in_2,
  input  [31:0] in_3,
  input  [31:0] in_4,
  input  [4:0] DestinationE,
  input  [31:0] in_6,
  input  MemWriteE,
  input  [31:0] in_8,
  input  RegWriteE,
  input  MemToRegE,
  input  ZeroBitE,
  input  JalE,
  input  jE,
  input  jrE,
  input  BranchE,
  input  clk,
  input  clear,
  input  stall,
  output [31:0] out_19,
  output [31:0] out_20,
  output [31:0] out_21,
  output [31:0] out_22,
  output [4:0] DestinationM,
  output [31:0] out_24,
  output MemWriteM,
  output [31:0] out_26,
  output RegWriteM,
  output MemToRegM,
  output ZeroBitM,
  output JalM,
  output jM,
  output jrM,
  output BranchM
);

  wire not_1_out;

  Register #(.width(32)) register_1 (.D(in_1), .en(not_1_out), .Q(out_19), .clk(clk), .clr(clear));
  Register #(.width(32)) register_2 (.D(in_3), .en(not_1_out), .Q(out_21), .clk(clk), .clr(clear));
  Register #(.width(32)) register_3 (.D(in_6), .en(not_1_out), .Q(out_24), .clk(clk), .clr(clear));
  Register #(.width(32)) register_4 (.D(in_8), .en(not_1_out), .Q(out_26), .clk(clk), .clr(clear));
  Register #(.width(1)) register_5 (.D(ZeroBitE), .en(not_1_out), .Q(ZeroBitM), .clk(clk), .clr(clear));
  Register #(.width(1)) register_6 (.D(BranchE), .en(not_1_out), .Q(BranchM), .clk(clk), .clr(clear));
  Register #(.width(32)) register_7 (.D(in_2), .en(not_1_out), .Q(out_20), .clk(clk), .clr(clear));
  Register #(.width(32)) register_8 (.D(in_4), .en(not_1_out), .Q(out_22), .clk(clk));  // open: clr
  Register #(.width(5)) register_9 (.D(DestinationE), .en(not_1_out), .Q(DestinationM), .clk(clk));  // open: clr
  Register #(.width(1)) register_10 (.D(MemWriteE), .en(not_1_out), .Q(MemWriteM), .clk(clk));  // open: clr
  Register #(.width(1)) register_11 (.D(RegWriteE), .en(not_1_out), .Q(RegWriteM), .clk(clk));  // open: clr
  Register #(.width(1)) register_12 (.D(JalE), .en(not_1_out), .Q(JalM), .clk(clk));  // open: clr
  Register #(.width(1)) register_13 (.D(jE), .en(not_1_out), .Q(jM), .clk(clk), .clr(clear));
  not not_1 (not_1_out, stall);
  Register #(.width(1)) register_14 (.D(MemToRegE), .en(not_1_out), .Q(MemToRegM), .clk(clk), .clr(clear));
  Register #(.width(1)) register_15 (.D(jrE), .en(not_1_out), .Q(jrM), .clk(clk), .clr(clear));

  // Notes on the sheet:
  //   rsValE
  //   PC+4E
  //   rtValE
  //   ALUResE
  //   rsValM
  //   PC+4M
  //   rtValM
  //   ALUResM
  //   BranchAddrE
  //   jAddrE
  //   BranchAddM
  //   jAddrM
endmodule

module MEM_WB (
  input  [31:0] in_1,
  input  [31:0] in_2,
  input  [31:0] in_3,
  input  jM,
  input  [31:0] in_5,
  input  [31:0] in_6,
  input  JalM,
  input  RegWriteM,
  input  [4:0] DestinationM,
  input  JrM,
  input  MemToRegtM,
  input  clk,
  input  clear,
  input  stall,
  output [31:0] out_15,
  output [31:0] out_16,
  output [31:0] out_17,
  output jW,
  output [31:0] out_19,
  output [31:0] out_20,
  output JalW,
  output RegWriteW,
  output [4:0] DestinationW,
  output JrW,
  output MemToRegtW
);

  wire not_1_out;

  Register #(.width(32)) register_1 (.D(in_1), .en(not_1_out), .Q(out_15), .clk(clk), .clr(clear));
  Register #(.width(32)) register_2 (.D(in_5), .en(not_1_out), .Q(out_19), .clk(clk));  // open: clr
  Register #(.width(5)) register_3 (.D(DestinationM), .en(not_1_out), .Q(DestinationW), .clk(clk));  // open: clr
  Register #(.width(1)) register_4 (.D(JrM), .en(not_1_out), .Q(JrW), .clk(clk));  // open: clr
  Register #(.width(32)) register_5 (.D(in_2), .en(not_1_out), .Q(out_16), .clk(clk), .clr(clear));
  Register #(.width(32)) register_6 (.D(in_6), .en(not_1_out), .Q(out_20), .clk(clk), .clr(clear));
  Register #(.width(1)) register_7 (.D(RegWriteM), .en(not_1_out), .Q(RegWriteW), .clk(clk), .clr(clear));
  Register #(.width(1)) register_8 (.D(MemToRegtM), .en(not_1_out), .Q(MemToRegtW), .clk(clk), .clr(clear));
  not not_1 (not_1_out, stall);
  Register #(.width(32)) register_9 (.D(in_3), .en(not_1_out), .Q(out_17), .clk(clk), .clr(clear));
  Register #(.width(1)) register_10 (.D(jM), .en(not_1_out), .Q(jW), .clk(clk), .clr(clear));
  Register #(.width(1)) register_11 (.D(JalM), .en(not_1_out), .Q(JalW), .clk(clk), .clr(clear));

  // Notes on the sheet:
  //   rsValM
  //   PC+4M
  //   rsValW
  //   PC+4W
  //   ALUResultM
  //   jAddrM
  //   ALUResultW
  //   jAddrW
  //   MemDataM
  //   MemDataW
endmodule

module InstructionSplitter (
  input  [31:0] in_1,
  output [4:0] shamt,
  output [5:0] Func,
  output [15:0] out_4,
  output [25:0] out_5,
  output [4:0] rd,
  output [4:0] rt,
  output [4:0] rs,
  output [5:0] opCode
);


  assign Func = in_1[5:0];
  assign opCode = in_1[31:26];
  assign out_4 = in_1[15:0];
  assign out_5 = in_1[25:0];
  assign rd = in_1[15:11];
  assign rs = in_1[25:21];
  assign rt = in_1[20:16];
  assign shamt = in_1[10:6];

  // Notes on the sheet:
  //   Input Machine Code
  //   Immediate
  //   Jump Address
endmodule

module Hazard_Unit_Og (
  input  [4:0] rsD,
  input  isBranch,
  input  [4:0] rtD,
  input  jD,
  input  [4:0] rsE,
  input  jrD,
  input  [4:0] rtE,
  input  jalD,
  input  [4:0] DestinationE,
  input  [4:0] DestinationM,
  input  [4:0] DestinationW,
  input  RegWriteM,
  input  RegWriteW,
  input  MemToRegE,
  input  BranchD,
  input  RegWriteE,
  input  MemToRegM,
  output [1:0] ForwardBE,
  output [1:0] ForwardAE,
  output ForwardAD,
  output ForwardBD,
  output branchStall,
  output lwStall,
  output StallF,
  output StallD,
  output FlushE,
  output FlushD
);

  wire and_1_out, and_2_out, and_5_out, and_6_out, and_7_out, and_8_out, and_11_out, and_12_out, and_13_out,
       and_14_out, and_15_out, comparator_1_eq, comparator_2_eq, comparator_3_eq, comparator_4_eq,
       comparator_5_eq, comparator_6_eq, comparator_7_eq, comparator_8_eq, comparator_9_eq, comparator_10_eq,
       comparator_11_eq, comparator_12_eq, comparator_13_eq, comparator_14_eq, comparator_15_eq,
       comparator_16_eq, comparator_17_eq, comparator_18_eq, comparator_19_eq, comparator_20_eq,
       comparator_21_eq, comparator_22_eq, comparator_23_eq, comparator_24_eq, comparator_25_eq, jrStall,
       not_1_out, not_2_out, not_3_out, not_4_out, not_5_out, not_6_out, not_7_out, not_8_out, or_1_out,
       or_3_out, or_4_out, or_5_out;
  wire [1:0] multiplexer_1_out, multiplexer_2_out, multiplexer_4_out, multiplexer_5_out;

  not not_1 (not_1_out, comparator_1_eq);
  Comparator #(.width(5)) comparator_1 (.a(rsE), .b({5{1'b0}}), .eq(comparator_1_eq));  // open: gt, lt
  Comparator #(.width(5)) comparator_2 (.a(rsE), .b(DestinationM), .eq(comparator_2_eq));  // open: gt, lt
  Comparator #(.width(5)) comparator_3 (.a(rsE), .b({5{1'b0}}), .eq(comparator_3_eq));  // open: gt, lt
  Comparator #(.width(5)) comparator_4 (.a(rsE), .b(DestinationW), .eq(comparator_4_eq));  // open: gt, lt
  and and_1 (and_1_out, not_1_out, comparator_2_eq, MemToRegM);
  not not_2 (not_2_out, comparator_3_eq);
  and and_2 (and_2_out, not_2_out, comparator_4_eq, RegWriteW);
  Comparator #(.width(5)) comparator_5 (.a(rsE), .b({5{1'b0}}), .eq(comparator_5_eq));  // open: gt, lt
  Comparator #(.width(5)) comparator_6 (.a(rsE), .b(DestinationM), .eq(comparator_6_eq));  // open: gt, lt
  Comparator #(.width(5)) comparator_7 (.a(rsD), .b({5{1'b0}}), .eq(comparator_7_eq));  // open: gt, lt
  Comparator #(.width(5)) comparator_8 (.a(rsD), .b(DestinationM), .eq(comparator_8_eq));  // open: gt, lt
  Comparator #(.width(5)) comparator_9 (.a(rsD), .b(rtE), .eq(comparator_9_eq));  // open: gt, lt
  or or_1 (or_1_out, comparator_9_eq, comparator_10_eq);
  Comparator #(.width(5)) comparator_10 (.a(rtD), .b(rtE), .eq(comparator_10_eq));  // open: gt, lt
  Multiplexer #(.width(2)) multiplexer_1 (
    .in0(2'b00), .in1(2'b01), .out(multiplexer_1_out), .sel(and_2_out));  // open: en
  not not_3 (not_3_out, comparator_5_eq);
  not not_4 (not_4_out, comparator_7_eq);
  and and_3 (ForwardAD, not_4_out, comparator_8_eq, RegWriteM);
  and and_4 (lwStall, or_1_out, MemToRegE);
  or or_2 (FlushD, isBranch, jD, jrD, jalD);
  Multiplexer #(.width(2)) multiplexer_2 (
    .in0(multiplexer_1_out), .in1(2'b10), .out(multiplexer_2_out), .sel(and_5_out));  // open: en
  and and_5 (and_5_out, not_3_out, comparator_6_eq, RegWriteM);
  Multiplexer #(.width(2)) multiplexer_3 (
    .in0(multiplexer_2_out), .in1(2'b11), .out(ForwardAE), .sel(and_1_out));  // open: en
  Comparator #(.width(5)) comparator_11 (.a(rsD), .b(DestinationE), .eq(comparator_11_eq));  // open: gt, lt
  Comparator #(.width(5)) comparator_12 (.a(rsD), .b(DestinationM), .eq(comparator_12_eq));  // open: gt, lt
  Comparator #(.width(5)) comparator_13 (.a(rsD), .b(DestinationW), .eq(comparator_13_eq));  // open: gt, lt
  not not_5 (not_5_out, comparator_14_eq);
  Comparator #(.width(5)) comparator_14 (.a(rtD), .b({5{1'b0}}), .eq(comparator_14_eq));  // open: gt, lt
  Comparator #(.width(5)) comparator_15 (.a(rtD), .b(DestinationM), .eq(comparator_15_eq));  // open: gt, lt
  Comparator #(.width(5)) comparator_16 (.a(DestinationE), .b(rsD), .eq(comparator_16_eq));  // open: gt, lt
  Comparator #(.width(5)) comparator_17 (.a(DestinationE), .b(rtD), .eq(comparator_17_eq));  // open: gt, lt
  Comparator #(.width(5)) comparator_18 (.a(DestinationM), .b(rsD), .eq(comparator_18_eq));  // open: gt, lt
  Comparator #(.width(5)) comparator_19 (.a(DestinationM), .b(rtD), .eq(comparator_19_eq));  // open: gt, lt
  and and_6 (and_6_out, comparator_11_eq, RegWriteE);
  or or_3 (or_3_out, and_6_out, and_7_out, and_8_out);
  and and_7 (and_7_out, comparator_12_eq, RegWriteM);
  and and_8 (and_8_out, comparator_13_eq, RegWriteW);
  and and_9 (ForwardBD, not_5_out, comparator_15_eq, RegWriteM);
  or or_4 (or_4_out, comparator_16_eq, comparator_17_eq);
  or or_5 (or_5_out, comparator_18_eq, comparator_19_eq);
  and and_10 (jrStall, or_3_out, jrD);
  Comparator #(.width(5)) comparator_20 (.a(rtE), .b({5{1'b0}}), .eq(comparator_20_eq));  // open: gt, lt
  Comparator #(.width(5)) comparator_21 (.a(rtE), .b(DestinationM), .eq(comparator_21_eq));  // open: gt, lt
  and and_11 (and_11_out, BranchD, RegWriteE, or_4_out);
  and and_12 (and_12_out, BranchD, MemToRegM, or_5_out);
  not not_6 (not_6_out, comparator_20_eq);
  and and_13 (and_13_out, not_6_out, comparator_21_eq, MemToRegM);
  not not_7 (not_7_out, comparator_22_eq);
  Comparator #(.width(5)) comparator_22 (.a(rtE), .b({5{1'b0}}), .eq(comparator_22_eq));  // open: gt, lt
  Comparator #(.width(5)) comparator_23 (.a(rtE), .b(DestinationW), .eq(comparator_23_eq));  // open: gt, lt
  or or_6 (branchStall, and_11_out, and_12_out);
  Multiplexer #(.width(2)) multiplexer_4 (
    .in0(2'b00), .in1(2'b01), .out(multiplexer_4_out), .sel(and_14_out));  // open: en
  and and_14 (and_14_out, not_7_out, comparator_23_eq, RegWriteW);
  Comparator #(.width(5)) comparator_24 (.a(rtE), .b({5{1'b0}}), .eq(comparator_24_eq));  // open: gt, lt
  not not_8 (not_8_out, comparator_24_eq);
  Comparator #(.width(5)) comparator_25 (.a(rtE), .b(DestinationM), .eq(comparator_25_eq));  // open: gt, lt
  and and_15 (and_15_out, not_8_out, comparator_25_eq, RegWriteM);
  Multiplexer #(.width(2)) multiplexer_5 (
    .in0(multiplexer_4_out), .in1(2'b10), .out(multiplexer_5_out), .sel(and_15_out));  // open: en
  Multiplexer #(.width(2)) multiplexer_6 (
    .in0(multiplexer_5_out), .in1(2'b11), .out(ForwardBE), .sel(and_13_out));  // open: en

  assign FlushE = branchStall;
  assign StallD = branchStall;
  assign StallF = branchStall;

  // Notes on the sheet:
  //   00
  //   01
  //   10
  //   00
  //   01
  //   10
endmodule

module _32X32RegFile (
  input  [4:0] Read_B,
  input  [4:0] Read_A,
  input  in_3,
  input  [4:0] Selection,
  input  in_5,
  input  in_6,
  input  [31:0] in_7,
  output [31:0] out_8,
  output [31:0] out_9
);

  wire and_1_out, and_2_out, and_3_out, and_4_out, and_5_out, and_6_out, and_7_out, and_8_out, and_9_out,
       and_10_out, and_11_out, and_12_out, and_13_out, and_14_out, and_15_out, and_16_out, and_17_out,
       and_18_out, and_19_out, and_20_out, and_21_out, and_22_out, and_23_out, and_24_out, and_25_out,
       and_26_out, and_27_out, and_28_out, and_29_out, and_30_out, and_31_out, and_32_out, and_33_out,
       comparator_1_eq, comparator_2_eq, demultiplexer_1_out1, demultiplexer_1_out2, demultiplexer_1_out3,
       demultiplexer_1_out4, demultiplexer_1_out5, demultiplexer_1_out6, demultiplexer_1_out7,
       demultiplexer_1_out8, demultiplexer_1_out9, demultiplexer_1_out10, demultiplexer_1_out11,
       demultiplexer_1_out12, demultiplexer_1_out13, demultiplexer_1_out14, demultiplexer_1_out15,
       demultiplexer_1_out16, demultiplexer_1_out17, demultiplexer_1_out18, demultiplexer_1_out19,
       demultiplexer_1_out20, demultiplexer_1_out21, demultiplexer_1_out22, demultiplexer_1_out23,
       demultiplexer_1_out24, demultiplexer_1_out25, demultiplexer_1_out26, demultiplexer_1_out27,
       demultiplexer_1_out28, demultiplexer_1_out29, demultiplexer_1_out30, demultiplexer_1_out31;
  wire [31:0] multiplexer_1_out, multiplexer_2_out, register_1_q, register_2_q, register_3_q, register_4_q,
       register_5_q, register_6_q, register_7_q, register_8_q, register_9_q, register_10_q, register_11_q,
       register_12_q, register_13_q, register_14_q, register_15_q, register_16_q, register_17_q,
       register_18_q, register_19_q, register_20_q, register_21_q, register_22_q, register_23_q,
       register_24_q, register_25_q, register_26_q, register_27_q, register_28_q, register_29_q,
       register_30_q, register_31_q;

  Demultiplexer #(.select(5)) demultiplexer_1 (
    .out1(demultiplexer_1_out1), .out2(demultiplexer_1_out2), .out3(demultiplexer_1_out3),
    .out4(demultiplexer_1_out4), .out5(demultiplexer_1_out5), .out6(demultiplexer_1_out6),
    .out7(demultiplexer_1_out7), .out8(demultiplexer_1_out8), .out9(demultiplexer_1_out9),
    .out10(demultiplexer_1_out10), .out11(demultiplexer_1_out11), .out12(demultiplexer_1_out12),
    .out13(demultiplexer_1_out13), .out14(demultiplexer_1_out14), .out15(demultiplexer_1_out15),
    .out16(demultiplexer_1_out16), .out17(demultiplexer_1_out17), .out18(demultiplexer_1_out18),
    .out19(demultiplexer_1_out19), .out20(demultiplexer_1_out20), .out21(demultiplexer_1_out21),
    .out22(demultiplexer_1_out22), .out23(demultiplexer_1_out23), .out24(demultiplexer_1_out24),
    .out25(demultiplexer_1_out25), .out26(demultiplexer_1_out26), .out27(demultiplexer_1_out27),
    .out28(demultiplexer_1_out28), .out29(demultiplexer_1_out29), .out30(demultiplexer_1_out30),
    .out31(demultiplexer_1_out31), .in(in_3), .sel(Selection));  // open: out0, en
  and and_1 (and_1_out, in_3, demultiplexer_1_out1);
  and and_2 (and_2_out, in_3, demultiplexer_1_out2);
  and and_3 (and_3_out, in_3, demultiplexer_1_out3);
  and and_4 (and_4_out, in_3, demultiplexer_1_out4);
  and and_5 (and_5_out, in_3, demultiplexer_1_out5);
  and and_6 (and_6_out, in_3, demultiplexer_1_out6);
  and and_7 (and_7_out, in_3, demultiplexer_1_out7);
  and and_8 (and_8_out, in_3, demultiplexer_1_out8);
  and and_9 (and_9_out, in_3, demultiplexer_1_out9);
  and and_10 (and_10_out, in_3, demultiplexer_1_out10);
  and and_11 (and_11_out, in_3, demultiplexer_1_out11);
  and and_12 (and_12_out, in_3, demultiplexer_1_out12);
  and and_13 (and_13_out, in_3, demultiplexer_1_out13);
  and and_14 (and_14_out, in_3, demultiplexer_1_out14);
  and and_15 (and_15_out, in_3, demultiplexer_1_out15);
  and and_16 (and_16_out, in_3, demultiplexer_1_out16);
  and and_17 (and_17_out, in_3, demultiplexer_1_out17);
  and and_18 (and_18_out, in_3, demultiplexer_1_out18);
  and and_19 (and_19_out, in_3, demultiplexer_1_out19);
  and and_20 (and_20_out, in_3, demultiplexer_1_out20);
  and and_21 (and_21_out, in_3, demultiplexer_1_out21);
  and and_22 (and_22_out, in_3, demultiplexer_1_out22);
  and and_23 (and_23_out, in_3, demultiplexer_1_out23);
  and and_24 (and_24_out, in_3, demultiplexer_1_out24);
  and and_25 (and_25_out, in_3, demultiplexer_1_out25);
  and and_26 (and_26_out, in_3, demultiplexer_1_out26);
  and and_27 (and_27_out, in_3, demultiplexer_1_out27);
  and and_28 (and_28_out, in_3, demultiplexer_1_out28);
  and and_29 (and_29_out, in_3, demultiplexer_1_out29);
  and and_30 (and_30_out, in_3, demultiplexer_1_out30);
  and and_31 (and_31_out, in_3, demultiplexer_1_out31);
  Register #(.width(32)) register_1 (.D(in_7), .en(and_1_out), .Q(register_1_q), .clk(in_6), .clr(in_5));
  Register #(.width(32)) register_2 (.D(in_7), .en(and_2_out), .Q(register_2_q), .clk(in_6), .clr(in_5));
  Register #(.width(32)) register_3 (.D(in_7), .en(and_3_out), .Q(register_3_q), .clk(in_6), .clr(in_5));
  Register #(.width(32)) register_4 (.D(in_7), .en(and_4_out), .Q(register_4_q), .clk(in_6), .clr(in_5));
  Register #(.width(32)) register_5 (.D(in_7), .en(and_5_out), .Q(register_5_q), .clk(in_6), .clr(in_5));
  Register #(.width(32)) register_6 (.D(in_7), .en(and_6_out), .Q(register_6_q), .clk(in_6), .clr(in_5));
  Register #(.width(32)) register_7 (.D(in_7), .en(and_7_out), .Q(register_7_q), .clk(in_6), .clr(in_5));
  Register #(.width(32)) register_8 (.D(in_7), .en(and_8_out), .Q(register_8_q), .clk(in_6), .clr(in_5));
  Register #(.width(32)) register_9 (.D(in_7), .en(and_9_out), .Q(register_9_q), .clk(in_6), .clr(in_5));
  Register #(.width(32)) register_10 (.D(in_7), .en(and_10_out), .Q(register_10_q), .clk(in_6), .clr(in_5));
  Register #(.width(32)) register_11 (.D(in_7), .en(and_11_out), .Q(register_11_q), .clk(in_6), .clr(in_5));
  Register #(.width(32)) register_12 (.D(in_7), .en(and_12_out), .Q(register_12_q), .clk(in_6), .clr(in_5));
  Register #(.width(32)) register_13 (.D(in_7), .en(and_13_out), .Q(register_13_q), .clk(in_6), .clr(in_5));
  Register #(.width(32)) register_14 (.D(in_7), .en(and_14_out), .Q(register_14_q), .clk(in_6), .clr(in_5));
  Register #(.width(32)) register_15 (.D(in_7), .en(and_15_out), .Q(register_15_q), .clk(in_6), .clr(in_5));
  Register #(.width(32)) register_16 (.D(in_7), .en(and_16_out), .Q(register_16_q), .clk(in_6), .clr(in_5));
  Register #(.width(32)) register_17 (.D(in_7), .en(and_17_out), .Q(register_17_q), .clk(in_6), .clr(in_5));
  Register #(.width(32)) register_18 (.D(in_7), .en(and_18_out), .Q(register_18_q), .clk(in_6), .clr(in_5));
  Register #(.width(32)) register_19 (.D(in_7), .en(and_19_out), .Q(register_19_q), .clk(in_6), .clr(in_5));
  Register #(.width(32)) register_20 (.D(in_7), .en(and_20_out), .Q(register_20_q), .clk(in_6), .clr(in_5));
  Register #(.width(32)) register_21 (.D(in_7), .en(and_21_out), .Q(register_21_q), .clk(in_6), .clr(in_5));
  Register #(.width(32)) register_22 (.D(in_7), .en(and_22_out), .Q(register_22_q), .clk(in_6), .clr(in_5));
  Register #(.width(32)) register_23 (.D(in_7), .en(and_23_out), .Q(register_23_q), .clk(in_6), .clr(in_5));
  Register #(.width(32)) register_24 (.D(in_7), .en(and_24_out), .Q(register_24_q), .clk(in_6), .clr(in_5));
  Register #(.width(32)) register_25 (.D(in_7), .en(and_25_out), .Q(register_25_q), .clk(in_6), .clr(in_5));
  Register #(.width(32)) register_26 (.D(in_7), .en(and_26_out), .Q(register_26_q), .clk(in_6), .clr(in_5));
  Register #(.width(32)) register_27 (.D(in_7), .en(and_27_out), .Q(register_27_q), .clk(in_6), .clr(in_5));
  Register #(.width(32)) register_28 (.D(in_7), .en(and_28_out), .Q(register_28_q), .clk(in_6), .clr(in_5));
  Register #(.width(32)) register_29 (.D(in_7), .en(and_29_out), .Q(register_29_q), .clk(in_6), .clr(in_5));
  Register #(.width(32)) register_30 (.D(in_7), .en(and_30_out), .Q(register_30_q), .clk(in_6), .clr(in_5));
  Register #(.width(32)) register_31 (.D(in_7), .en(and_31_out), .Q(register_31_q), .clk(in_6), .clr(in_5));
  Multiplexer #(.select(5), .width(32)) multiplexer_1 (
    .in0({32{1'b0}}), .in1(register_1_q), .in2(register_2_q), .in3(register_3_q), .in4(register_4_q),
    .in5(register_5_q), .in6(register_6_q), .in7(register_7_q), .in8(register_8_q), .in9(register_9_q),
    .in10(register_10_q), .in11(register_11_q), .in12(register_12_q), .in13(register_13_q),
    .in14(register_14_q), .in15(register_15_q), .in16(register_16_q), .in17(register_17_q),
    .in18(register_18_q), .in19(register_19_q), .in20(register_20_q), .in21(register_21_q),
    .in22(register_22_q), .in23(register_23_q), .in24(register_24_q), .in25(register_25_q),
    .in26(register_26_q), .in27(register_27_q), .in28(register_28_q), .in29(register_29_q),
    .in30(register_30_q), .in31(register_31_q), .out(multiplexer_1_out), .sel(Read_A));  // open: en
  Multiplexer #(.select(5), .width(32)) multiplexer_2 (
    .in0({32{1'b0}}), .in1(register_1_q), .in2(register_2_q), .in3(register_3_q), .in4(register_4_q),
    .in5(register_5_q), .in6(register_6_q), .in7(register_7_q), .in8(register_8_q), .in9(register_9_q),
    .in10(register_10_q), .in11(register_11_q), .in12(register_12_q), .in13(register_13_q),
    .in14(register_14_q), .in15(register_15_q), .in16(register_16_q), .in17(register_17_q),
    .in18(register_18_q), .in19(register_19_q), .in20(register_20_q), .in21(register_21_q),
    .in22(register_22_q), .in23(register_23_q), .in24(register_24_q), .in25(register_25_q),
    .in26(register_26_q), .in27(register_27_q), .in28(register_28_q), .in29(register_29_q),
    .in30(register_30_q), .in31(register_31_q), .out(multiplexer_2_out), .sel(Read_B));  // open: en
  Multiplexer #(.width(32)) multiplexer_3 (
    .in0(multiplexer_1_out), .in1(in_7), .out(out_8), .sel(and_32_out));  // open: en
  Comparator #(.width(5), .mode("unsigned")) comparator_1 (
    .a(Read_B), .b(Selection), .eq(comparator_1_eq));  // open: gt, lt
  Comparator #(.width(5), .mode("unsigned")) comparator_2 (
    .a(Read_A), .b(Selection), .eq(comparator_2_eq));  // open: gt, lt
  and and_32 (and_32_out, in_3, comparator_2_eq);
  Multiplexer #(.width(32)) multiplexer_4 (
    .in0(multiplexer_2_out), .in1(in_7), .out(out_9), .sel(and_33_out));  // open: en
  and and_33 (and_33_out, comparator_1_eq, in_3);

  // Other names for the same wires on the sheet: RegWrite = in_3; WriteAddress[4:0] = Selection;
  //   WriteData[31:0] = in_7

  // Notes on the sheet:
  //   ANJNEY LAWANIYA - 2402CS11   
  //   ANJNEY LAWANIYA - 2402CS11
  //   Input
  //   Clear
  //   YOU HAVE REACHED THE END OF BEGINNING  - ANJNEY LAWANIYA
  //   11-$t3
  //   13-$t5
  //   14-$t6
  //   15-$t7
  //   16-$s0
  //   17-$s1
  //   18-$s2
  //   19-$s3
  //   20-$s4
  //   21-$s5
  //   22-$s6
  //   23-$s7
  //   24-$t8
  //   25-$t9
  //   26-$k0
  //   Clk
  //   1-$at
  //   2-$v0
  //   3-$v1
  //   4-$a0
  //   5-$a1
  //   6-$a2
  //   7-$a3
  //   8-$t0
  //   9-$t1
  //   12-$t4
  //   27-$k1
  //   28-$gp
  //   29-$sp
  //   30-$fp
  //   31-$ra
  //   10-$t2
  //   A
  //   B
endmodule

module ALU (
  input  [31:0] in_1,
  input  [31:0] in_2,
  input  [2:0] OpCode,
  output isZero,
  output [31:0] out_5
);

  wire subtractor_1_bout;
  wire [31:0] adder_1_out, and_1_out, and_2_out, bit_extender_1_out, not_1_out, or_1_out, or_2_out,
       subtractor_1_out;

  assign not_1_out = ~in_2;  // NOT_Gate not_1, 32 bits wide
  assign and_1_out = in_1 & in_2;  // AND_Gate and_1, 32 bits wide
  assign or_1_out = in_1 | in_2;  // OR_Gate or_1, 32 bits wide
  Adder #(.width(32)) adder_1 (.a(in_1), .b(in_2), .out(adder_1_out));  // open: cin, cout
  assign and_2_out = not_1_out & in_1;  // AND_Gate and_2, 32 bits wide
  assign or_2_out = not_1_out | in_1;  // OR_Gate or_2, 32 bits wide
  Subtractor #(.width(32)) subtractor_1 (
    .a(in_1), .b(in_2), .out(subtractor_1_out), .bout(subtractor_1_bout));  // open: bin
  assign bit_extender_1_out = {{31{1'b0}}, subtractor_1_bout};  // Bit_Extender bit_extender_1
  Multiplexer #(.select(3), .width(32)) multiplexer_1 (
    .in0(and_1_out), .in1(or_1_out), .in2(adder_1_out), .in3({32{1'b0}}), .in4(and_2_out), .in5(or_2_out),
    .in6(subtractor_1_out), .in7(bit_extender_1_out), .out(out_5), .sel(OpCode));  // open: en
  Comparator #(.width(32)) comparator_1 (.a({32{1'b0}}), .b(out_5), .eq(isZero));  // open: gt, lt

  // Notes on the sheet:
  //   A
  //   B
  //   ANJNEY LAWANIYA - 2402CS11
  //   A&B.000
  //   A|B.001
  //   A+B.010
  //   A&~B.100
  //   A|~B.101
  //   A-B.110
  //   Output
endmodule

module jAddressMaker (
  input  [31:0] in_1,
  input  [25:0] in_2,
  output [31:0] out_3
);


  assign out_3 = {in_1[31:28], in_2, 2'b00};

  // Notes on the sheet:
  //   jAddress
  //   PC + 4
  //   Final_Jump
endmodule
