// Logisim project XOR_usingNAND.circ as structural Verilog: 1 circuit, main circuit main
module main (
  input  in_1,
  input  in_2,
  output out_3
);

  wire main_1_out_3, main_2_out_3, main_3_out_3;

  NAND_transistor_main main_1 (.in_1(in_1), .in_2(in_2), .out_3(main_1_out_3));
  NAND_transistor_main main_2 (.in_1(in_1), .in_2(main_1_out_3), .out_3(main_2_out_3));
  NAND_transistor_main main_3 (.in_1(main_1_out_3), .in_2(in_2), .out_3(main_3_out_3));
  NAND_transistor_main main_4 (.in_1(main_2_out_3), .in_2(main_3_out_3), .out_3(out_3));
endmodule
