// Logisim project GateLib.circ as structural Verilog: 10 circuits, main circuit main
module main (
  input  in_1,
  input  in_2
);

  wire transistor_1_out, transistor_2_out;

  Transistor #(.\type ("n")) transistor_1 (.in(1'b0), .out(transistor_1_out), .gate(in_2));
  Transistor transistor_2 (.in(1'b1), .out(transistor_2_out), .gate(in_1));
  Transistor transistor_3 (.in(transistor_2_out), .out(transistor_1_out), .gate(in_2));
  Transistor #(.\type ("n")) transistor_4 (.in(1'b0), .out(transistor_1_out), .gate(in_1));
  LED led_1 (.in(transistor_1_out));

  // Notes on the sheet:
  //   Inputs
  //   NOR GATE
  //   Ground
  //   High voltage
  //   Output
endmodule

module NOR (
  input  A,
  input  B,
  output Y
);

  wire transistor_2_out;

  Transistor #(.\type ("n")) transistor_1 (.in(1'b0), .out(Y), .gate(B));
  Transistor transistor_2 (.in(1'b1), .out(transistor_2_out), .gate(A));
  Transistor transistor_3 (.in(transistor_2_out), .out(Y), .gate(B));
  Transistor #(.\type ("n")) transistor_4 (.in(1'b0), .out(Y), .gate(A));

  // Notes on the sheet:
  //   Inputs
  //   NOR GATE
  //   Ground
  //   High voltage
  //   Output
endmodule

module tb_nor (
  input  in_1,
  input  in_2
);

  wire nor_1_y;

  NOR nor_1 (.A(in_1), .B(in_2), .Y(nor_1_y));
  LED led_1 (.in(nor_1_y));
endmodule

module NAND (
  input  in_1,
  input  in_2,
  output Output
);

  wire transistor_3_out;

  Transistor transistor_1 (.in(1'b1), .out(Output), .gate(in_2));
  Transistor #(.\type ("n")) transistor_2 (.in(transistor_3_out), .out(Output), .gate(in_1));
  Transistor #(.\type ("n")) transistor_3 (.in(1'b0), .out(transistor_3_out), .gate(in_2));
  Transistor transistor_4 (.in(1'b1), .out(Output), .gate(in_1));

  // Notes on the sheet:
  //   NAND GATE
  //   Inputs
  //   High voltage
  //   Ground
endmodule

module \xor  (
  input  in_1,
  input  in_2,
  output Output
);

  wire transistor_1_out;

  Transistor transistor_1 (.in(1'b1), .out(transistor_1_out), .gate(in_1));
  Transistor #(.\type ("n")) transistor_2 (.in(1'b0), .out(transistor_1_out), .gate(in_1));
  Transistor transistor_3 (.in(in_1), .out(Output), .gate(in_2));
  Transistor #(.\type ("n")) transistor_4 (.in(transistor_1_out), .out(Output), .gate(in_2));

  // Notes on the sheet:
  //   XOR GATE
  //                        Inputs
  //               Highvoltage
  //   Ground
endmodule

module _3_Nand (
  input  A,
  input  B,
  input  C,
  output Y
);

  wire transistor_4_out, transistor_5_out;

  Transistor transistor_1 (.in(1'b0), .out(Y), .gate(B));
  Transistor transistor_2 (.in(1'b0), .out(Y), .gate(A));
  Transistor #(.\type ("n")) transistor_3 (.in(transistor_4_out), .out(Y), .gate(A));
  Transistor #(.\type ("n")) transistor_4 (.in(transistor_5_out), .out(transistor_4_out), .gate(B));
  Transistor #(.\type ("n")) transistor_5 (.in(1'b1), .out(transistor_5_out), .gate(C));
  Transistor transistor_6 (.in(1'b0), .out(Y), .gate(C));

  // Notes on the sheet:
  //   Inputs
  //   3- INPUT NAND GATE
  //   Grounded
  //   Highvoltage
  //   Grounded
  //   Grounded
  //   Output
endmodule

module _3_AND (
  input  in_1,
  input  in_2,
  input  in_3,
  output Output
);

  wire transistor_5_out, transistor_6_out, transistor_7_out;

  Transistor transistor_1 (.in(1'b0), .out(Output), .gate(in_1));
  Transistor transistor_2 (.in(1'b0), .out(Output), .gate(in_2));
  Transistor transistor_3 (.in(1'b0), .out(Output), .gate(in_3));
  Transistor #(.\type ("n")) transistor_4 (.in(transistor_5_out), .out(Output), .gate(in_1));
  Transistor #(.\type ("n")) transistor_5 (.in(transistor_6_out), .out(transistor_5_out), .gate(in_2));
  Transistor #(.\type ("n")) transistor_6 (.in(1'b1), .out(transistor_6_out), .gate(in_3));
  Transistor transistor_7 (.in(1'b0), .out(transistor_7_out), .gate(Output));
  Transistor #(.\type ("n")) transistor_8 (.in(1'b1), .out(transistor_7_out), .gate(Output));

  // Notes on the sheet:
  //   Inputs
  //   3- INPUT AND GATE
  //   Grounded
  //   Highvoltage
  //   Grounded
  //   Grounded
  //   Highvoltage
endmodule

module Hall_adder (
  input  A,
  input  B,
  output C,
  output S
);

  AND and_1 (.A(A), .B(B), .Y(C));
  \xor  xor_1 (.in_1(A), .in_2(B), .Output(S));
endmodule

module AND (
  input  A,
  input  B,
  output Y
);

  wire transistor_1_out, transistor_3_out;

  Transistor transistor_1 (.in(1'b1), .out(transistor_1_out), .gate(B));
  Transistor #(.\type ("n")) transistor_2 (.in(transistor_3_out), .out(transistor_1_out), .gate(A));
  Transistor #(.\type ("n")) transistor_3 (.in(1'b0), .out(transistor_3_out), .gate(B));
  Transistor transistor_4 (.in(1'b1), .out(transistor_1_out), .gate(A));
  Transistor transistor_5 (.in(1'b1), .out(Y), .gate(transistor_1_out));
  Transistor #(.\type ("n")) transistor_6 (.in(1'b0), .out(Y), .gate(transistor_1_out));

  // Notes on the sheet:
  //   AND GATE
  //   Inputs
  //   High  
  //   Ground
endmodule

module full_adder (
  input  A,
  input  B,
  input  C,
  output C_2,
  output S
);

  wire and_1_out, and_2_out, and_3_out;

  and and_1 (and_1_out, A, B);
  and and_2 (and_2_out, C, B);
  and and_3 (and_3_out, A, C);
  or or_1 (C_2, and_1_out, and_2_out, and_3_out);
  ExactlyOne xor_1 (.out(S), .in0(B), .in1(A), .in2(C));
endmodule
