// Logisim project LAB1.circ as structural Verilog: 12 circuits, main circuit main
module main (
  input  in_1,
  input  in_2,
  output out_3
);

  wire transistor_3_out;

  Transistor transistor_1 (.in(1'b1), .out(out_3), .gate(in_2));
  Transistor #(.\type ("n")) transistor_2 (.in(transistor_3_out), .out(out_3), .gate(in_1));
  Transistor #(.\type ("n")) transistor_3 (.in(1'b0), .out(transistor_3_out), .gate(in_2));
  Transistor transistor_4 (.in(1'b1), .out(out_3), .gate(in_1));
endmodule

module NAND_transistor (
  input  Input_A,
  input  Input_B,
  output Output
);

  wire transistor_3_out;

  Transistor transistor_1 (.in(1'b1), .out(Output), .gate(Input_B));
  Transistor #(.\type ("n")) transistor_2 (.in(transistor_3_out), .out(Output), .gate(Input_A));
  Transistor #(.\type ("n")) transistor_3 (.in(1'b0), .out(transistor_3_out), .gate(Input_B));
  Transistor transistor_4 (.in(1'b1), .out(Output), .gate(Input_A));

  // Notes on the sheet:
  //   Power supply
  //   P-type Transisitor
  //   N-type Transistor
  //   N-Type Transistor
  //   Ground Supply
  //   P-type Transistor
endmodule

module XOR (
  input  Input_A,
  input  Input_B,
  output Output
);

  wire nand_transistor_1_output, nand_transistor_2_output, nand_transistor_3_output;

  NAND_transistor nand_transistor_1 (.Input_A(Input_A), .Input_B(Input_B), .Output(nand_transistor_1_output));
  NAND_transistor nand_transistor_2 (
    .Input_A(Input_A), .Input_B(nand_transistor_1_output), .Output(nand_transistor_2_output));
  NAND_transistor nand_transistor_3 (
    .Input_A(nand_transistor_1_output), .Input_B(Input_B), .Output(nand_transistor_3_output));
  NAND_transistor nand_transistor_4 (
    .Input_A(nand_transistor_2_output), .Input_B(nand_transistor_3_output), .Output(Output));
endmodule

module _4bitAdder (
  input  [3:0] in_1,
  input  [3:0] Input_B,
  input  Carry_In,
  output Carry_Out,
  output [3:0] Output_Sum
);

  wire fulladder_2_c, fulladder_3_c, fulladder_4_c;

  fullAdder fulladder_1 (
    .Input_A(Input_B[3]), .Input_B(in_1[3]), .Input_C(fulladder_2_c), .S(Output_Sum[3]), .C(Carry_Out));
  fullAdder fulladder_2 (
    .Input_A(Input_B[2]), .Input_B(in_1[2]), .Input_C(fulladder_3_c), .S(Output_Sum[2]), .C(fulladder_2_c));
  fullAdder fulladder_3 (
    .Input_A(Input_B[1]), .Input_B(in_1[1]), .Input_C(fulladder_4_c), .S(Output_Sum[1]), .C(fulladder_3_c));
  fullAdder fulladder_4 (
    .Input_A(Input_B[0]), .Input_B(in_1[0]), .Input_C(Carry_In), .S(Output_Sum[0]), .C(fulladder_4_c));

  // Notes on the sheet:
  //   Input A
endmodule

module NOT_transistor (
  input  Input,
  output NOT_of_Input
);

  Transistor transistor_1 (.in(1'b1), .out(NOT_of_Input), .gate(Input));
  Transistor #(.\type ("n")) transistor_2 (.in(1'b0), .out(NOT_of_Input), .gate(Input));

  // Notes on the sheet:
  //   Power Supply
  //   P-type transistor
  //   N-type Transistor
  //   Gorund
endmodule

module fullAdder (
  input  Input_A,
  input  Input_B,
  input  Input_C,
  output S,
  output C
);

  wire and_usingnand_1_output, and_usingnand_2_output, and_usingnand_3_output, or_usingnand_1_output,
       xor_1_output;

  XOR xor_1 (.Input_A(Input_A), .Input_B(Input_B), .Output(xor_1_output));
  AND_usingNAND and_usingnand_1 (.Input_A(Input_A), .Input_B(Input_B), .Output(and_usingnand_1_output));
  AND_usingNAND and_usingnand_2 (.Input_A(Input_B), .Input_B(Input_C), .Output(and_usingnand_2_output));
  AND_usingNAND and_usingnand_3 (.Input_A(Input_A), .Input_B(Input_C), .Output(and_usingnand_3_output));
  XOR xor_2 (.Input_A(xor_1_output), .Input_B(Input_C), .Output(S));
  OR_usingNAND or_usingnand_1 (
    .Input_B(and_usingnand_1_output), .Output(or_usingnand_1_output), .Input_A(and_usingnand_2_output));
  OR_usingNAND or_usingnand_2 (.Input_B(or_usingnand_1_output), .Output(C), .Input_A(and_usingnand_3_output));
endmodule

module OR_usingNAND (
  input  Input_A,
  input  Input_B,
  output Output
);

  wire not_transistor_1_not_of_input, not_transistor_2_not_of_input;

  NOT_transistor not_transistor_1 (.Input(Input_A), .NOT_of_Input(not_transistor_1_not_of_input));
  NOT_transistor not_transistor_2 (.Input(Input_B), .NOT_of_Input(not_transistor_2_not_of_input));
  NAND_transistor nand_transistor_1 (
    .Input_A(not_transistor_1_not_of_input), .Input_B(not_transistor_2_not_of_input), .Output(Output));
endmodule

module AND_usingNAND (
  input  Input_A,
  input  Input_B,
  output Output
);

  wire nand_transistor_1_output;

  NAND_transistor nand_transistor_1 (.Input_A(Input_A), .Input_B(Input_B), .Output(nand_transistor_1_output));
  NOT_transistor not_transistor_1 (.Input(nand_transistor_1_output), .NOT_of_Input(Output));
endmodule

module _8bitAdder (
  input  [7:0] Input_B,
  input  [7:0] Input_A,
  input  Carry_In,
  output Carry_Out,
  output [7:0] out_5
);

  wire n4bitadder_2_carry_out;

  _4bitAdder u_4bitadder_1 (
    .Carry_In(n4bitadder_2_carry_out), .Input_B(Input_B[7:4]), .in_1(Input_A[7:4]), .Carry_Out(Carry_Out),
    .Output_Sum(out_5[7:4]));
  _4bitAdder u_4bitadder_2 (
    .Carry_In(Carry_In), .Input_B(Input_B[3:0]), .in_1(Input_A[3:0]), .Carry_Out(n4bitadder_2_carry_out),
    .Output_Sum(out_5[3:0]));

  // Notes on the sheet:
  //   Output Sum
endmodule

module _32bitAdder (
  input  [31:0] in_1,
  input  [31:0] in_2,
  input  Carry_In,
  output Carry_Out,
  output [31:0] out_5
);

  wire n8bitadder_2_carry_out, n8bitadder_3_carry_out, n8bitadder_4_carry_out;

  _8bitAdder u_8bitadder_1 (
    .Carry_In(n8bitadder_2_carry_out), .Input_B(in_1[31:24]), .Input_A(in_2[31:24]), .out_5(out_5[31:24]),
    .Carry_Out(Carry_Out));
  _8bitAdder u_8bitadder_2 (
    .Carry_In(n8bitadder_3_carry_out), .Input_B(in_1[23:16]), .Input_A(in_2[23:16]), .out_5(out_5[23:16]),
    .Carry_Out(n8bitadder_2_carry_out));
  _8bitAdder u_8bitadder_3 (
    .Carry_In(n8bitadder_4_carry_out), .Input_B(in_1[15:8]), .Input_A(in_2[15:8]), .out_5(out_5[15:8]),
    .Carry_Out(n8bitadder_3_carry_out));
  _8bitAdder u_8bitadder_4 (
    .Carry_In(Carry_In), .Input_B(in_1[7:0]), .Input_A(in_2[7:0]), .out_5(out_5[7:0]),
    .Carry_Out(n8bitadder_4_carry_out));

  // Notes on the sheet:
  //   Input B
  //   Input A
  //   Output
endmodule

module accumulator (
  input  [31:0] in_1,
  input  Carry_In,
  input  Enable,
  input  Clear,
  output [31:0] out_5,
  output out_6
);

  wire clock_1_out;
  wire [31:0] n32bitadder_1_out_5;

  _32bitAdder u_32bitadder_1 (
    .Carry_In(Carry_In), .in_1(in_1), .in_2(out_5), .Carry_Out(out_6), .out_5(n32bitadder_1_out_5));
  Clock clock_1 (.out(clock_1_out));
  Register #(.width(32)) register_1 (.D(n32bitadder_1_out_5), .en(Enable), .Q(out_5), .clk(clock_1_out), .clr(Clear));

  // Notes on the sheet:
  //   Carry Out
  //   Input B
  //   Feedback Sum
  //   Clock
  //   Output 
endmodule

module halfAdder (
  input  Input_A,
  input  Input_B,
  output S,
  output C
);

  XOR xor_1 (.Input_A(Input_A), .Input_B(Input_B), .Output(S));
  AND_usingNAND and_usingnand_1 (.Input_A(Input_B), .Input_B(Input_A), .Output(C));
endmodule
