// Logisim project Lab2_2402CS11_anjney_lawaniya.circ as structural Verilog: 6 circuits, main circuit 16bitExpMaker
module _16bitExpMaker (
  input  [15:0] in_1,
  input  [15:0] in_2,
  output [4:0] Max_Exp,
  output [3:0] Shift_Amt,
  output [10:0] out_5,
  output [10:0] out_6
);

  wire and_1_out, comparator_1_gt, comparator_1_lt, n16bitspecialcases_1_zero, n16bitspecialcases_2_zero,
       not_1_out;
  wire [4:0] multiplexer_3_out, subtractor_1_out;
  wire [10:10] multiplexer_1_out;

  and and_1 (and_1_out, n16bitspecialcases_1_zero, n16bitspecialcases_2_zero);
  _16bitSpecialCases u_16bitspecialcases_1 (
    .exp(in_1[14:10]), .in_2(in_1[9:0]), .Zero(n16bitspecialcases_1_zero));  // open: INF, NaN
  _16bitSpecialCases u_16bitspecialcases_2 (
    .exp(in_2[14:10]), .in_2(in_2[9:0]), .Zero(n16bitspecialcases_2_zero));  // open: INF, NaN
  Multiplexer multiplexer_1 (.in0(1'b1), .in1(1'b0), .out(multiplexer_1_out[10]), .sel(and_1_out));  // open: en
  Comparator #(.width(5), .mode("unsigned")) comparator_1 (
    .a(in_1[14:10]), .b(in_2[14:10]), .gt(comparator_1_gt), .lt(comparator_1_lt));  // open: eq
  Multiplexer #(.width(5)) multiplexer_2 (
    .in0(in_2[14:10]), .in1(in_1[14:10]), .out(Max_Exp), .sel(comparator_1_gt));  // open: en
  Multiplexer #(.width(5)) multiplexer_3 (
    .in0(in_2[14:10]), .in1(in_1[14:10]), .out(multiplexer_3_out), .sel(comparator_1_lt));  // open: en
  Subtractor #(.width(5)) subtractor_1 (.a(Max_Exp), .b(multiplexer_3_out), .out(subtractor_1_out));  // open: bin, bout
  not not_1 (not_1_out, comparator_1_lt);
  Multiplexer #(.width(11)) multiplexer_4 (
    .in0({multiplexer_1_out[10], in_2[9:0]}), .in1({multiplexer_1_out[10], in_1[9:0]}), .out(out_5),
    .sel(comparator_1_lt));  // open: en
  Multiplexer #(.width(11)) multiplexer_5 (
    .in0({multiplexer_1_out[10], in_2[9:0]}), .in1({multiplexer_1_out[10], in_1[9:0]}), .out(out_6),
    .sel(not_1_out));  // open: en
  Multiplexer #(.width(4)) multiplexer_6 (
    .in0(subtractor_1_out[3:0]), .in1(4'b1100), .out(Shift_Amt), .sel(subtractor_1_out[4]));  // open: en

  // Notes on the sheet:
  //   Input A
  //   Input B
  //   ANJNEY LAWANIYA - 2402CS11
  //   Zero Checker
  //   Min
  //   Max
endmodule

module _16BITADDER (
  input  [15:0] in_1,
  input  [15:0] in_2,
  output [15:0] out_3,
  output [10:0] Added_Mantissa
);

  wire adder_2_cout, handler_1_inf, handler_1_nan, handler_1_zero, zerospcase_1_iszero;
  wire [3:0] n16bitexpmaker_1_shift_amt;
  wire [4:0] adder_1_out, multiplexer_1_out, n16bitexpmaker_1_max_exp;
  wire [10:0] n16bitexpmaker_1_out_5, n16bitexpmaker_1_out_6, shifter_1_out;
  wire [15:0] multiplexer_2_out, zerospcase_1_out_4;

  ZeroSpCase zerospcase_1 (.in_1(in_1), .in_2(in_2), .isZero(zerospcase_1_iszero), .out_4(zerospcase_1_out_4));
  Handler handler_1 (.in_1(in_1), .in_2(in_2), .Zero(handler_1_zero), .INF(handler_1_inf), .NaN(handler_1_nan));
  _16bitExpMaker u_16bitexpmaker_1 (
    .in_1(in_1), .in_2(in_2), .Max_Exp(n16bitexpmaker_1_max_exp), .Shift_Amt(n16bitexpmaker_1_shift_amt),
    .out_5(n16bitexpmaker_1_out_5), .out_6(n16bitexpmaker_1_out_6));
  _16bitSign u_16bitsign_1 (.in_1(in_1), .in_2(in_2), .Sign_of_greater(multiplexer_2_out[15]));
  LED led_1 (.in(handler_1_zero));
  LED led_2 (.in(handler_1_inf));
  LED led_3 (.in(handler_1_nan));
  Shifter #(.width(11), .shift("lr")) shifter_1 (
    .in(n16bitexpmaker_1_out_5), .\dist (n16bitexpmaker_1_shift_amt), .out(shifter_1_out));
  Adder #(.width(5)) adder_1 (.a(n16bitexpmaker_1_max_exp), .b(5'b00001), .out(adder_1_out));  // open: cin, cout
  Adder #(.width(11)) adder_2 (
    .a(shifter_1_out), .b(n16bitexpmaker_1_out_6), .out(Added_Mantissa), .cout(adder_2_cout));  // open: cin
  Multiplexer #(.width(5)) multiplexer_1 (
    .in0(n16bitexpmaker_1_max_exp), .in1(adder_1_out), .out(multiplexer_1_out), .sel(adder_2_cout));  // open: en
  Multiplexer #(.width(10)) multiplexer_2 (
    .in0(Added_Mantissa[9:0]), .in1(Added_Mantissa[10:1]), .out(multiplexer_2_out[9:0]), .sel(adder_2_cout));  // open: en
  Multiplexer #(.width(16)) multiplexer_3 (
    .in0({multiplexer_2_out[15], multiplexer_1_out, multiplexer_2_out[9:0]}), .in1(zerospcase_1_out_4),
    .out(out_3), .sel(zerospcase_1_iszero));  // open: en

  // Notes on the sheet:
  //   Input A
  //   Input B
  //   ANJNEY LAWANIYA - 2402CS11
  //   Sign Checker
  //   Special Case Zero
  //   Zero
  //   INF
  //   NaN
  //   Output
endmodule

module _16bitSpecialCases (
  input  [4:0] exp,
  input  [9:0] in_2,
  output Zero,
  output INF,
  output NaN
);

  wire comparator_1_eq, comparator_2_eq, comparator_3_eq, comparator_4_eq, not_1_out;

  Comparator #(.width(5), .mode("unsigned")) comparator_1 (
    .a(exp), .b({5{1'b1}}), .eq(comparator_1_eq));  // open: gt, lt
  Comparator #(.width(10), .mode("unsigned")) comparator_2 (
    .a(in_2), .b({10{1'b0}}), .eq(comparator_2_eq));  // open: gt, lt
  Comparator #(.width(5), .mode("unsigned")) comparator_3 (
    .a(exp), .b({5{1'b0}}), .eq(comparator_3_eq));  // open: gt, lt
  Comparator #(.width(10), .mode("unsigned")) comparator_4 (
    .a({10{1'b0}}), .b(in_2), .eq(comparator_4_eq));  // open: gt, lt
  not not_1 (not_1_out, comparator_2_eq);
  and and_1 (Zero, comparator_3_eq, comparator_4_eq);
  and and_2 (INF, comparator_4_eq, comparator_1_eq);
  and and_3 (NaN, comparator_1_eq, not_1_out);

  // Notes on the sheet:
  //   mantissa
  //   ANJNEY LAWANIYA - 2402CS11
endmodule

module Handler (
  input  [15:0] in_1,
  input  [15:0] in_2,
  output Zero,
  output INF,
  output NaN
);

  wire n16bitspecialcases_1_inf, n16bitspecialcases_1_nan, n16bitspecialcases_1_zero,
       n16bitspecialcases_2_inf, n16bitspecialcases_2_nan, n16bitspecialcases_2_zero, not_1_out, or_1_out;

  _16bitSpecialCases u_16bitspecialcases_1 (
    .exp(in_1[14:10]), .in_2(in_1[9:0]), .Zero(n16bitspecialcases_1_zero), .INF(n16bitspecialcases_1_inf),
    .NaN(n16bitspecialcases_1_nan));
  _16bitSpecialCases u_16bitspecialcases_2 (
    .exp(in_2[14:10]), .in_2(in_2[9:0]), .Zero(n16bitspecialcases_2_zero), .INF(n16bitspecialcases_2_inf),
    .NaN(n16bitspecialcases_2_nan));
  and and_1 (Zero, n16bitspecialcases_1_zero, n16bitspecialcases_2_zero);
  or or_1 (or_1_out, n16bitspecialcases_1_inf, n16bitspecialcases_2_inf);
  not not_1 (not_1_out, NaN);
  or or_2 (NaN, n16bitspecialcases_1_nan, n16bitspecialcases_2_nan);
  and and_2 (INF, or_1_out, not_1_out);

  // Notes on the sheet:
  //   ANJNEY LAWANIYA - 2402CS11
  //   Input A
  //   Input B
endmodule

module _16bitSign (
  input  [15:0] in_1,
  input  [15:0] in_2,
  output Sign_of_greater
);

  wire and_1_out, comparator_1_eq, comparator_1_gt, comparator_2_gt, or_1_out;

  Comparator #(.width(5), .mode("unsigned")) comparator_1 (
    .a(in_1[14:10]), .b(in_2[14:10]), .gt(comparator_1_gt), .eq(comparator_1_eq));  // open: lt
  Comparator #(.width(10), .mode("unsigned")) comparator_2 (
    .a(in_1[9:0]), .b(in_2[9:0]), .gt(comparator_2_gt));  // open: eq, lt
  and and_1 (and_1_out, comparator_1_eq, comparator_2_gt);
  or or_1 (or_1_out, comparator_1_gt, and_1_out);
  Multiplexer multiplexer_1 (.in0(in_2[15]), .in1(in_1[15]), .out(Sign_of_greater), .sel(or_1_out));  // open: en

  // Notes on the sheet:
  //   Sign Bit
  //   Exp
  //   Mantissa
  //   Input A
  //   Input B
  //   ANJNEY LAWANIYA - 2402CS11
endmodule

module ZeroSpCase (
  input  [15:0] in_1,
  input  [15:0] in_2,
  output isZero,
  output [15:0] out_4
);

  wire n16bitspecialcases_1_zero, n16bitspecialcases_2_zero;

  _16bitSpecialCases u_16bitspecialcases_1 (
    .exp(in_1[14:10]), .in_2(in_1[9:0]), .Zero(n16bitspecialcases_1_zero));  // open: INF, NaN
  _16bitSpecialCases u_16bitspecialcases_2 (
    .exp(in_2[14:10]), .in_2(in_2[9:0]), .Zero(n16bitspecialcases_2_zero));  // open: INF, NaN
  Multiplexer #(.width(16)) multiplexer_1 (
    .in0(in_1), .in1(in_2), .out(out_4), .sel(n16bitspecialcases_1_zero));  // open: en
  or or_1 (isZero, n16bitspecialcases_1_zero, n16bitspecialcases_2_zero);

  // Notes on the sheet:
  //   Input B
  //   Input A
  //   ANJNEY LAWANIYA - 2402CS11
  //   Non-Zero
endmodule
