// Logisim project Lab3_2402CS11_anjney_lawaniya.circ as structural Verilog: 4 circuits, main circuit 4x4Register
module _4x4Register (
  input  [3:0] in_1,
  input  in_2,
  input  [1:0] in_3
);

  wire and_1_out, and_2_out, and_3_out, and_4_out, clock_1_out, demultiplexer_1_out0, demultiplexer_1_out1,
       demultiplexer_1_out2, demultiplexer_1_out3;

  Demultiplexer #(.select(2)) demultiplexer_1 (
    .out0(demultiplexer_1_out0), .out1(demultiplexer_1_out1), .out2(demultiplexer_1_out2),
    .out3(demultiplexer_1_out3), .in(in_2), .sel(in_3));  // open: en
  Clock clock_1 (.out(clock_1_out));
  Register #(.width(4)) register_1 (.D(in_1), .en(and_1_out), .clk(clock_1_out));  // open: Q, clr
  and and_1 (and_1_out, in_2, demultiplexer_1_out0);
  Register #(.width(4)) register_2 (.D(in_1), .en(and_2_out), .clk(clock_1_out));  // open: Q, clr
  and and_2 (and_2_out, in_2, demultiplexer_1_out1);
  Register #(.width(4)) register_3 (.D(in_1), .en(and_3_out), .clk(clock_1_out));  // open: Q, clr
  and and_3 (and_3_out, demultiplexer_1_out2, in_2);
  Register #(.width(4)) register_4 (.D(in_1), .en(and_4_out), .clk(clock_1_out));  // open: Q, clr
  and and_4 (and_4_out, demultiplexer_1_out3, in_2);

  // Notes on the sheet:
  //   ANJNEY LAWANIYA - 2402CS11
endmodule

module _32bit_ALU (
  input  [31:0] in_1,
  input  [31:0] in_2,
  input  [2:0] OpCode,
  output isZero,
  output [31:0] out_5
);

  wire subtractor_1_bout;
  wire [31:0] adder_1_out, and_1_out, and_2_out, bit_extender_1_out, not_1_out, or_1_out, or_2_out,
       subtractor_1_out;

  assign not_1_out = ~in_2;  // NOT_Gate not_1, 32 bits wide
  assign and_1_out = in_1 & in_2;  // AND_Gate and_1, 32 bits wide
  assign or_1_out = in_1 | in_2;  // OR_Gate or_1, 32 bits wide
  Adder #(.width(32)) adder_1 (.a(in_1), .b(in_2), .out(adder_1_out));  // open: cin, cout
  assign and_2_out = not_1_out & in_1;  // AND_Gate and_2, 32 bits wide
  assign or_2_out = not_1_out | in_1;  // OR_Gate or_2, 32 bits wide
  Subtractor #(.width(32)) subtractor_1 (
    .a(in_1), .b(in_2), .out(subtractor_1_out), .bout(subtractor_1_bout));  // open: bin
  assign bit_extender_1_out = {{31{1'b0}}, subtractor_1_bout};  // Bit_Extender bit_extender_1
  Multiplexer #(.select(3), .width(32)) multiplexer_1 (
    .in0(and_1_out), .in1(or_1_out), .in2(adder_1_out), .in3({32{1'b0}}), .in4(and_2_out), .in5(or_2_out),
    .in6(subtractor_1_out), .in7(bit_extender_1_out), .out(out_5), .sel(OpCode));  // open: en
  Comparator #(.width(32)) comparator_1 (.a({32{1'b0}}), .b(out_5), .eq(isZero));  // open: gt, lt

  // Notes on the sheet:
  //   A
  //   B
  //   ANJNEY LAWANIYA - 2402CS11
  //   A&B.000
  //   A|B.001
  //   A+B.010
  //   A&~B.100
  //   A|~B.101
  //   A-B.110
  //   Output
endmodule

module _32x32Register (
  input  [4:0] Read_B,
  input  [4:0] Read_A,
  input  in_3,
  input  [4:0] Selection,
  input  in_5,
  input  in_6,
  input  [31:0] in_7,
  output [31:0] out_8,
  output [31:0] out_9
);

  wire and_1_out, and_2_out, and_3_out, and_4_out, and_5_out, and_6_out, and_7_out, and_8_out, and_9_out,
       and_10_out, and_11_out, and_12_out, and_13_out, and_14_out, and_15_out, and_16_out, and_17_out,
       and_18_out, and_19_out, and_20_out, and_21_out, and_22_out, and_23_out, and_24_out, and_25_out,
       and_26_out, and_27_out, and_28_out, and_29_out, and_30_out, and_31_out, demultiplexer_1_out1,
       demultiplexer_1_out2, demultiplexer_1_out3, demultiplexer_1_out4, demultiplexer_1_out5,
       demultiplexer_1_out6, demultiplexer_1_out7, demultiplexer_1_out8, demultiplexer_1_out9,
       demultiplexer_1_out10, demultiplexer_1_out11, demultiplexer_1_out12, demultiplexer_1_out13,
       demultiplexer_1_out14, demultiplexer_1_out15, demultiplexer_1_out16, demultiplexer_1_out17,
       demultiplexer_1_out18, demultiplexer_1_out19, demultiplexer_1_out20, demultiplexer_1_out21,
       demultiplexer_1_out22, demultiplexer_1_out23, demultiplexer_1_out24, demultiplexer_1_out25,
       demultiplexer_1_out26, demultiplexer_1_out27, demultiplexer_1_out28, demultiplexer_1_out29,
       demultiplexer_1_out30, demultiplexer_1_out31;
  wire [31:0] register_1_q, register_2_q, register_3_q, register_4_q, register_5_q, register_6_q,
       register_7_q, register_8_q, register_9_q, register_10_q, register_11_q, register_12_q, register_13_q,
       register_14_q, register_15_q, register_16_q, register_17_q, register_18_q, register_19_q,
       register_20_q, register_21_q, register_22_q, register_23_q, register_24_q, register_25_q,
       register_26_q, register_27_q, register_28_q, register_29_q, register_30_q, register_31_q;

  Demultiplexer #(.select(5)) demultiplexer_1 (
    .out1(demultiplexer_1_out1), .out2(demultiplexer_1_out2), .out3(demultiplexer_1_out3),
    .out4(demultiplexer_1_out4), .out5(demultiplexer_1_out5), .out6(demultiplexer_1_out6),
    .out7(demultiplexer_1_out7), .out8(demultiplexer_1_out8), .out9(demultiplexer_1_out9),
    .out10(demultiplexer_1_out10), .out11(demultiplexer_1_out11), .out12(demultiplexer_1_out12),
    .out13(demultiplexer_1_out13), .out14(demultiplexer_1_out14), .out15(demultiplexer_1_out15),
    .out16(demultiplexer_1_out16), .out17(demultiplexer_1_out17), .out18(demultiplexer_1_out18),
    .out19(demultiplexer_1_out19), .out20(demultiplexer_1_out20), .out21(demultiplexer_1_out21),
    .out22(demultiplexer_1_out22), .out23(demultiplexer_1_out23), .out24(demultiplexer_1_out24),
    .out25(demultiplexer_1_out25), .out26(demultiplexer_1_out26), .out27(demultiplexer_1_out27),
    .out28(demultiplexer_1_out28), .out29(demultiplexer_1_out29), .out30(demultiplexer_1_out30),
    .out31(demultiplexer_1_out31), .in(in_3), .sel(Selection));  // open: out0, en
  and and_1 (and_1_out, in_3, demultiplexer_1_out1);
  and and_2 (and_2_out, in_3, demultiplexer_1_out2);
  and and_3 (and_3_out, in_3, demultiplexer_1_out3);
  and and_4 (and_4_out, in_3, demultiplexer_1_out4);
  and and_5 (and_5_out, in_3, demultiplexer_1_out5);
  and and_6 (and_6_out, in_3, demultiplexer_1_out6);
  and and_7 (and_7_out, in_3, demultiplexer_1_out7);
  and and_8 (and_8_out, in_3, demultiplexer_1_out8);
  and and_9 (and_9_out, in_3, demultiplexer_1_out9);
  and and_10 (and_10_out, in_3, demultiplexer_1_out10);
  and and_11 (and_11_out, in_3, demultiplexer_1_out11);
  and and_12 (and_12_out, in_3, demultiplexer_1_out12);
  and and_13 (and_13_out, in_3, demultiplexer_1_out13);
  and and_14 (and_14_out, in_3, demultiplexer_1_out14);
  and and_15 (and_15_out, in_3, demultiplexer_1_out15);
  and and_16 (and_16_out, in_3, demultiplexer_1_out16);
  and and_17 (and_17_out, in_3, demultiplexer_1_out17);
  and and_18 (and_18_out, in_3, demultiplexer_1_out18);
  and and_19 (and_19_out, in_3, demultiplexer_1_out19);
  and and_20 (and_20_out, in_3, demultiplexer_1_out20);
  and and_21 (and_21_out, in_3, demultiplexer_1_out21);
  and and_22 (and_22_out, in_3, demultiplexer_1_out22);
  and and_23 (and_23_out, in_3, demultiplexer_1_out23);
  and and_24 (and_24_out, in_3, demultiplexer_1_out24);
  and and_25 (and_25_out, in_3, demultiplexer_1_out25);
  and and_26 (and_26_out, in_3, demultiplexer_1_out26);
  and and_27 (and_27_out, in_3, demultiplexer_1_out27);
  and and_28 (and_28_out, in_3, demultiplexer_1_out28);
  and and_29 (and_29_out, in_3, demultiplexer_1_out29);
  and and_30 (and_30_out, in_3, demultiplexer_1_out30);
  and and_31 (and_31_out, in_3, demultiplexer_1_out31);
  Register #(.width(32)) register_1 (.D(in_7), .en(and_1_out), .Q(register_1_q), .clk(in_6), .clr(in_5));
  Register #(.width(32)) register_2 (.D(in_7), .en(and_2_out), .Q(register_2_q), .clk(in_6), .clr(in_5));
  Register #(.width(32)) register_3 (.D(in_7), .en(and_3_out), .Q(register_3_q), .clk(in_6), .clr(in_5));
  Register #(.width(32)) register_4 (.D(in_7), .en(and_4_out), .Q(register_4_q), .clk(in_6), .clr(in_5));
  Register #(.width(32)) register_5 (.D(in_7), .en(and_5_out), .Q(register_5_q), .clk(in_6), .clr(in_5));
  Register #(.width(32)) register_6 (.D(in_7), .en(and_6_out), .Q(register_6_q), .clk(in_6), .clr(in_5));
  Register #(.width(32)) register_7 (.D(in_7), .en(and_7_out), .Q(register_7_q), .clk(in_6), .clr(in_5));
  Register #(.width(32)) register_8 (.D(in_7), .en(and_8_out), .Q(register_8_q), .clk(in_6), .clr(in_5));
  Register #(.width(32)) register_9 (.D(in_7), .en(and_9_out), .Q(register_9_q), .clk(in_6), .clr(in_5));
  Register #(.width(32)) register_10 (.D(in_7), .en(and_10_out), .Q(register_10_q), .clk(in_6), .clr(in_5));
  Register #(.width(32)) register_11 (.D(in_7), .en(and_11_out), .Q(register_11_q), .clk(in_6), .clr(in_5));
  Register #(.width(32)) register_12 (.D(in_7), .en(and_12_out), .Q(register_12_q), .clk(in_6), .clr(in_5));
  Register #(.width(32)) register_13 (.D(in_7), .en(and_13_out), .Q(register_13_q), .clk(in_6), .clr(in_5));
  Register #(.width(32)) register_14 (.D(in_7), .en(and_14_out), .Q(register_14_q), .clk(in_6), .clr(in_5));
  Register #(.width(32)) register_15 (.D(in_7), .en(and_15_out), .Q(register_15_q), .clk(in_6), .clr(in_5));
  Register #(.width(32)) register_16 (.D(in_7), .en(and_16_out), .Q(register_16_q), .clk(in_6), .clr(in_5));
  Register #(.width(32)) register_17 (.D(in_7), .en(and_17_out), .Q(register_17_q), .clk(in_6), .clr(in_5));
  Register #(.width(32)) register_18 (.D(in_7), .en(and_18_out), .Q(register_18_q), .clk(in_6), .clr(in_5));
  Register #(.width(32)) register_19 (.D(in_7), .en(and_19_out), .Q(register_19_q), .clk(in_6), .clr(in_5));
  Register #(.width(32)) register_20 (.D(in_7), .en(and_20_out), .Q(register_20_q), .clk(in_6), .clr(in_5));
  Register #(.width(32)) register_21 (.D(in_7), .en(and_21_out), .Q(register_21_q), .clk(in_6), .clr(in_5));
  Register #(.width(32)) register_22 (.D(in_7), .en(and_22_out), .Q(register_22_q), .clk(in_6), .clr(in_5));
  Register #(.width(32)) register_23 (.D(in_7), .en(and_23_out), .Q(register_23_q), .clk(in_6), .clr(in_5));
  Register #(.width(32)) register_24 (.D(in_7), .en(and_24_out), .Q(register_24_q), .clk(in_6), .clr(in_5));
  Register #(.width(32)) register_25 (.D(in_7), .en(and_25_out), .Q(register_25_q), .clk(in_6), .clr(in_5));
  Register #(.width(32)) register_26 (.D(in_7), .en(and_26_out), .Q(register_26_q), .clk(in_6), .clr(in_5));
  Register #(.width(32)) register_27 (.D(in_7), .en(and_27_out), .Q(register_27_q), .clk(in_6), .clr(in_5));
  Register #(.width(32)) register_28 (.D(in_7), .en(and_28_out), .Q(register_28_q), .clk(in_6), .clr(in_5));
  Register #(.width(32)) register_29 (.D(in_7), .en(and_29_out), .Q(register_29_q), .clk(in_6), .clr(in_5));
  Register #(.width(32)) register_30 (.D(in_7), .en(and_30_out), .Q(register_30_q), .clk(in_6), .clr(in_5));
  Register #(.width(32)) register_31 (.D(in_7), .en(and_31_out), .Q(register_31_q), .clk(in_6), .clr(in_5));
  Multiplexer #(.select(5), .width(32)) multiplexer_1 (
    .in0({32{1'b0}}), .in1(register_1_q), .in2(register_2_q), .in3(register_3_q), .in4(register_4_q),
    .in5(register_5_q), .in6(register_6_q), .in7(register_7_q), .in8(register_8_q), .in9(register_9_q),
    .in10(register_10_q), .in11(register_11_q), .in12(register_12_q), .in13(register_13_q),
    .in14(register_14_q), .in15(register_15_q), .in16(register_16_q), .in17(register_17_q),
    .in18(register_18_q), .in19(register_19_q), .in20(register_20_q), .in21(register_21_q),
    .in22(register_22_q), .in23(register_23_q), .in24(register_24_q), .in25(register_25_q),
    .in26(register_26_q), .in27(register_27_q), .in28(register_28_q), .in29(register_29_q),
    .in30(register_30_q), .in31(register_31_q), .out(out_8), .sel(Read_A));  // open: en
  Multiplexer #(.select(5), .width(32)) multiplexer_2 (
    .in0({32{1'b0}}), .in1(register_1_q), .in2(register_2_q), .in3(register_3_q), .in4(register_4_q),
    .in5(register_5_q), .in6(register_6_q), .in7(register_7_q), .in8(register_8_q), .in9(register_9_q),
    .in10(register_10_q), .in11(register_11_q), .in12(register_12_q), .in13(register_13_q),
    .in14(register_14_q), .in15(register_15_q), .in16(register_16_q), .in17(register_17_q),
    .in18(register_18_q), .in19(register_19_q), .in20(register_20_q), .in21(register_21_q),
    .in22(register_22_q), .in23(register_23_q), .in24(register_24_q), .in25(register_25_q),
    .in26(register_26_q), .in27(register_27_q), .in28(register_28_q), .in29(register_29_q),
    .in30(register_30_q), .in31(register_31_q), .out(out_9), .sel(Read_B));  // open: en

  // Notes on the sheet:
  //   ANJNEY LAWANIYA - 2402CS11   
  //   ANJNEY LAWANIYA - 2402CS11
  //   Input
  //   Clear
  //   YOU HAVE REACHED THE END OF BEGINNING  - ANJNEY LAWANIYA
  //   11
  //   12
  //   13
  //   14
  //   15
  //   16
  //   17
  //   18
  //   19
  //   20
  //   21
  //   22
  //   23
  //   24
  //   25
  //   26
  //   28
  //   29
  //   31
  //   Clk
  //   1
  //   2
  //   3
  //   4
  //   5
  //   6
  //   7
  //   8
  //   9
  //   27
  //   30
  //   10
  //   A
  //   B
endmodule

module ALU_Operator (
  input  [4:0] Read_B,
  input  [4:0] Read_A,
  input  [2:0] OpCode,
  input  in_4,
  input  [4:0] Write_Address,
  input  Cl,
  input  en,
  input  in_8,
  input  [31:0] in_9,
  output [31:0] out_10,
  output [31:0] out_11,
  output [31:0] Output
);

  wire clock_1_out;
  wire [31:0] multiplexer_1_out;

  _32x32Register u_32x32register_1 (
    .Read_B(Read_B), .Read_A(Read_A), .in_3(in_4), .out_8(out_10), .out_9(out_11), .in_7(multiplexer_1_out),
    .in_6(clock_1_out), .in_5(Cl), .Selection(Write_Address));
  Clock clock_1 (.out(clock_1_out));
  _32bit_ALU u_32bit_alu_1 (.in_1(out_10), .in_2(out_11), .out_5(Output), .OpCode(OpCode));  // open: isZero
  Multiplexer #(.width(32)) multiplexer_1 (.in0(Output), .in1(in_9), .out(multiplexer_1_out), .sel(in_8), .en(en));

  // Notes on the sheet:
  //   ANJNEY LAWANiYA - 2402CS11
  //   CLK
  //   Input
  //   Check A
  //   Check B
endmodule
