// Logisim project Lab6.circ as structural Verilog: 10 circuits, main circuit Memory_Block
module Memory_Block (
  input  [31:0] in_1,
  input  [31:0] in_2,
  input  Write_En,
  input  Clock,
  output [31:0] out_5
);

  RAM #(.addrWidth(24), .dataWidth(32), .bus("separate")) ram_1 (
    .addr(in_1[25:2]), .din(in_2), .data(out_5), .str(Write_En), .sel(1'b1), .clk(Clock), .ld(1'b1),
    .clr(1'b0));

  // Notes on the sheet:
  //   Write_Address
  //   Address
  //   Read_Address
endmodule

module Datapath_sw (
  input  [5:0] opCode,
  input  [2:0] in_2,
  input  Reg_Write,
  input  in_4,
  input  in_5,
  output [31:0] out_6
);

  wire clock_1_out;
  wire [4:0] instruction_splitter_1_rs, instruction_splitter_1_rt;
  wire [15:0] instruction_splitter_1_out_3;
  wire [23:0] register_1_q, shifter_1_out, shifter_2_out;
  wire [31:0] adder_1_out, alu_1_out_5, bit_extender_1_out, n32x32register_1_out_8, n32x32register_1_out_9,
       rom_1_data;
  wire [31:24] register_1_q_2;

  Clock clock_1 (.out(clock_1_out));
  Register #(.width(32)) register_1 (
    .D(adder_1_out), .Q({register_1_q_2, register_1_q}), .clk(clock_1_out), .clr(in_4));  // open: en
  Shifter #(.width(24), .shift("lr")) shifter_1 (.in(register_1_q), .\dist (5'b00010), .out(shifter_1_out));
  Adder #(.width(32)) adder_1 (.a({register_1_q_2, register_1_q}), .b(32'h4), .out(adder_1_out));  // open: cin, cout
  ROM #(.addrWidth(24), .dataWidth(32)) rom_1 (.addr(shifter_1_out), .data(rom_1_data));  // open: sel
  Instruction_Splitter instruction_splitter_1 (
    .in_1(rom_1_data), .out_3(instruction_splitter_1_out_3), .rt(instruction_splitter_1_rt),
    .rs(instruction_splitter_1_rs));  // open: Func, out_4, rd, opCode
  assign bit_extender_1_out = {{16{instruction_splitter_1_out_3[15]}}, instruction_splitter_1_out_3};  // Bit_Extender bit_extender_1
  _32x32Register u_32x32register_1 (
    .Read_B(instruction_splitter_1_rt), .Read_A(instruction_splitter_1_rs), .in_3(Reg_Write),
    .out_8(n32x32register_1_out_8), .out_9(n32x32register_1_out_9), .in_7(out_6), .in_6(clock_1_out),
    .in_5(in_5));  // open: Selection
  ALUcontrol alucontrol_1 (.Opcode(opCode));  // open: ALUcode
  ALU alu_1 (
    .Function(in_2), .in_2(n32x32register_1_out_8), .in_3(bit_extender_1_out), .out_5(alu_1_out_5));  // open: isZero
  Shifter #(.width(24), .shift("lr")) shifter_2 (.in(alu_1_out_5[23:0]), .\dist (5'b00010), .out(shifter_2_out));
  RAM #(.addrWidth(24), .dataWidth(32), .bus("separate")) ram_1 (
    .addr(shifter_2_out), .din(n32x32register_1_out_9), .data(out_6), .clk(clock_1_out));  // open: str, sel, ld, clr

  // Notes on the sheet:
  //   PC
  //   opCode for sw = 101011
  //   DATAPATH SW
  //   contents of rom_1 (hex, n*v repeats v):
  //   8c020004 2003000c 2067fff7 e22025 642824 a42820 10a7000a 64202a 10800001 20050000 e2202a 853820
  //   e23822 ac670044 8c020050 8000011 20020001 ac020054
endmodule

module Instruction_Splitter (
  input  [31:0] in_1,
  output [5:0] Func,
  output [15:0] out_3,
  output [25:0] out_4,
  output [4:0] rd,
  output [4:0] rt,
  output [4:0] rs,
  output [5:0] opCode
);


  assign Func = in_1[5:0];
  assign opCode = in_1[31:26];
  assign out_3 = in_1[15:0];
  assign out_4 = in_1[25:0];
  assign rd = in_1[15:11];
  assign rs = in_1[25:21];
  assign rt = in_1[20:16];

  // Notes on the sheet:
  //   Input Machine Code
  //   Immediate
  //   Jump Address
endmodule

module ALUcontrol (
  input  [5:0] Opcode,
  output [2:0] ALUcode
);

  wire and_1_out, and_2_out, and_3_out, not_1_out, not_2_out, not_3_out, not_4_out;

  not not_1 (not_1_out, Opcode[0]);
  not not_2 (not_2_out, Opcode[3]);
  not not_3 (not_3_out, Opcode[2]);
  not not_4 (not_4_out, Opcode[1]);
  and and_1 (and_1_out, Opcode[2], not_1_out);
  and and_2 (and_2_out, Opcode[1], not_2_out);
  and and_3 (and_3_out, not_3_out, not_4_out);
  or or_1 (ALUcode[2], Opcode[3], and_1_out);
  or or_2 (ALUcode[1], Opcode[0], and_2_out);
  or or_3 (ALUcode[0], Opcode[0], Opcode[3], and_3_out);
endmodule

module ALU (
  input  [2:0] Function,
  input  [31:0] in_2,
  input  [31:0] in_3,
  output isZero,
  output [31:0] out_5
);

  wire [31:0] adder_1_out, and_1_out, bit_extender_1_out, multiplexer_1_out, not_1_out, or_1_out;

  assign not_1_out = ~in_2;  // NOT_Gate not_1, 32 bits wide
  Multiplexer #(.width(32), .enable("false")) multiplexer_1 (
    .in0(in_2), .in1(not_1_out), .out(multiplexer_1_out), .sel(Function[2]));
  assign and_1_out = multiplexer_1_out & in_3;  // AND_Gate and_1, 32 bits wide
  assign or_1_out = multiplexer_1_out | in_3;  // OR_Gate or_1, 32 bits wide
  Adder #(.width(32)) adder_1 (.a(multiplexer_1_out), .b(in_3), .out(adder_1_out), .cin(Function[2]));  // open: cout
  assign bit_extender_1_out = {{1{1'b0}}, adder_1_out[30:0]};  // Bit_Extender bit_extender_1
  Multiplexer #(.select(2), .width(32), .enable("false")) multiplexer_2 (
    .in0(and_1_out), .in1(or_1_out), .in2(adder_1_out), .in3(bit_extender_1_out), .out(out_5),
    .sel(Function[1:0]));
  Comparator #(.width(32)) comparator_1 (.a({32{1'b0}}), .b(out_5), .eq(isZero));  // open: gt, lt

  // Notes on the sheet:
  //   B
  //   A
endmodule

module Datapath_addi (
  input  RegDst,
  input  ALU_Src,
  input  [2:0] ALU_OP,
  input  in_4,
  input  in_5,
  output [31:0] out_6
);

  wire clock_1_out;
  wire [4:0] instruction_splitter_1_rd, instruction_splitter_1_rs, instruction_splitter_1_rt,
       multiplexer_1_out;
  wire [15:0] instruction_splitter_1_out_3;
  wire [23:0] register_1_q, shifter_1_out;
  wire [31:0] adder_1_out, bit_extender_1_out, multiplexer_2_out, n32x32register_1_p7, n32x32register_1_p8,
       rom_1_data;
  wire [31:24] register_1_q_2;

  Clock clock_1 (.out(clock_1_out));
  Register #(.width(32)) register_1 (
    .D(adder_1_out), .Q({register_1_q_2, register_1_q}), .clk(clock_1_out), .clr(in_5));  // open: en
  Shifter #(.width(24), .shift("lr")) shifter_1 (.in(register_1_q), .\dist (5'b00010), .out(shifter_1_out));
  Adder #(.width(32)) adder_1 (.a({register_1_q_2, register_1_q}), .b(32'h4), .out(adder_1_out));  // open: cin, cout
  ROM #(.addrWidth(24), .dataWidth(32)) rom_1 (.addr(shifter_1_out), .data(rom_1_data));  // open: sel
  Instruction_Splitter instruction_splitter_1 (
    .in_1(rom_1_data), .out_3(instruction_splitter_1_out_3), .rd(instruction_splitter_1_rd),
    .rt(instruction_splitter_1_rt), .rs(instruction_splitter_1_rs));  // open: Func, out_4, opCode
  Multiplexer #(.width(5), .enable("false")) multiplexer_1 (
    .in0(instruction_splitter_1_rd), .in1(instruction_splitter_1_rt), .out(multiplexer_1_out), .sel(RegDst));
  assign bit_extender_1_out = {{16{instruction_splitter_1_out_3[15]}}, instruction_splitter_1_out_3};  // Bit_Extender bit_extender_1
  // _32x32Register 32x32register_1: pin names not known; wires that end beside it: out_6, in_4, multiplexer_1_out, instruction_splitter_1_rt, clock_1_out, instruction_splitter_1_rs, n32x32register_1_p7, n32x32register_1_p8
  Multiplexer #(.width(32), .enable("false")) multiplexer_2 (
    .in0(n32x32register_1_p7), .in1(bit_extender_1_out), .out(multiplexer_2_out), .sel(ALU_Src));
  ALU alu_1 (.Function(ALU_OP), .in_2(multiplexer_2_out), .in_3(n32x32register_1_p8), .out_5(out_6));  // open: isZero

  // Notes on the sheet:
  //   DATAPATH ADDI
  //   contents of rom_1 (hex, n*v repeats v):
  //   20020005 2003000c 2067fff7 e22025 642824 a42820 10a7000a 64202a 10800001 20050000 e2202a 853820
  //   e23822 ac670044 8c020050 8000011 20020001 ac020054
endmodule

module Datapath_or (
  input  in_1,
  input  in_2,
  output [31:0] out_3
);

  wire clock_1_out;
  wire [2:0] alucontrol_1_alucode;
  wire [4:0] instruction_splitter_1_rd, instruction_splitter_1_rs, instruction_splitter_1_rt;
  wire [5:0] instruction_splitter_1_func;
  wire [23:0] shifter_1_out;
  wire [31:0] adder_1_out, n32x32register_1_p6, n32x32register_1_p7, register_1_q, rom_1_data;

  Register #(.width(32)) register_1 (.D(adder_1_out), .en(1'b1), .Q(register_1_q), .clk(clock_1_out), .clr(in_2));
  Clock clock_1 (.out(clock_1_out));
  Shifter #(.width(24), .shift("lr")) shifter_1 (.in(register_1_q[23:0]), .\dist (5'b00010), .out(shifter_1_out));
  Adder #(.width(32)) adder_1 (.a(register_1_q), .b(32'h4), .out(adder_1_out));  // open: cin, cout
  ROM #(.addrWidth(24), .dataWidth(32)) rom_1 (.addr(shifter_1_out), .data(rom_1_data));  // open: sel
  Instruction_Splitter instruction_splitter_1 (
    .in_1(rom_1_data), .Func(instruction_splitter_1_func), .rd(instruction_splitter_1_rd),
    .rt(instruction_splitter_1_rt), .rs(instruction_splitter_1_rs));  // open: out_3, out_4, opCode
  // _32x32Register 32x32register_1: pin names not known; wires that end beside it: in_1, instruction_splitter_1_rd, instruction_splitter_1_rs, clock_1_out, instruction_splitter_1_rt, n32x32register_1_p6, n32x32register_1_p7
  ALU alu_1 (
    .Function(alucontrol_1_alucode), .in_2(n32x32register_1_p7), .in_3(n32x32register_1_p6), .out_5(out_3));  // open: isZero
  ALUcontrol alucontrol_1 (.Opcode(instruction_splitter_1_func), .ALUcode(alucontrol_1_alucode));

  // Notes on the sheet:
  //   DATAPATH OR
  //   contents of rom_1 (hex, n*v repeats v):
  //   8432000 c0100014 2067fff7 e22025 642824 a42820 10a7000a 64202a 10800001 20050000 e2202a 853820
  //   e23822 ac670044 8c020050 8000011 20020001 ac020054
endmodule

module Datapath_and (
  input  in_1,
  input  in_2,
  output [31:0] out_3
);

  wire clock_1_out;
  wire [2:0] alucontrol_1_alucode;
  wire [4:0] instruction_splitter_1_rd, instruction_splitter_1_rs, instruction_splitter_1_rt;
  wire [5:0] instruction_splitter_1_func;
  wire [23:0] register_1_q, shifter_1_out;
  wire [31:0] adder_1_out, n32x32register_1_p7, n32x32register_1_p8, rom_1_data;
  wire [31:24] register_1_q_2;

  Register #(.width(32)) register_1 (
    .D(adder_1_out), .Q({register_1_q_2, register_1_q}), .clk(clock_1_out), .clr(in_2));  // open: en
  Clock clock_1 (.out(clock_1_out));
  Shifter #(.width(24), .shift("lr")) shifter_1 (.in(register_1_q), .\dist (5'b00010), .out(shifter_1_out));
  Adder #(.width(32)) adder_1 (.a({register_1_q_2, register_1_q}), .b(32'h4), .out(adder_1_out));  // open: cin, cout
  ROM #(.addrWidth(24), .dataWidth(32)) rom_1 (.addr(shifter_1_out), .data(rom_1_data));  // open: sel
  Instruction_Splitter instruction_splitter_1 (
    .in_1(rom_1_data), .Func(instruction_splitter_1_func), .rd(instruction_splitter_1_rd),
    .rt(instruction_splitter_1_rt), .rs(instruction_splitter_1_rs));  // open: out_3, out_4, opCode
  // _32x32Register 32x32register_1: pin names not known; wires that end beside it: out_3, in_1, instruction_splitter_1_rd, instruction_splitter_1_rs, clock_1_out, instruction_splitter_1_rt, n32x32register_1_p7, n32x32register_1_p8
  ALUcontrol alucontrol_1 (.Opcode(instruction_splitter_1_func), .ALUcode(alucontrol_1_alucode));
  ALU alu_1 (
    .Function(alucontrol_1_alucode), .in_2(n32x32register_1_p8), .in_3(n32x32register_1_p7), .out_5(out_3));  // open: isZero

  // Notes on the sheet:
  //   DATAPATH AND
  //   contents of rom_1 (hex, n*v repeats v):
  //   8432000 c0100014 2067fff7 e22025 642824 a42820 10a7000a 64202a 10800001 20050000 e2202a 853820
  //   e23822 ac670044 8c020050 8000011 20020001 ac020054
  //   Output
endmodule

module Datapath_add (
  input  in_1,
  input  in_2,
  input  in_3,
  output [31:0] out_4
);

  wire clock_1_out;
  wire [2:0] alucontrol_1_alucode;
  wire [4:0] instruction_splitter_1_rd, instruction_splitter_1_rs, instruction_splitter_1_rt;
  wire [5:0] instruction_splitter_1_func;
  wire [23:0] shifter_1_out;
  wire [31:0] adder_1_out, n32x32register_1_p8, n32x32register_1_p9, register_1_q, rom_1_data;

  Register #(.width(32)) register_1 (.D(adder_1_out), .Q(register_1_q), .clk(clock_1_out), .clr(in_2));  // open: en
  Clock clock_1 (.out(clock_1_out));
  Shifter #(.width(24), .shift("lr")) shifter_1 (.in(register_1_q[23:0]), .\dist (5'b00010), .out(shifter_1_out));
  Adder #(.width(32)) adder_1 (.a(register_1_q), .b(32'h4), .out(adder_1_out));  // open: cin, cout
  ROM #(.addrWidth(24), .dataWidth(32)) rom_1 (.addr(shifter_1_out), .data(rom_1_data));  // open: sel
  Instruction_Splitter instruction_splitter_1 (
    .in_1(rom_1_data), .Func(instruction_splitter_1_func), .rd(instruction_splitter_1_rd),
    .rt(instruction_splitter_1_rt), .rs(instruction_splitter_1_rs));  // open: out_3, out_4, opCode
  // _32x32Register 32x32register_1: pin names not known; wires that end beside it: out_4, in_1, instruction_splitter_1_rd, instruction_splitter_1_rs, in_3, clock_1_out, instruction_splitter_1_rt, n32x32register_1_p8, n32x32register_1_p9
  ALU alu_1 (
    .Function(alucontrol_1_alucode), .in_2(n32x32register_1_p9), .in_3(n32x32register_1_p8), .out_5(out_4));  // open: isZero
  ALUcontrol alucontrol_1 (.Opcode(instruction_splitter_1_func), .ALUcode(alucontrol_1_alucode));

  // Notes on the sheet:
  //   DATAPATH ADD
  //   contents of rom_1 (hex, n*v repeats v):
  //   8432000 c0100014 2067fff7 e22025 642824 a42820 10a7000a 64202a 10800001 20050000 e2202a 853820
  //   e23822 ac670044 8c020050 8000011 20020001 ac020054
  //   Opcode
endmodule

module Datapath_beq (
  input  RegDst,
  input  ALUsrc,
  input  [5:0] in_3,
  input  in_4,
  input  in_5
);

  wire alu_1_iszero, clock_1_out, isBranch;
  wire [2:0] alucontrol_1_alucode;
  wire [4:0] instruction_splitter_1_rd, instruction_splitter_1_rs, instruction_splitter_1_rt,
       multiplexer_2_out;
  wire [15:0] instruction_splitter_1_out_3;
  wire [23:0] shifter_1_out;
  wire [31:0] adder_1_out, adder_2_out, alu_1_out_5, bit_extender_1_out, multiplexer_1_out,
       multiplexer_3_out, n32x32register_1_p5, n32x32register_1_p6, register_1_q, rom_1_data;

  Multiplexer #(.width(32)) multiplexer_1 (
    .in0(adder_2_out), .in1(adder_1_out), .out(multiplexer_1_out), .sel(isBranch));  // open: en
  Register #(.width(32)) register_1 (
    .D(multiplexer_1_out), .Q(register_1_q), .clk(clock_1_out), .clr(in_5));  // open: en
  Adder #(.width(32)) adder_1 (.a(register_1_q), .b(alu_1_out_5), .out(adder_1_out));  // open: cin, cout
  Clock clock_1 (.out(clock_1_out));
  Shifter #(.width(24), .shift("lr")) shifter_1 (.in(register_1_q[23:0]), .\dist (5'b00010), .out(shifter_1_out));
  Adder #(.width(32)) adder_2 (.a(register_1_q), .b(32'h4), .out(adder_2_out));  // open: cin, cout
  ROM #(.addrWidth(24), .dataWidth(32)) rom_1 (.addr(shifter_1_out), .data(rom_1_data));  // open: sel
  Instruction_Splitter instruction_splitter_1 (
    .in_1(rom_1_data), .out_3(instruction_splitter_1_out_3), .rd(instruction_splitter_1_rd),
    .rt(instruction_splitter_1_rt), .rs(instruction_splitter_1_rs));  // open: Func, out_4, opCode
  Multiplexer #(.width(5)) multiplexer_2 (
    .in0(instruction_splitter_1_rd), .in1(instruction_splitter_1_rt), .out(multiplexer_2_out), .sel(RegDst));  // open: en
  assign bit_extender_1_out = {{16{1'b0}}, instruction_splitter_1_out_3};  // Bit_Extender bit_extender_1
  // _32x32Register 32x32register_1: pin names not known; wires that end beside it: multiplexer_2_out, instruction_splitter_1_rs, clock_1_out, instruction_splitter_1_rt, n32x32register_1_p5, n32x32register_1_p6
  Multiplexer #(.width(32)) multiplexer_3 (
    .in0(n32x32register_1_p5), .in1(bit_extender_1_out), .out(multiplexer_3_out), .sel(ALUsrc));  // open: en
  ALU alu_1 (
    .Function(alucontrol_1_alucode), .in_2(n32x32register_1_p6), .in_3(multiplexer_3_out),
    .out_5(alu_1_out_5), .isZero(alu_1_iszero));
  ALUcontrol alucontrol_1 (.Opcode(in_3), .ALUcode(alucontrol_1_alucode));
  and and_1 (isBranch, in_4, alu_1_iszero);

  // Other names for the same wires on the sheet: Branch = in_4

  // Notes on the sheet:
  //   DATAPATH BEQ
  //   contents of rom_1 (hex, n*v repeats v):
  //   8432000 c0100014 2067fff7 e22025 642824 a42820 10a7000a 64202a 10800001 20050000 e2202a 853820
  //   e23822 ac670044 8c020050 8000011 20020001 ac020054
endmodule
