// Logisim project Lab6_Demo.circ as structural Verilog: 12 circuits, main circuit Datapath-ex
module main (
  input  Clear_PC
);

  wire clock_1_out, undriven, undriven_2, undriven_4, undriven_5, undriven_8, undriven_9;
  wire [1:0] undriven_3;
  wire [2:0] alucont_1_out_2;
  wire [4:0] instruction_splitter_1_reg_read_rd, instruction_splitter_1_reg_read_rs,
       instruction_splitter_1_reg_read_rt, multiplexer_4_out;
  wire [5:0] instruction_splitter_1_function, instruction_splitter_1_opcode;
  wire [15:0] instruction_splitter_1_constant_address;
  wire [23:0] shifter_2_out, shifter_4_out;
  wire [25:0] instruction_splitter_1_address, shifter_1_out;
  wire [31:0] adder_1_out, adder_2_out, alu_1_out_4, and_1_out, bit_extender_1_out, bit_extender_2_out,
       multiplexer_1_out, multiplexer_2_out, multiplexer_3_out, multiplexer_5_out, multiplexer_6_out,
       ram_1_data, reg32_1_value_0, reg32_1_value_1, register_1_q, rom_1_data, shifter_3_out, undriven_6,
       undriven_7;

  Multiplexer #(.width(32), .enable("false")) multiplexer_1 (
    .in0(adder_1_out), .in1(adder_2_out), .out(multiplexer_1_out), .sel(and_1_out[0]));
  Multiplexer #(.width(32), .enable("false")) multiplexer_2 (
    .in0(multiplexer_1_out), .in1(bit_extender_1_out), .out(multiplexer_2_out), .sel(undriven));
  Clock clock_1 (.out(clock_1_out));
  Register #(.width(32)) register_1 (
    .D(multiplexer_2_out), .Q(register_1_q), .clk(clock_1_out), .clr(Clear_PC));  // open: en
  Shifter #(.width(26)) shifter_1 (.in(instruction_splitter_1_address), .\dist (5'b00010), .out(shifter_1_out));
  Shifter #(.width(24), .shift("lr")) shifter_2 (.in(register_1_q[23:0]), .\dist (5'b00010), .out(shifter_2_out));
  Adder #(.width(32)) adder_1 (.a(register_1_q), .b(32'h4), .out(adder_1_out));  // open: cin, cout
  assign bit_extender_1_out = {{6{1'b0}}, shifter_1_out};  // Bit_Extender bit_extender_1
  ROM #(.addrWidth(24), .dataWidth(32)) rom_1 (.addr(shifter_2_out), .data(rom_1_data));  // open: sel
  Multiplexer #(.width(32), .enable("false")) multiplexer_3 (
    .in0(multiplexer_6_out), .in1(adder_1_out), .out(multiplexer_3_out), .sel(undriven_2));
  Instruction_Splitter instruction_splitter_1 (
    .in_1(rom_1_data), .Function(instruction_splitter_1_function),
    .Constant_Address(instruction_splitter_1_constant_address),
    .Reg_read_rd(instruction_splitter_1_reg_read_rd), .Address(instruction_splitter_1_address),
    .Reg_read_rt(instruction_splitter_1_reg_read_rt), .Reg_read_rs(instruction_splitter_1_reg_read_rs),
    .Opcode(instruction_splitter_1_opcode));
  Multiplexer #(.select(2), .width(5), .enable("false")) multiplexer_4 (
    .in0(instruction_splitter_1_reg_read_rt), .in1(instruction_splitter_1_reg_read_rd), .in2(5'b10001),
    .out(multiplexer_4_out), .sel(undriven_3));  // open: in3
  assign bit_extender_2_out = {{16{instruction_splitter_1_constant_address[15]}}, instruction_splitter_1_constant_address};  // Bit_Extender bit_extender_2
  ALUcont alucont_1 (.in_1(instruction_splitter_1_function), .out_2(alucont_1_out_2));
  reg32 reg32_1 (
    .Read_0(instruction_splitter_1_reg_read_rs), .Read_1(instruction_splitter_1_reg_read_rt),
    .write_addr(multiplexer_4_out), .RegWrite(undriven_4), .Clock(clock_1_out),
    .write_value(multiplexer_3_out), .Value_0(reg32_1_value_0), .Value_1(reg32_1_value_1));  // open: RegClear
  Multiplexer #(.width(32), .enable("false")) multiplexer_5 (
    .in0(reg32_1_value_1), .in1(bit_extender_2_out), .out(multiplexer_5_out), .sel(undriven_5));
  ALU alu_1 (.Function(alucont_1_out_2), .Input_B(reg32_1_value_0), .Input_A(multiplexer_5_out), .out_4(alu_1_out_4));
  Shifter #(.width(32)) shifter_3 (.in(bit_extender_2_out), .\dist (5'b00010), .out(shifter_3_out));
  Adder #(.width(32)) adder_2 (.a(shifter_3_out), .b(adder_1_out), .out(adder_2_out));  // open: cin, cout
  assign and_1_out = undriven_7 & alu_1_out_4;  // AND_Gate and_1, 32 bits wide
  Shifter #(.width(24), .shift("lr")) shifter_4 (.in(undriven_6[23:0]), .\dist (5'b00010), .out(shifter_4_out));
  RAM #(.addrWidth(24), .dataWidth(32), .bus("separate")) ram_1 (
    .addr(shifter_4_out), .din(reg32_1_value_1), .data(ram_1_data), .str(undriven_8), .clk(clock_1_out));  // open: sel, ld, clr
  Multiplexer #(.width(32), .enable("false")) multiplexer_6 (
    .in0(undriven_6), .in1(ram_1_data), .out(multiplexer_6_out), .sel(undriven_9));
  // Pins of 1 and 32 bits meet at and_1_out

  // Notes on the sheet:
  //   contents of rom_1 (hex, n*v repeats v):
  //   20020005 2003000c 2067fff7 e22025 642824 a42820 10a7000a 64202a 10800001 20050000 e2202a 853820
  //   e23822 ac670044 8c020050 8000011 20020001 ac020054
  //   Memory location 84(01010100) is shifted right by 2 (010101) and then stored in RAM
endmodule

module reg32 (
  input  [4:0] Read_0,
  input  [4:0] Read_1,
  input  [4:0] write_addr,
  input  [31:0] write_value,
  input  Clock,
  input  RegClear,
  input  RegWrite,
  output [31:0] Value_0,
  output [31:0] Value_1
);

  wire and_1_out, and_2_out, and_3_out, and_4_out, and_5_out, and_6_out, and_7_out, and_8_out, and_9_out,
       and_10_out, and_11_out, and_12_out, and_13_out, and_14_out, and_15_out, and_16_out, and_17_out,
       and_18_out, and_19_out, and_20_out, and_21_out, and_22_out, and_23_out, and_24_out, and_25_out,
       and_26_out, and_27_out, and_28_out, and_29_out, and_30_out, and_31_out, decoder_1_out1,
       decoder_1_out2, decoder_1_out3, decoder_1_out4, decoder_1_out5, decoder_1_out6, decoder_1_out7,
       decoder_1_out8, decoder_1_out9, decoder_1_out10, decoder_1_out11, decoder_1_out12, decoder_1_out13,
       decoder_1_out14, decoder_1_out15, decoder_1_out16, decoder_1_out17, decoder_1_out18, decoder_1_out19,
       decoder_1_out20, decoder_1_out21, decoder_1_out22, decoder_1_out23, decoder_1_out24, decoder_1_out25,
       decoder_1_out26, decoder_1_out27, decoder_1_out28, decoder_1_out29, decoder_1_out30, decoder_1_out31;
  wire [31:0] a0_q, a1_q, a2_q, a3_q, at_q, fp_q, gp_q, k0_q, k1_q, ra_q, s0_q, s1_q, s2_q, s3_q, s4_q, s5_q,
       s6_q, s7_q, sp_q, t0_q, t1_q, t2_q, t3_q, t4_q, t5_q, t6_q, t7_q, t8_q, t9_q, v0_q, v1_q;

  Decoder #(.select(5)) decoder_1 (
    .out1(decoder_1_out1), .out2(decoder_1_out2), .out3(decoder_1_out3), .out4(decoder_1_out4),
    .out5(decoder_1_out5), .out6(decoder_1_out6), .out7(decoder_1_out7), .out8(decoder_1_out8),
    .out9(decoder_1_out9), .out10(decoder_1_out10), .out11(decoder_1_out11), .out12(decoder_1_out12),
    .out13(decoder_1_out13), .out14(decoder_1_out14), .out15(decoder_1_out15), .out16(decoder_1_out16),
    .out17(decoder_1_out17), .out18(decoder_1_out18), .out19(decoder_1_out19), .out20(decoder_1_out20),
    .out21(decoder_1_out21), .out22(decoder_1_out22), .out23(decoder_1_out23), .out24(decoder_1_out24),
    .out25(decoder_1_out25), .out26(decoder_1_out26), .out27(decoder_1_out27), .out28(decoder_1_out28),
    .out29(decoder_1_out29), .out30(decoder_1_out30), .out31(decoder_1_out31), .sel(write_addr));  // open: out0, en
  and and_1 (and_1_out, decoder_1_out1, RegWrite);
  and and_2 (and_2_out, RegWrite, decoder_1_out2);
  and and_3 (and_3_out, RegWrite, decoder_1_out3);
  and and_4 (and_4_out, RegWrite, decoder_1_out4);
  and and_5 (and_5_out, RegWrite, decoder_1_out5);
  and and_6 (and_6_out, RegWrite, decoder_1_out6);
  and and_7 (and_7_out, RegWrite, decoder_1_out7);
  and and_8 (and_8_out, RegWrite, decoder_1_out8);
  and and_9 (and_9_out, RegWrite, decoder_1_out9);
  and and_10 (and_10_out, RegWrite, decoder_1_out10);
  and and_11 (and_11_out, RegWrite, decoder_1_out11);
  and and_12 (and_12_out, RegWrite, decoder_1_out12);
  and and_13 (and_13_out, RegWrite, decoder_1_out13);
  and and_14 (and_14_out, RegWrite, decoder_1_out14);
  and and_15 (and_15_out, RegWrite, decoder_1_out15);
  and and_16 (and_16_out, decoder_1_out16, RegWrite);
  and and_17 (and_17_out, decoder_1_out17, RegWrite);
  and and_18 (and_18_out, decoder_1_out18, RegWrite);
  and and_19 (and_19_out, decoder_1_out19, RegWrite);
  and and_20 (and_20_out, decoder_1_out20, RegWrite);
  and and_21 (and_21_out, decoder_1_out21, RegWrite);
  and and_22 (and_22_out, decoder_1_out22, RegWrite);
  and and_23 (and_23_out, decoder_1_out23, RegWrite);
  and and_24 (and_24_out, decoder_1_out24, RegWrite);
  and and_25 (and_25_out, decoder_1_out25, RegWrite);
  and and_26 (and_26_out, decoder_1_out26, RegWrite);
  and and_27 (and_27_out, decoder_1_out27, RegWrite);
  and and_28 (and_28_out, decoder_1_out28, RegWrite);
  and and_29 (and_29_out, decoder_1_out29, RegWrite);
  and and_30 (and_30_out, decoder_1_out30, RegWrite);
  and and_31 (and_31_out, decoder_1_out31, RegWrite);
  Register #(.width(32)) at (.D(write_value), .en(and_1_out), .Q(at_q), .clk(Clock), .clr(RegClear));
  Register #(.width(32)) v0 (.D(write_value), .en(and_2_out), .Q(v0_q), .clk(Clock), .clr(RegClear));
  Register #(.width(32)) v1 (.D(write_value), .en(and_3_out), .Q(v1_q), .clk(Clock), .clr(RegClear));
  Register #(.width(32)) a0 (.D(write_value), .en(and_4_out), .Q(a0_q), .clk(Clock), .clr(RegClear));
  Register #(.width(32)) a1 (.D(write_value), .en(and_5_out), .Q(a1_q), .clk(Clock), .clr(RegClear));
  Register #(.width(32)) a2 (.D(write_value), .en(and_6_out), .Q(a2_q), .clk(Clock), .clr(RegClear));
  Register #(.width(32)) a3 (.D(write_value), .en(and_7_out), .Q(a3_q), .clk(Clock), .clr(RegClear));
  Register #(.width(32)) t0 (.D(write_value), .en(and_8_out), .Q(t0_q), .clk(Clock), .clr(RegClear));
  Register #(.width(32)) t1 (.D(write_value), .en(and_9_out), .Q(t1_q), .clk(Clock), .clr(RegClear));
  Register #(.width(32)) t2 (.D(write_value), .en(and_10_out), .Q(t2_q), .clk(Clock), .clr(RegClear));
  Register #(.width(32)) t3 (.D(write_value), .en(and_11_out), .Q(t3_q), .clk(Clock), .clr(RegClear));
  Register #(.width(32)) t4 (.D(write_value), .en(and_12_out), .Q(t4_q), .clk(Clock), .clr(RegClear));
  Register #(.width(32)) t5 (.D(write_value), .en(and_13_out), .Q(t5_q), .clk(Clock), .clr(RegClear));
  Register #(.width(32)) t6 (.D(write_value), .en(and_14_out), .Q(t6_q), .clk(Clock), .clr(RegClear));
  Register #(.width(32)) t7 (.D(write_value), .en(and_15_out), .Q(t7_q), .clk(Clock), .clr(RegClear));
  Register #(.width(32)) s0 (.D(write_value), .en(and_16_out), .Q(s0_q), .clk(Clock), .clr(RegClear));
  Register #(.width(32)) s1 (.D(write_value), .en(and_17_out), .Q(s1_q), .clk(Clock), .clr(RegClear));
  Register #(.width(32)) s2 (.D(write_value), .en(and_18_out), .Q(s2_q), .clk(Clock), .clr(RegClear));
  Register #(.width(32)) s3 (.D(write_value), .en(and_19_out), .Q(s3_q), .clk(Clock), .clr(RegClear));
  Register #(.width(32)) s4 (.D(write_value), .en(and_20_out), .Q(s4_q), .clk(Clock), .clr(RegClear));
  Register #(.width(32)) s5 (.D(write_value), .en(and_21_out), .Q(s5_q), .clk(Clock), .clr(RegClear));
  Register #(.width(32)) s6 (.D(write_value), .en(and_22_out), .Q(s6_q), .clk(Clock), .clr(RegClear));
  Register #(.width(32)) s7 (.D(write_value), .en(and_23_out), .Q(s7_q), .clk(Clock), .clr(RegClear));
  Register #(.width(32)) t8 (.D(write_value), .en(and_24_out), .Q(t8_q), .clk(Clock), .clr(RegClear));
  Register #(.width(32)) t9 (.D(write_value), .en(and_25_out), .Q(t9_q), .clk(Clock), .clr(RegClear));
  Register #(.width(32)) k0 (.D(write_value), .en(and_26_out), .Q(k0_q), .clk(Clock), .clr(RegClear));
  Register #(.width(32)) k1 (.D(write_value), .en(and_27_out), .Q(k1_q), .clk(Clock), .clr(RegClear));
  Register #(.width(32)) gp (.D(write_value), .en(and_28_out), .Q(gp_q), .clk(Clock), .clr(RegClear));
  Register #(.width(32)) sp (.D(write_value), .en(and_29_out), .Q(sp_q), .clk(Clock), .clr(RegClear));
  Register #(.width(32)) fp (.D(write_value), .en(and_30_out), .Q(fp_q), .clk(Clock), .clr(RegClear));
  Register #(.width(32)) ra (.D(write_value), .en(and_31_out), .Q(ra_q), .clk(Clock), .clr(RegClear));
  Multiplexer #(.select(5), .width(32)) multiplexer_1 (
    .in0({32{1'b0}}), .in1(at_q), .in2(v0_q), .in3(v1_q), .in4(a0_q), .in5(a1_q), .in6(a2_q), .in7(a3_q),
    .in8(t0_q), .in9(t1_q), .in10(t2_q), .in11(t3_q), .in12(t4_q), .in13(t5_q), .in14(t6_q), .in15(t7_q),
    .in16(s0_q), .in17(s1_q), .in18(s2_q), .in19(s3_q), .in20(s4_q), .in21(s5_q), .in22(s6_q), .in23(s7_q),
    .in24(t8_q), .in25(t9_q), .in26(k0_q), .in27(k1_q), .in28(gp_q), .in29(sp_q), .in30(fp_q), .in31(ra_q),
    .out(Value_0), .sel(Read_0));  // open: en
  Multiplexer #(.select(5), .width(32)) multiplexer_2 (
    .in0({32{1'b0}}), .in1(at_q), .in2(v0_q), .in3(v1_q), .in4(a0_q), .in5(a1_q), .in6(a2_q), .in7(a3_q),
    .in8(t0_q), .in9(t1_q), .in10(t2_q), .in11(t3_q), .in12(t4_q), .in13(t5_q), .in14(t6_q), .in15(t7_q),
    .in16(s0_q), .in17(s1_q), .in18(s2_q), .in19(s3_q), .in20(s4_q), .in21(s5_q), .in22(s6_q), .in23(s7_q),
    .in24(t8_q), .in25(t9_q), .in26(k0_q), .in27(k1_q), .in28(gp_q), .in29(sp_q), .in30(fp_q), .in31(ra_q),
    .out(Value_1), .sel(Read_1));  // open: en
endmodule

module Instruction_Splitter (
  input  [31:0] in_1,
  output [5:0] Function,
  output [15:0] Constant_Address,
  output [4:0] Reg_read_rd,
  output [25:0] Address,
  output [4:0] Reg_read_rt,
  output [4:0] Reg_read_rs,
  output [5:0] Opcode
);


  assign Address = in_1[25:0];
  assign Constant_Address = in_1[15:0];
  assign Function = in_1[5:0];
  assign Opcode = in_1[31:26];
  assign Reg_read_rd = in_1[15:11];
  assign Reg_read_rs = in_1[25:21];
  assign Reg_read_rt = in_1[20:16];
endmodule

module ALU (
  input  [2:0] Function,
  input  [31:0] Input_B,
  input  [31:0] Input_A,
  output [31:0] out_4
);

  wire [31:0] adder_1_out, and_1_out, bit_extender_1_out, multiplexer_1_out, not_1_out, or_1_out;

  assign not_1_out = ~Input_B;  // NOT_Gate not_1, 32 bits wide
  Multiplexer #(.width(32), .enable("false")) multiplexer_1 (
    .in0(Input_B), .in1(not_1_out), .out(multiplexer_1_out), .sel(Function[2]));
  assign and_1_out = multiplexer_1_out & Input_A;  // AND_Gate and_1, 32 bits wide
  assign or_1_out = Input_A | multiplexer_1_out;  // OR_Gate or_1, 32 bits wide
  Adder #(.width(32)) adder_1 (.a(multiplexer_1_out), .b(Input_A), .out(adder_1_out), .cin(Function[2]));  // open: cout
  assign bit_extender_1_out = {{1{1'b0}}, adder_1_out[30:0]};  // Bit_Extender bit_extender_1
  Multiplexer #(.select(2), .width(32), .enable("false")) multiplexer_2 (
    .in0(and_1_out), .in1(or_1_out), .in2(adder_1_out), .in3(bit_extender_1_out), .out(out_4),
    .sel(Function[1:0]));
endmodule

module ALUcont (
  input  [5:0] in_1,
  output [2:0] out_2
);

  wire and_1_out, and_2_out, and_3_out, not_1_out, not_2_out, not_3_out, not_4_out;

  not not_1 (not_1_out, in_1[0]);
  not not_2 (not_2_out, in_1[3]);
  not not_3 (not_3_out, in_1[2]);
  not not_4 (not_4_out, in_1[1]);
  and and_1 (and_1_out, in_1[2], not_1_out);
  and and_2 (and_2_out, not_2_out, in_1[1]);
  and and_3 (and_3_out, not_3_out, not_4_out);
  or or_1 (out_2[2], and_1_out, in_1[3]);
  or or_2 (out_2[1], in_1[0], and_2_out);
  or or_3 (out_2[0], and_3_out, in_1[0], in_1[3]);
endmodule

module Datapath_ex (
  input  in_1,
  input  in_2,
  input  in_3,
  input  in_4,
  input  Clear_PC
);

  wire clock_1_out, undriven_2;
  wire [2:0] alucont_1_out_2;
  wire [4:0] instruction_splitter_1_reg_read_rd, instruction_splitter_1_reg_read_rs,
       instruction_splitter_1_reg_read_rt;
  wire [5:0] instruction_splitter_1_function, instruction_splitter_1_opcode;
  wire [15:0] instruction_splitter_1_constant_address;
  wire [23:0] shifter_1_out, shifter_2_out;
  wire [25:0] instruction_splitter_1_address;
  wire [31:0] adder_1_out, alu_1_out_4, bit_extender_1_out, multiplexer_1_out, multiplexer_2_out,
       multiplexer_3_out, ram_1_data, reg32_1_value_0, reg32_1_value_1, register_1_q, rom_1_data, undriven;

  Clock clock_1 (.out(clock_1_out));
  Register #(.width(32)) register_1 (.D(adder_1_out), .Q(register_1_q), .clk(clock_1_out), .clr(Clear_PC));  // open: en
  Shifter #(.width(24), .shift("lr")) shifter_1 (.in(register_1_q[23:0]), .\dist (5'b00010), .out(shifter_1_out));
  Adder #(.width(32)) adder_1 (.a(register_1_q), .b(32'h4), .out(adder_1_out));  // open: cin, cout
  ROM #(.addrWidth(24), .dataWidth(32)) rom_1 (.addr(shifter_1_out), .data(rom_1_data));  // open: sel
  Multiplexer #(.width(32), .enable("false")) multiplexer_1 (
    .in0(multiplexer_3_out), .in1(adder_1_out), .out(multiplexer_1_out), .sel(in_2));
  Instruction_Splitter instruction_splitter_1 (
    .in_1(rom_1_data), .Function(instruction_splitter_1_function),
    .Constant_Address(instruction_splitter_1_constant_address),
    .Reg_read_rd(instruction_splitter_1_reg_read_rd), .Address(instruction_splitter_1_address),
    .Reg_read_rt(instruction_splitter_1_reg_read_rt), .Reg_read_rs(instruction_splitter_1_reg_read_rs),
    .Opcode(instruction_splitter_1_opcode));
  assign bit_extender_1_out = {{16{instruction_splitter_1_constant_address[15]}}, instruction_splitter_1_constant_address};  // Bit_Extender bit_extender_1
  ALUcont alucont_1 (.in_1(instruction_splitter_1_function), .out_2(alucont_1_out_2));
  reg32 reg32_1 (
    .Read_0(instruction_splitter_1_reg_read_rs), .write_addr(instruction_splitter_1_reg_read_rt),
    .RegWrite(in_1), .Clock(clock_1_out), .write_value(multiplexer_1_out), .Value_0(reg32_1_value_0),
    .Value_1(reg32_1_value_1));  // open: Read_1, RegClear
  Multiplexer #(.width(32), .enable("false")) multiplexer_2 (
    .in0(reg32_1_value_1), .in1(bit_extender_1_out), .out(multiplexer_2_out), .sel(in_4));
  ALU alu_1 (.Function(alucont_1_out_2), .Input_B(reg32_1_value_0), .Input_A(multiplexer_2_out), .out_4(alu_1_out_4));
  Shifter #(.width(24), .shift("lr")) shifter_2 (.in(undriven[23:0]), .\dist (5'b00010), .out(shifter_2_out));
  RAM #(.addrWidth(24), .dataWidth(32), .bus("separate")) ram_1 (
    .addr(shifter_2_out), .din(reg32_1_value_1), .data(ram_1_data), .str(undriven_2), .clk(clock_1_out));  // open: sel, ld, clr
  Multiplexer #(.width(32), .enable("false")) multiplexer_3 (
    .in0(undriven), .in1(ram_1_data), .out(multiplexer_3_out), .sel(in_3));

  // Notes on the sheet:
  //   load word
  //   contents of rom_1 (hex, n*v repeats v):
  //   66666666 c0100014 2067fff7 e22025 642824 a42820 10a7000a 64202a 10800001 20050000 e2202a 853820
  //   e23822 ac670044 8c020050 8000011 20020001 ac020054 14*0 8
endmodule

module datapath_sw (
  input  [5:0] in_1,
  input  in_2,
  input  Clear_PC,
  output [31:0] out_4
);

  wire clock_1_out;
  wire [2:0] alucont_1_out_2;
  wire [4:0] instruction_splitter_1_reg_read_rs, instruction_splitter_1_reg_read_rt;
  wire [15:0] instruction_splitter_1_constant_address;
  wire [23:0] shifter_1_out, shifter_2_out;
  wire [31:0] adder_1_out, alu_1_out_4, bit_extender_1_out, reg32_1_value_0, reg32_1_value_1, register_1_q,
       rom_1_data;

  Clock clock_1 (.out(clock_1_out));
  Register #(.width(32)) register_1 (.D(adder_1_out), .Q(register_1_q), .clk(clock_1_out), .clr(Clear_PC));  // open: en
  Shifter #(.width(24), .shift("lr")) shifter_1 (.in(register_1_q[23:0]), .\dist (5'b00010), .out(shifter_1_out));
  Adder #(.width(32)) adder_1 (.a(register_1_q), .b(32'h4), .out(adder_1_out));  // open: cin, cout
  ROM #(.addrWidth(24), .dataWidth(32)) rom_1 (.addr(shifter_1_out), .data(rom_1_data));  // open: sel
  Instruction_Splitter instruction_splitter_1 (
    .in_1(rom_1_data), .Constant_Address(instruction_splitter_1_constant_address),
    .Reg_read_rt(instruction_splitter_1_reg_read_rt), .Reg_read_rs(instruction_splitter_1_reg_read_rs));  // open: Function, Reg_read_rd, Address, Opcode
  assign bit_extender_1_out = {{16{instruction_splitter_1_constant_address[15]}}, instruction_splitter_1_constant_address};  // Bit_Extender bit_extender_1
  ALUcont alucont_1 (.in_1(in_1), .out_2(alucont_1_out_2));
  reg32 reg32_1 (
    .Read_0(instruction_splitter_1_reg_read_rs), .Read_1(instruction_splitter_1_reg_read_rt),
    .RegWrite(in_2), .Clock(clock_1_out), .write_value(out_4), .Value_0(reg32_1_value_0),
    .Value_1(reg32_1_value_1));  // open: write_addr, RegClear
  ALU alu_1 (.Function(alucont_1_out_2), .Input_B(reg32_1_value_0), .Input_A(bit_extender_1_out), .out_4(alu_1_out_4));
  Shifter #(.width(24), .shift("lr")) shifter_2 (.in(alu_1_out_4[23:0]), .\dist (5'b00010), .out(shifter_2_out));
  RAM #(.addrWidth(24), .dataWidth(32), .bus("separate")) ram_1 (
    .addr(shifter_2_out), .din(reg32_1_value_1), .data(out_4), .clk(clock_1_out));  // open: str, sel, ld, clr

  // Notes on the sheet:
  //   contents of rom_1 (hex, n*v repeats v):
  //   8c020004 c0100014 2067fff7 e22025 642824 a42820 10a7000a 64202a 10800001 20050000 e2202a 853820
  //   e23822 ac670044 8c020050 8000011 20020001 ac020054
endmodule

module datapath_add (
  input  [5:0] in_1,
  input  in_2,
  input  Clear_PC,
  output [31:0] out_4
);

  wire clock_1_out;
  wire [2:0] alucont_1_out_2;
  wire [4:0] instruction_splitter_1_reg_read_rd, instruction_splitter_1_reg_read_rs,
       instruction_splitter_1_reg_read_rt;
  wire [23:0] shifter_1_out;
  wire [31:0] adder_1_out, reg32_1_value_0, reg32_1_value_1, register_1_q, rom_1_data;

  Clock clock_1 (.out(clock_1_out));
  Adder #(.width(32)) adder_1 (.a(32'h4), .b(register_1_q), .out(adder_1_out));  // open: cin, cout
  Register #(.width(32)) register_1 (.D(adder_1_out), .en(1'b1), .Q(register_1_q), .clk(clock_1_out), .clr(Clear_PC));
  Shifter #(.width(24), .shift("lr")) shifter_1 (.in(register_1_q[23:0]), .\dist (5'b00010), .out(shifter_1_out));
  ROM #(.addrWidth(24), .dataWidth(32)) rom_1 (.addr(shifter_1_out), .data(rom_1_data));  // open: sel
  Instruction_Splitter instruction_splitter_1 (
    .in_1(rom_1_data), .Reg_read_rd(instruction_splitter_1_reg_read_rd),
    .Reg_read_rt(instruction_splitter_1_reg_read_rt), .Reg_read_rs(instruction_splitter_1_reg_read_rs));  // open: Function, Constant_Address, Address, Opcode
  ALUcont alucont_1 (.in_1(in_1), .out_2(alucont_1_out_2));
  reg32 reg32_1 (
    .Read_0(instruction_splitter_1_reg_read_rs), .Read_1(instruction_splitter_1_reg_read_rt),
    .write_addr(instruction_splitter_1_reg_read_rd), .RegWrite(in_2), .Clock(clock_1_out),
    .write_value(out_4), .Value_0(reg32_1_value_0), .Value_1(reg32_1_value_1));  // open: RegClear
  ALU alu_1 (.Function(alucont_1_out_2), .Input_B(reg32_1_value_0), .Input_A(reg32_1_value_1), .out_4(out_4));

  // Notes on the sheet:
  //   000010 00010 00011 00100 00000 000000
  //   add $s0,$s1,$2
  //   contents of rom_1 (hex, n*v repeats v):
  //   8432000 c0100014 2067fff7 e22025 642824 a42820 10a7000a 64202a 10800001 20050000 e2202a 853820
  //   e23822 ac670044 8c020050 8000011 20020001 ac020054
endmodule

module datapath_addi (
  input  Regdest,
  input  ALUsrc,
  input  [2:0] ALUop,
  input  Clear_PC,
  output [31:0] out_5
);

  wire clock_1_out;
  wire [4:0] instruction_splitter_1_reg_read_rd, instruction_splitter_1_reg_read_rs,
       instruction_splitter_1_reg_read_rt, multiplexer_1_out;
  wire [15:0] instruction_splitter_1_constant_address;
  wire [23:0] shifter_1_out;
  wire [31:0] adder_1_out, bit_extender_1_out, multiplexer_2_out, reg32_1_value_0, reg32_1_value_1,
       register_1_q, rom_1_data;

  Clock clock_1 (.out(clock_1_out));
  Register #(.width(32)) register_1 (.D(adder_1_out), .Q(register_1_q), .clk(clock_1_out), .clr(Clear_PC));  // open: en
  Shifter #(.width(24), .shift("lr")) shifter_1 (.in(register_1_q[23:0]), .\dist (5'b00010), .out(shifter_1_out));
  Adder #(.width(32)) adder_1 (.a(register_1_q), .b(32'h4), .out(adder_1_out));  // open: cin, cout
  ROM #(.addrWidth(24), .dataWidth(32)) rom_1 (.addr(shifter_1_out), .data(rom_1_data));  // open: sel
  Instruction_Splitter instruction_splitter_1 (
    .in_1(rom_1_data), .Constant_Address(instruction_splitter_1_constant_address),
    .Reg_read_rd(instruction_splitter_1_reg_read_rd), .Reg_read_rt(instruction_splitter_1_reg_read_rt),
    .Reg_read_rs(instruction_splitter_1_reg_read_rs));  // open: Function, Address, Opcode
  Multiplexer #(.width(5), .enable("false")) multiplexer_1 (
    .in0(instruction_splitter_1_reg_read_rd), .in1(instruction_splitter_1_reg_read_rt),
    .out(multiplexer_1_out), .sel(Regdest));
  assign bit_extender_1_out = {{16{instruction_splitter_1_constant_address[15]}}, instruction_splitter_1_constant_address};  // Bit_Extender bit_extender_1
  reg32 reg32_1 (
    .Read_0(instruction_splitter_1_reg_read_rs), .Read_1(instruction_splitter_1_reg_read_rt),
    .write_addr(multiplexer_1_out), .Clock(clock_1_out), .write_value(out_5), .Value_0(reg32_1_value_0),
    .Value_1(reg32_1_value_1));  // open: RegWrite, RegClear
  Multiplexer #(.width(32), .enable("false")) multiplexer_2 (
    .in0(reg32_1_value_1), .in1(bit_extender_1_out), .out(multiplexer_2_out), .sel(ALUsrc));
  ALU alu_1 (.Function(ALUop), .Input_B(reg32_1_value_0), .Input_A(multiplexer_2_out), .out_4(out_5));

  // Notes on the sheet:
  //   contents of rom_1 (hex, n*v repeats v):
  //   8c020004 c0100014 2067fff7 e22025 642824 a42820 10a7000a 64202a 10800001 20050000 e2202a 853820
  //   e23822 ac670044 8c020050 8000011 20020001 ac020054
endmodule

module datapath_beq (
  input  Regdest,
  input  ALUsrc,
  input  [2:0] ALUop,
  input  Clear_PC,
  input  in_5,
  output [31:0] out_6
);

  wire clock_1_out;
  wire [4:0] instruction_splitter_1_reg_read_rd, instruction_splitter_1_reg_read_rs,
       instruction_splitter_1_reg_read_rt, multiplexer_1_out;
  wire [15:0] instruction_splitter_1_constant_address;
  wire [23:0] shifter_1_out, shifter_3_out;
  wire [31:0] adder_1_out, adder_2_out, alu_1_out_4, bit_extender_1_out, multiplexer_2_out,
       multiplexer_3_out, reg32_1_value_0, reg32_1_value_1, register_1_q, rom_1_data, shifter_2_out;

  Clock clock_1 (.out(clock_1_out));
  Register #(.width(32)) register_1 (.D(adder_1_out), .Q(register_1_q), .clk(clock_1_out), .clr(Clear_PC));  // open: en
  Shifter #(.width(24), .shift("lr")) shifter_1 (.in(register_1_q[23:0]), .\dist (5'b00010), .out(shifter_1_out));
  Adder #(.width(32)) adder_1 (.a(register_1_q), .b(32'h4), .out(adder_1_out));  // open: cin, cout
  ROM #(.addrWidth(24), .dataWidth(32)) rom_1 (.addr(shifter_1_out), .data(rom_1_data));  // open: sel
  Instruction_Splitter instruction_splitter_1 (
    .in_1(rom_1_data), .Constant_Address(instruction_splitter_1_constant_address),
    .Reg_read_rd(instruction_splitter_1_reg_read_rd), .Reg_read_rt(instruction_splitter_1_reg_read_rt),
    .Reg_read_rs(instruction_splitter_1_reg_read_rs));  // open: Function, Address, Opcode
  Multiplexer #(.width(5), .enable("false")) multiplexer_1 (
    .in0(instruction_splitter_1_reg_read_rd), .in1(instruction_splitter_1_reg_read_rt),
    .out(multiplexer_1_out), .sel(Regdest));
  assign bit_extender_1_out = {{16{instruction_splitter_1_constant_address[15]}}, instruction_splitter_1_constant_address};  // Bit_Extender bit_extender_1
  reg32 reg32_1 (
    .Read_0(instruction_splitter_1_reg_read_rs), .Read_1(instruction_splitter_1_reg_read_rt),
    .write_addr(multiplexer_1_out), .Clock(clock_1_out), .write_value(multiplexer_3_out),
    .Value_0(reg32_1_value_0), .Value_1(reg32_1_value_1));  // open: RegWrite, RegClear
  Adder #(.width(32)) adder_2 (.a(shifter_2_out), .b(adder_1_out), .out(adder_2_out));  // open: cin, cout
  Shifter #(.width(32)) shifter_2 (.in(bit_extender_1_out), .\dist (5'b00010), .out(shifter_2_out));
  Multiplexer #(.width(32), .enable("false")) multiplexer_2 (
    .in0(reg32_1_value_1), .in1(bit_extender_1_out), .out(multiplexer_2_out), .sel(ALUsrc));
  Multiplexer #(.width(32), .enable("false")) multiplexer_3 (
    .in0(alu_1_out_4), .in1(out_6), .out(multiplexer_3_out), .sel(in_5));
  ALU alu_1 (.Function(ALUop), .Input_B(reg32_1_value_0), .Input_A(multiplexer_2_out), .out_4(alu_1_out_4));
  Multiplexer #(.width(32), .enable("false")) multiplexer_4 (.in0(adder_2_out), .in1(adder_1_out));  // open: out, sel
  Shifter #(.width(24), .shift("lr")) shifter_3 (.in(alu_1_out_4[23:0]), .\dist (5'b00010), .out(shifter_3_out));
  RAM #(.addrWidth(24), .dataWidth(32), .bus("separate")) ram_1 (
    .addr(shifter_3_out), .din(reg32_1_value_1), .data(out_6));  // open: str, sel, clk, ld, clr

  // Notes on the sheet:
  //   contents of rom_1 (hex, n*v repeats v):
  //   8c020004 c0100014 2067fff7 e22025 642824 a42820 10a7000a 64202a 10800001 20050000 e2202a 853820
  //   e23822 ac670044 8c020050 8000011 20020001 ac020054
endmodule

module datapath_or (
  input  [5:0] in_1,
  input  in_2,
  input  Clear_PC,
  output [31:0] out_4
);

  wire clock_1_out;
  wire [2:0] alucont_1_out_2;
  wire [4:0] instruction_splitter_1_reg_read_rd, instruction_splitter_1_reg_read_rs,
       instruction_splitter_1_reg_read_rt;
  wire [23:0] shifter_1_out;
  wire [31:0] adder_1_out, reg32_1_value_0, reg32_1_value_1, register_1_q, rom_1_data;

  Clock clock_1 (.out(clock_1_out));
  Adder #(.width(32)) adder_1 (.a(32'h4), .b(register_1_q), .out(adder_1_out));  // open: cin, cout
  Register #(.width(32)) register_1 (.D(adder_1_out), .en(1'b1), .Q(register_1_q), .clk(clock_1_out), .clr(Clear_PC));
  Shifter #(.width(24), .shift("lr")) shifter_1 (.in(register_1_q[23:0]), .\dist (5'b00010), .out(shifter_1_out));
  ROM #(.addrWidth(24), .dataWidth(32)) rom_1 (.addr(shifter_1_out), .data(rom_1_data));  // open: sel
  Instruction_Splitter instruction_splitter_1 (
    .in_1(rom_1_data), .Reg_read_rd(instruction_splitter_1_reg_read_rd),
    .Reg_read_rt(instruction_splitter_1_reg_read_rt), .Reg_read_rs(instruction_splitter_1_reg_read_rs));  // open: Function, Constant_Address, Address, Opcode
  ALUcont alucont_1 (.in_1(in_1), .out_2(alucont_1_out_2));
  reg32 reg32_1 (
    .Read_0(instruction_splitter_1_reg_read_rs), .Read_1(instruction_splitter_1_reg_read_rt),
    .write_addr(instruction_splitter_1_reg_read_rd), .RegWrite(in_2), .Clock(clock_1_out),
    .write_value(out_4), .Value_0(reg32_1_value_0), .Value_1(reg32_1_value_1));  // open: RegClear
  ALU alu_1 (.Function(alucont_1_out_2), .Input_B(reg32_1_value_0), .Input_A(reg32_1_value_1), .out_4(out_4));

  // Notes on the sheet:
  //   000010 00010 00011 00100 00000 000000
  //   or $s0,$s1,$2
  //   contents of rom_1 (hex, n*v repeats v):
  //   8432000 c0100014 2067fff7 e22025 642824 a42820 10a7000a 64202a 10800001 20050000 e2202a 853820
  //   e23822 ac670044 8c020050 8000011 20020001 ac020054
endmodule

module datapath_and (
  input  [5:0] in_1,
  input  in_2,
  input  Clear_PC,
  output [31:0] out_4
);

  wire clock_1_out;
  wire [2:0] alucont_1_out_2;
  wire [4:0] instruction_splitter_1_reg_read_rd, instruction_splitter_1_reg_read_rs,
       instruction_splitter_1_reg_read_rt;
  wire [23:0] shifter_1_out;
  wire [31:0] adder_1_out, reg32_1_value_0, reg32_1_value_1, register_1_q, rom_1_data;

  Clock clock_1 (.out(clock_1_out));
  Adder #(.width(32)) adder_1 (.a(32'h4), .b(register_1_q), .out(adder_1_out));  // open: cin, cout
  Register #(.width(32)) register_1 (.D(adder_1_out), .en(1'b1), .Q(register_1_q), .clk(clock_1_out), .clr(Clear_PC));
  Shifter #(.width(24), .shift("lr")) shifter_1 (.in(register_1_q[23:0]), .\dist (5'b00010), .out(shifter_1_out));
  ROM #(.addrWidth(24), .dataWidth(32)) rom_1 (.addr(shifter_1_out), .data(rom_1_data));  // open: sel
  Instruction_Splitter instruction_splitter_1 (
    .in_1(rom_1_data), .Reg_read_rd(instruction_splitter_1_reg_read_rd),
    .Reg_read_rt(instruction_splitter_1_reg_read_rt), .Reg_read_rs(instruction_splitter_1_reg_read_rs));  // open: Function, Constant_Address, Address, Opcode
  ALUcont alucont_1 (.in_1(in_1), .out_2(alucont_1_out_2));
  reg32 reg32_1 (
    .Read_0(instruction_splitter_1_reg_read_rs), .Read_1(instruction_splitter_1_reg_read_rt),
    .write_addr(instruction_splitter_1_reg_read_rd), .RegWrite(in_2), .Clock(clock_1_out),
    .write_value(out_4), .Value_0(reg32_1_value_0), .Value_1(reg32_1_value_1));  // open: RegClear
  ALU alu_1 (.Function(alucont_1_out_2), .Input_B(reg32_1_value_0), .Input_A(reg32_1_value_1), .out_4(out_4));

  // Notes on the sheet:
  //   000010 00010 00011 00100 00000 000000
  //   and $s0,$s1,$2
  //   contents of rom_1 (hex, n*v repeats v):
  //   8432000 c0100014 2067fff7 e22025 642824 a42820 10a7000a 64202a 10800001 20050000 e2202a 853820
  //   e23822 ac670044 8c020050 8000011 20020001 ac020054
endmodule
