// Logisim project sampleDesign.circ as structural Verilog: 9 circuits, main circuit Mem-Reg-ALU
module Reg_ALU (
  input  [2:0] in_1,
  input  [2:0] in_2,
  input  [2:0] in_3,
  input  in_4,
  input  in_5,
  input  [15:0] in_6,
  output [15:0] out_7
);

  wire clock_1_out;
  wire [15:0] alu_addsub_1_result, multiplexer_1_out, registerfile_1_read_data_2;

  Clock clock_1 (.out(clock_1_out));
  Multiplexer #(.width(16)) multiplexer_1 (
    .in0(in_6), .in1(alu_addsub_1_result), .out(multiplexer_1_out), .sel(in_5));  // open: en
  RegisterFile registerfile_1 (
    .Write_Data(multiplexer_1_out), .Read_Data_1(out_7), .Read_Data_2(registerfile_1_read_data_2),
    .WriteRegister(in_3), .RegWrite(in_4), .Clock(clock_1_out), .Read_Register_1(in_1), .Read_Register_2(in_2));  // open: Reg_out_0, Reg_out_4, Reg_out_1, Reg_out_5, Reg_out_2, Reg_out_6, Reg_out_3, Reg_out_7, clr
  ALU_Addsub alu_addsub_1 (
    .A(out_7), .B(registerfile_1_read_data_2), .Result(alu_addsub_1_result));  // open: Overflow, Select
endmodule

module Mem_Reg_ALU (
  input  in_1,
  input  [9:0] in_2,
  input  in_3,
  input  in_4,
  input  [7:0] in_5,
  output [15:0] out_6,
  output [2:0] out_7,
  output [2:0] out_8,
  output [2:0] out_9,
  output [15:0] out_10
);

  wire addsub, button_1_out;
  wire [9:0] adder_1_out, register_1_q;
  wire [15:0] alu_addsub_1_result, multiplexer_1_out, registerfile_1_reg_out_0, registerfile_1_reg_out_1,
       registerfile_1_reg_out_2, registerfile_1_reg_out_3, registerfile_1_reg_out_4,
       registerfile_1_reg_out_5, registerfile_1_reg_out_6, registerfile_1_reg_out_7;
  wire [22:0] rom_1_data;

  Button button_1 (.out(button_1_out));
  Register #(.width(10)) register_1 (.D(adder_1_out), .Q(register_1_q), .clk(button_1_out), .clr(in_4));  // open: en
  Adder #(.width(10)) adder_1 (.a(in_2), .b(register_1_q), .out(adder_1_out));  // open: cin, cout
  ROM #(.addrWidth(10), .dataWidth(32)) rom_1 (
    .addr(register_1_q), .data({out_7, out_8, out_9, rom_1_data[22], addsub, rom_1_data[20:0]}));  // open: sel
  // Probe on registerfile_1_reg_out_7
  // Probe on registerfile_1_reg_out_3
  // Probe on registerfile_1_reg_out_6
  // Probe on registerfile_1_reg_out_2
  // Probe on registerfile_1_reg_out_5
  // Probe on registerfile_1_reg_out_1
  // Probe on registerfile_1_reg_out_4
  // Probe on registerfile_1_reg_out_0
  RegisterFile registerfile_1 (
    .Write_Data(multiplexer_1_out), .Read_Data_1(out_6), .Read_Data_2(out_10),
    .Reg_out_0(registerfile_1_reg_out_0), .Reg_out_4(registerfile_1_reg_out_4),
    .Reg_out_1(registerfile_1_reg_out_1), .Reg_out_5(registerfile_1_reg_out_5),
    .Reg_out_2(registerfile_1_reg_out_2), .Reg_out_6(registerfile_1_reg_out_6),
    .Reg_out_3(registerfile_1_reg_out_3), .Reg_out_7(registerfile_1_reg_out_7), .WriteRegister(out_9),
    .RegWrite(rom_1_data[22]), .Clock(button_1_out), .clr(in_1), .Read_Register_1(out_7),
    .Read_Register_2(out_8));
  Multiplexer #(.width(16)) multiplexer_1 (
    .in0(rom_1_data[15:0]), .in1(alu_addsub_1_result), .out(multiplexer_1_out), .sel(rom_1_data[20]));  // open: en
  ALU_Addsub alu_addsub_1 (.A(out_6), .B(out_10), .Result(alu_addsub_1_result), .Select(addsub));  // open: Overflow
  RAM #(.dataWidth(16)) ram_1 (
    .addr(in_5), .data(alu_addsub_1_result), .clk(button_1_out), .ld(in_3));  // open: sel, clr

  // Notes on the sheet:
  //   contents of rom_1 (hex, n*v repeats v):
  //   400000 c00001 1400002 1c00003 2400004 2c00005 3400006 3c00007 4500000 8500000 8500000 10500000
  //   14500000 18500000 1c500000
  //   MuxCtrl
  //   data
endmodule

module RegisterFile (
  input  [2:0] Read_Register_1,
  input  [2:0] WriteRegister,
  input  [15:0] Write_Data,
  input  [2:0] Read_Register_2,
  input  RegWrite,
  input  Clock,
  input  clr,
  output [15:0] Reg_out_0,
  output [15:0] Reg_out_1,
  output [15:0] Reg_out_2,
  output [15:0] Reg_out_3,
  output [15:0] Reg_out_4,
  output [15:0] Reg_out_5,
  output [15:0] Reg_out_6,
  output [15:0] Reg_out_7,
  output [15:0] Read_Data_1,
  output [15:0] Read_Data_2
);

  wire and_1_out, and_2_out, and_3_out, and_4_out, and_5_out, and_6_out, and_7_out, and_8_out,
       decoder_1_out0, decoder_1_out1, decoder_1_out2, decoder_1_out3, decoder_1_out4, decoder_1_out5,
       decoder_1_out6, decoder_1_out7;

  Decoder #(.select(3)) decoder_1 (
    .out0(decoder_1_out0), .out1(decoder_1_out1), .out2(decoder_1_out2), .out3(decoder_1_out3),
    .out4(decoder_1_out4), .out5(decoder_1_out5), .out6(decoder_1_out6), .out7(decoder_1_out7),
    .sel(WriteRegister), .en(1'b1));
  and and_1 (and_1_out, decoder_1_out0, RegWrite);
  and and_2 (and_2_out, decoder_1_out1, RegWrite);
  and and_3 (and_3_out, decoder_1_out2, RegWrite);
  and and_4 (and_4_out, decoder_1_out3, RegWrite);
  and and_5 (and_5_out, decoder_1_out4, RegWrite);
  and and_6 (and_6_out, decoder_1_out5, RegWrite);
  and and_7 (and_7_out, decoder_1_out6, RegWrite);
  and and_8 (and_8_out, decoder_1_out7, RegWrite);
  Register #(.width(16)) register_1 (.D(Write_Data), .en(and_1_out), .Q(Reg_out_0), .clk(Clock), .clr(clr));
  Register #(.width(16)) register_2 (.D(Write_Data), .en(and_2_out), .Q(Reg_out_1), .clk(Clock), .clr(clr));
  Register #(.width(16)) register_3 (.D(Write_Data), .en(and_3_out), .Q(Reg_out_2), .clk(Clock), .clr(clr));
  Register #(.width(16)) register_4 (.D(Write_Data), .en(and_4_out), .Q(Reg_out_3), .clk(Clock), .clr(clr));
  Register #(.width(16)) register_5 (.D(Write_Data), .en(and_5_out), .Q(Reg_out_4), .clk(Clock), .clr(clr));
  Register #(.width(16)) register_6 (.D(Write_Data), .en(and_6_out), .Q(Reg_out_5), .clk(Clock), .clr(clr));
  Register #(.width(16)) register_7 (.D(Write_Data), .en(and_7_out), .Q(Reg_out_6), .clk(Clock), .clr(clr));
  Register #(.width(16)) register_8 (.D(Write_Data), .en(and_8_out), .Q(Reg_out_7), .clk(Clock), .clr(clr));
  Multiplexer #(.select(3), .width(16)) multiplexer_1 (
    .in0(Reg_out_0), .in1(Reg_out_1), .in2(Reg_out_2), .in3(Reg_out_3), .in4(Reg_out_4), .in5(Reg_out_5),
    .in6(Reg_out_6), .in7(Reg_out_7), .out(Read_Data_1), .sel(Read_Register_1), .en(1'b1));
  Multiplexer #(.select(3), .width(16)) multiplexer_2 (
    .in0(Reg_out_0), .in1(Reg_out_1), .in2(Reg_out_2), .in3(Reg_out_3), .in4(Reg_out_4), .in5(Reg_out_5),
    .in6(Reg_out_6), .in7(Reg_out_7), .out(Read_Data_2), .sel(Read_Register_2), .en(1'b1));

  // Notes on the sheet:
  //   Write Bus
  //   R0
  //   R1
  //   R2
  //   R3
  //   R4
  //   R5
  //   R6
  //   R7
  //   Read Bus B
  //   Read Bus A
endmodule

module ALU_Addsub (
  input  [15:0] A,
  input  [15:0] B,
  input  Select,
  output [15:0] Result,
  output Overflow
);

  wire adder_1_cout, subtractor_1_bout;
  wire [15:0] adder_1_out, subtractor_1_out;

  Adder #(.width(16)) adder_1 (.a(A), .b(B), .out(adder_1_out), .cout(adder_1_cout));  // open: cin
  Subtractor #(.width(16)) subtractor_1 (.a(A), .b(B), .out(subtractor_1_out), .bout(subtractor_1_bout));  // open: bin
  Multiplexer #(.width(16), .enable("false")) multiplexer_1 (
    .in0(adder_1_out), .in1(subtractor_1_out), .out(Result), .sel(Select));
  Multiplexer #(.enable("false")) multiplexer_2 (
    .in0(adder_1_cout), .in1(subtractor_1_bout), .out(Overflow), .sel(Select));
endmodule

module AUL_reg_mem (
  input  in_1,
  input  [9:0] in_2,
  input  in_3,
  output [15:0] out_4,
  output [2:0] out_5,
  output [2:0] out_6,
  output [2:0] out_7,
  output [15:0] out_8
);

  wire addsub, button_1_out;
  wire [9:0] adder_1_out, register_1_q;
  wire [15:0] alu_addsub_1_result, multiplexer_1_out, registerfile_1_reg_out_0, registerfile_1_reg_out_1,
       registerfile_1_reg_out_4;
  wire [22:0] rom_1_data;

  Button button_1 (.out(button_1_out));
  Register #(.width(10)) register_1 (.D(adder_1_out), .Q(register_1_q), .clk(button_1_out), .clr(in_3));  // open: en
  Adder #(.width(10)) adder_1 (.a(in_2), .b(register_1_q), .out(adder_1_out));  // open: cin, cout
  ROM #(.addrWidth(10), .dataWidth(32)) rom_1 (
    .addr(register_1_q), .data({out_5, out_6, out_7, rom_1_data[22], addsub, rom_1_data[20:0]}));  // open: sel
  // Probe on registerfile_1_reg_out_1
  // Probe on registerfile_1_reg_out_4
  // Probe on registerfile_1_reg_out_0
  RegisterFile registerfile_1 (
    .Write_Data(multiplexer_1_out), .Read_Data_1(out_4), .Read_Data_2(out_8),
    .Reg_out_0(registerfile_1_reg_out_0), .Reg_out_4(registerfile_1_reg_out_4),
    .Reg_out_1(registerfile_1_reg_out_1), .WriteRegister(out_7), .RegWrite(rom_1_data[22]),
    .Clock(button_1_out), .clr(in_1), .Read_Register_1(out_5), .Read_Register_2(out_6));  // open: Reg_out_5, Reg_out_2, Reg_out_6, Reg_out_3, Reg_out_7
  Multiplexer #(.width(16)) multiplexer_1 (
    .in0(rom_1_data[15:0]), .in1(alu_addsub_1_result), .out(multiplexer_1_out), .sel(rom_1_data[20]));  // open: en
  ALU_Addsub alu_addsub_1 (.A(out_4), .B(out_8), .Result(alu_addsub_1_result), .Select(addsub));  // open: Overflow

  // Notes on the sheet:
  //   contents of rom_1 (hex, n*v repeats v):
  //   400000 c00001 1400002 1c00003 2400004 2c00005 3400006 3c00007 4500000 8500000 8500000 10500000
  //   14500000 18500000 1c500000
  //   MuxCtrl
  //   data
endmodule

module Two_10_FSM (
  input  in_1,
  input  in_2,
  output out_3
);

  wire and_1_out, button_1_out, d_ff_1_q, not_1_out;

  Button button_1 (.out(button_1_out));
  not not_1 (not_1_out, in_1);
  D_Flip_Flop d_ff_1 (.clk(button_1_out), .D(in_1), .Q(d_ff_1_q), .preset(in_2));  // open: Qn, en, reset
  and and_1 (and_1_out, not_1_out, d_ff_1_q);
  D_Flip_Flop d_ff_2 (.clk(button_1_out), .D(and_1_out), .Q(out_3), .preset(in_2));  // open: Qn, en, reset
endmodule

module FSM_10_sameState (
  input  in_1,
  input  in_2,
  output out_3
);

  wire and_1_out, button_1_out, d_ff_1_q, not_1_out, or_1_out;

  not not_1 (not_1_out, in_1);
  Button button_1 (.out(button_1_out));
  or or_1 (or_1_out, out_3, d_ff_1_q);
  D_Flip_Flop d_ff_1 (.clk(button_1_out), .D(in_1), .Q(d_ff_1_q), .preset(in_2));  // open: Qn, en, reset
  and and_1 (and_1_out, or_1_out, not_1_out);
  D_Flip_Flop d_ff_2 (.clk(button_1_out), .D(and_1_out), .Q(out_3), .preset(in_2));  // open: Qn, en, reset
endmodule

module cnt_2bit (
  input  cnt,
  output out_2,
  output out_3
);

  wire and_1_out, and_2_out, and_3_out, button_1_out, d_ff_1_qn, d_ff_2_qn, not_1_out, or_1_out, xor_1_out;

  not not_1 (not_1_out, cnt);
  and and_1 (and_1_out, d_ff_2_qn, cnt, out_2);
  and and_2 (and_2_out, not_1_out, out_3);
  and and_3 (and_3_out, out_3, d_ff_1_qn);
  xor xor_1 (xor_1_out, out_2, cnt);
  or or_1 (or_1_out, and_1_out, and_2_out, and_3_out);
  Button button_1 (.out(button_1_out));
  D_Flip_Flop d_ff_1 (.clk(button_1_out), .D(xor_1_out), .Q(out_2), .Qn(d_ff_1_qn));  // open: preset, en, reset
  D_Flip_Flop d_ff_2 (.clk(button_1_out), .D(or_1_out), .Q(out_3), .Qn(d_ff_2_qn));  // open: preset, en, reset
endmodule

module Tb_ALU_Reg (
  input  in_1,
  input  [9:0] in_2,
  input  in_3
);

  wire addsub, button_1_out;
  wire [9:0] adder_1_out, register_1_q;
  wire [15:0] alu_addsub_1_result, multiplexer_1_out, registerfile_1_read_data_1, registerfile_1_read_data_2,
       registerfile_1_reg_out_0, registerfile_1_reg_out_1, registerfile_1_reg_out_2,
       registerfile_1_reg_out_3, registerfile_1_reg_out_4, registerfile_1_reg_out_5,
       registerfile_1_reg_out_6, registerfile_1_reg_out_7;
  wire [31:0] rom_1_data;

  Button button_1 (.out(button_1_out));
  Register #(.width(10)) register_1 (.D(adder_1_out), .Q(register_1_q), .clk(button_1_out), .clr(in_3));  // open: en
  Adder #(.width(10)) adder_1 (.a(in_2), .b(register_1_q), .out(adder_1_out));  // open: cin, cout
  ROM #(.addrWidth(10), .dataWidth(32)) rom_1 (
    .addr(register_1_q), .data({rom_1_data[31:22], addsub, rom_1_data[20:0]}));  // open: sel
  // Probe on registerfile_1_reg_out_7
  // Probe on registerfile_1_reg_out_3
  // Probe on registerfile_1_reg_out_6
  // Probe on registerfile_1_reg_out_2
  // Probe on registerfile_1_reg_out_5
  // Probe on registerfile_1_reg_out_1
  // Probe on registerfile_1_reg_out_4
  // Probe on registerfile_1_reg_out_0
  RegisterFile registerfile_1 (
    .Write_Data(multiplexer_1_out), .Read_Data_1(registerfile_1_read_data_1),
    .Read_Data_2(registerfile_1_read_data_2), .Reg_out_0(registerfile_1_reg_out_0),
    .Reg_out_4(registerfile_1_reg_out_4), .Reg_out_1(registerfile_1_reg_out_1),
    .Reg_out_5(registerfile_1_reg_out_5), .Reg_out_2(registerfile_1_reg_out_2),
    .Reg_out_6(registerfile_1_reg_out_6), .Reg_out_3(registerfile_1_reg_out_3),
    .Reg_out_7(registerfile_1_reg_out_7), .WriteRegister(rom_1_data[25:23]), .RegWrite(rom_1_data[22]),
    .Clock(button_1_out), .clr(in_1), .Read_Register_1(rom_1_data[31:29]), .Read_Register_2(rom_1_data[28:26]));
  Multiplexer #(.width(16)) multiplexer_1 (
    .in0(rom_1_data[15:0]), .in1(alu_addsub_1_result), .out(multiplexer_1_out), .sel(rom_1_data[20]));  // open: en
  ALU_Addsub alu_addsub_1 (
    .A(registerfile_1_read_data_1), .B(registerfile_1_read_data_2), .Result(alu_addsub_1_result),
    .Select(addsub));  // open: Overflow

  // Notes on the sheet:
  //   contents of rom_1 (hex, n*v repeats v):
  //   400000 c00001 1400002 1c00003 2400004 2c00005 3400006 3c00007 4500000 8500000 8500000 10500000
  //   14500000 18500000 1c500000
  //   MuxCtrl
  //   data
endmodule
