// Logisim project 2402cs11_Lab7.circ as structural Verilog: 8 circuits, main circuit single-cycle datapath
module Control_Unit (
  input  [5:0] Opcode,
  input  [5:0] Funct,
  output RegDst,
  output ALU_Src,
  output RegWrite,
  output MemRead,
  output MemWrite,
  output MemToReg,
  output Branch
);

  wire comparator_1_eq, comparator_4_eq;

  Comparator #(.width(6)) comparator_1 (.a({6{1'b0}}), .b(Opcode), .eq(comparator_1_eq));  // open: gt, lt
  Multiplexer multiplexer_1 (.in0(1'b0), .in1(1'b1), .out(RegDst), .sel(comparator_1_eq));  // open: en
  Comparator #(.width(6)) comparator_2 (.a(6'b101011), .b(Opcode), .eq(MemWrite));  // open: gt, lt
  Comparator #(.width(6)) comparator_3 (.a(6'b100011), .b(Opcode), .eq(MemRead));  // open: gt, lt
  Comparator #(.width(6)) comparator_4 (.a(6'b001000), .b(Opcode), .eq(comparator_4_eq));  // open: gt, lt
  Comparator #(.width(6)) comparator_5 (.a(6'b000100), .b(Opcode), .eq(Branch));  // open: gt, lt
  or or_1 (ALU_Src, MemWrite, MemRead, comparator_4_eq);
  or or_2 (RegWrite, comparator_1_eq, comparator_4_eq, MemRead);

  assign MemToReg = MemRead;

  // Notes on the sheet:
  //   sw
  //   lw
  //   addi
  //   beq
  //   for lw
  //   regdst set to 1 for R-type
  //   ALU src 1 for I-type mostly
  //   either R-type, lw OR addi
  //   only for lw
  //   only for sw
  //   only for beq
endmodule

module single_cycle_datapath (
  input  in_1,
  input  in_2,
  input  [23:0] in_3
);

  wire and_1_out, clock_1_out, control_unit_final_1_jr, control_unit_final_1_out_4,
       control_unit_final_1_out_5, control_unit_final_1_out_6, control_unit_final_1_out_8,
       control_unit_final_1_out_9, control_unit_final_1_out_10, control_unit_final_1_out_11, Link,
       n32bit_alu_1_iszero;
  wire [2:0] control_unit_final_1_alucontrol;
  wire [4:0] instruction_splitter_1_rd, instruction_splitter_1_rs, instruction_splitter_1_rt,
       multiplexer_4_out, multiplexer_5_out;
  wire [5:0] instruction_splitter_1_func, instruction_splitter_1_opcode;
  wire [15:0] instruction_splitter_1_out_3;
  wire [23:0] shifter_1_out;
  wire [25:0] instruction_splitter_1_out_4;
  wire [31:0] adder_1_out, adder_2_out, bit_extender_1_out, jump_address_maker_1_out_3, multiplexer_1_out,
       multiplexer_2_out, multiplexer_3_out, multiplexer_6_out, multiplexer_7_out, multiplexer_8_out,
       n32bit_alu_1_out_5, n32x32register_1_out_8, n32x32register_1_out_9, ram_1_data, register_1_q,
       rom_1_data, shifter_2_out;

  Multiplexer #(.width(32)) multiplexer_1 (
    .in0(multiplexer_3_out), .in1(jump_address_maker_1_out_3), .out(multiplexer_1_out),
    .sel(control_unit_final_1_out_11));  // open: en
  Multiplexer #(.width(32)) multiplexer_2 (
    .in0(multiplexer_1_out), .in1(n32x32register_1_out_8), .out(multiplexer_2_out),
    .sel(control_unit_final_1_jr));  // open: en
  Multiplexer #(.width(32)) multiplexer_3 (
    .in0(adder_1_out), .in1(adder_2_out), .out(multiplexer_3_out), .sel(and_1_out));  // open: en
  Register #(.width(32)) register_1 (
    .D(multiplexer_2_out), .Q(register_1_q), .clk(clock_1_out), .clr(in_1));  // open: en
  Clock clock_1 (.out(clock_1_out));
  Shifter #(.width(24), .shift("lr")) shifter_1 (.in(register_1_q[23:0]), .\dist (5'b00010), .out(shifter_1_out));
  Adder #(.width(32)) adder_1 (.a(register_1_q), .b(32'h4), .out(adder_1_out));  // open: cin, cout
  Adder #(.width(32)) adder_2 (.a(shifter_2_out), .b(adder_1_out), .out(adder_2_out));  // open: cin, cout
  Jump_Address_Maker jump_address_maker_1 (
    .in_1(instruction_splitter_1_out_4), .in_2(adder_1_out), .out_3(jump_address_maker_1_out_3));
  ROM #(.addrWidth(24), .dataWidth(32)) rom_1 (.addr(shifter_1_out), .data(rom_1_data));  // open: sel
  and and_1 (and_1_out, n32bit_alu_1_iszero, control_unit_final_1_out_10);
  Instruction_Splitter instruction_splitter_1 (
    .in_1(rom_1_data), .Func(instruction_splitter_1_func), .out_3(instruction_splitter_1_out_3),
    .out_4(instruction_splitter_1_out_4), .rd(instruction_splitter_1_rd), .rt(instruction_splitter_1_rt),
    .rs(instruction_splitter_1_rs), .opCode(instruction_splitter_1_opcode));
  Shifter #(.width(32)) shifter_2 (.in(bit_extender_1_out), .\dist (5'b00010), .out(shifter_2_out));
  Control_Unit_Final control_unit_final_1 (
    .Opcode(instruction_splitter_1_opcode), .Func(instruction_splitter_1_func),
    .out_4(control_unit_final_1_out_4), .out_5(control_unit_final_1_out_5),
    .out_6(control_unit_final_1_out_6), .out_8(control_unit_final_1_out_8),
    .out_9(control_unit_final_1_out_9), .out_10(control_unit_final_1_out_10),
    .out_11(control_unit_final_1_out_11), .ALUControl(control_unit_final_1_alucontrol), .out_3(Link),
    .jr(control_unit_final_1_jr));  // open: out_7
  Multiplexer #(.width(5)) multiplexer_4 (
    .in0(instruction_splitter_1_rt), .in1(instruction_splitter_1_rd), .out(multiplexer_4_out),
    .sel(control_unit_final_1_out_4));  // open: en
  Multiplexer #(.width(5)) multiplexer_5 (
    .in0(multiplexer_4_out), .in1({5{1'b1}}), .out(multiplexer_5_out), .sel(Link));  // open: en
  assign bit_extender_1_out = {{16{instruction_splitter_1_out_3[15]}}, instruction_splitter_1_out_3};  // Bit_Extender bit_extender_1
  _32x32Register u_32x32register_1 (
    .Read_B(instruction_splitter_1_rt), .Read_A(instruction_splitter_1_rs),
    .in_3(control_unit_final_1_out_6), .out_8(n32x32register_1_out_8), .out_9(n32x32register_1_out_9),
    .in_7(multiplexer_8_out), .in_6(clock_1_out), .in_5(in_2), .Selection(multiplexer_5_out));
  Multiplexer #(.width(32)) multiplexer_6 (
    .in0(n32x32register_1_out_9), .in1(bit_extender_1_out), .out(multiplexer_6_out),
    .sel(control_unit_final_1_out_5));  // open: en
  _32bit_ALU u_32bit_alu_1 (
    .in_1(n32x32register_1_out_8), .in_2(multiplexer_6_out), .out_5(n32bit_alu_1_out_5),
    .OpCode(control_unit_final_1_alucontrol), .isZero(n32bit_alu_1_iszero));
  RAM #(.addrWidth(24), .dataWidth(32), .bus("separate")) ram_1 (
    .addr(n32bit_alu_1_out_5[23:0]), .din(n32x32register_1_out_9), .data(ram_1_data),
    .str(control_unit_final_1_out_8), .clk(clock_1_out), .clr(in_2));  // open: sel, ld
  Multiplexer #(.width(32)) multiplexer_7 (
    .in0(n32bit_alu_1_out_5), .in1(ram_1_data), .out(multiplexer_7_out), .sel(control_unit_final_1_out_9));  // open: en
  Multiplexer #(.width(32)) multiplexer_8 (
    .in0(multiplexer_7_out), .in1(adder_1_out), .out(multiplexer_8_out), .sel(Link));  // open: en

  // Notes on the sheet:
  //   j
  //   jr
  //   beq
  //   This line shows if branching will happen or not
  //   contents of rom_1 (hex, n*v repeats v):
  //   2008000a 20090000 11000003 1284820 2108ffff 8100002 ac090004
  //   Custom instruction box
endmodule

module Main_Decoder (
  input  [5:0] Opcode,
  output RegDst,
  output ALUsrc,
  output RegWrite,
  output MemRead,
  output MemWrite,
  output MemtoReg,
  output Branch,
  output ALUop1,
  output ALUop0,
  output Jump,
  output Link
);

  wire and_2_out, and_3_out, not_1_out, not_2_out, not_3_out, not_4_out, not_5_out, not_6_out, not_7_out,
       not_8_out, not_9_out, not_10_out, not_11_out, not_12_out;

  not not_1 (not_1_out, Opcode[3]);
  not not_2 (not_2_out, Opcode[2]);
  not not_3 (not_3_out, Opcode[1]);
  not not_4 (not_4_out, Opcode[2]);
  not not_5 (not_5_out, Opcode[1]);
  not not_6 (not_6_out, Opcode[3]);
  not not_7 (not_7_out, Opcode[3]);
  not not_8 (not_8_out, Opcode[3]);
  not not_9 (not_9_out, Opcode[3]);
  not not_10 (not_10_out, Opcode[2]);
  not not_11 (not_11_out, Opcode[1]);
  not not_12 (not_12_out, Opcode[0]);
  and and_1 (RegDst, not_1_out, not_2_out, not_3_out);
  or or_1 (ALUsrc, Opcode[3], Opcode[5]);
  and and_2 (and_2_out, not_4_out, not_5_out);
  and and_3 (and_3_out, Opcode[5], not_6_out);
  and and_4 (MemRead, Opcode[5], not_7_out);
  and and_5 (MemWrite, Opcode[5], Opcode[3]);
  and and_6 (MemtoReg, Opcode[5], not_8_out);
  and and_7 (ALUop1, not_9_out, not_10_out, not_11_out);
  and and_8 (Jump, Opcode[1], not_12_out);
  Comparator #(.width(6)) comparator_1 (.a(Opcode), .b(6'b000011), .eq(Link));  // open: gt, lt
  or or_2 (RegWrite, and_2_out, and_3_out);

  assign ALUop0 = Opcode[2];
  assign Branch = Opcode[2];
endmodule

module Control_Unit_Final (
  input  [5:0] Opcode,
  input  [5:0] Func,
  output out_3,
  output out_4,
  output out_5,
  output out_6,
  output out_7,
  output out_8,
  output out_9,
  output out_10,
  output out_11,
  output jr,
  output [2:0] ALUControl
);

  wire and_2_out, and_3_out, and_4_out, comparator_1_eq, comparator_2_eq, main_decoder_1_aluop0,
       main_decoder_1_aluop1, main_decoder_1_jump, not_1_out, not_2_out;

  and and_1 (jr, comparator_1_eq, comparator_2_eq);
  Comparator #(.width(6)) comparator_1 (.a(Opcode), .b({6{1'b0}}), .eq(comparator_1_eq));  // open: gt, lt
  Comparator #(.width(6)) comparator_2 (.a(6'b001000), .b(Func), .eq(comparator_2_eq));  // open: gt, lt
  Main_Decoder main_decoder_1 (
    .Opcode(Opcode), .RegDst(out_4), .ALUsrc(out_5), .RegWrite(out_6), .MemRead(out_7), .MemWrite(out_8),
    .MemtoReg(out_9), .Branch(out_10), .ALUop1(main_decoder_1_aluop1), .ALUop0(main_decoder_1_aluop0),
    .Jump(main_decoder_1_jump), .Link(out_3));
  and and_2 (and_2_out, main_decoder_1_aluop1, Func[1]);
  not not_1 (not_1_out, main_decoder_1_aluop1);
  not not_2 (not_2_out, Func[2]);
  and and_3 (and_3_out, main_decoder_1_aluop1, Func[0]);
  and and_4 (and_4_out, main_decoder_1_aluop1, Func[3]);
  or or_1 (ALUControl[2], main_decoder_1_aluop0, and_2_out);
  or or_2 (ALUControl[1], not_1_out, not_2_out);
  or or_3 (ALUControl[0], and_3_out, and_4_out);
  or or_4 (out_11, out_3, main_decoder_1_jump);
endmodule

module Jump_Address_Maker (
  input  [25:0] in_1,
  input  [31:0] in_2,
  output [31:0] out_3
);

  wire [27:0] bit_extender_1_out, shifter_1_out;

  assign bit_extender_1_out = {{2{1'b0}}, in_1};  // Bit_Extender bit_extender_1
  Shifter #(.width(28)) shifter_1 (.in(bit_extender_1_out), .\dist (5'b00010), .out(shifter_1_out));
  Subtractor #(.width(32)) subtractor_1 (
    .a({in_2[31:28], shifter_1_out}), .b(32'h400000), .out(out_3));  // open: bin, bout

  // Notes on the sheet:
  //   Jump
  //   Base
endmodule

module single_cycle_ultimate (
  input  clr
);

  wire and_1_out, button_1_out, jal, main_decoder_ultimate_1_alusrc, main_decoder_ultimate_1_branch,
       main_decoder_ultimate_1_jr, main_decoder_ultimate_1_jump, main_decoder_ultimate_1_memtoreg,
       main_decoder_ultimate_1_memwrite, main_decoder_ultimate_1_regdst, main_decoder_ultimate_1_regwrite,
       n32bit_alu_1_iszero, or_1_out;
  wire [2:0] main_decoder_ultimate_1_alu_control;
  wire [4:0] instruction_splitter_1_rd, instruction_splitter_1_rs, instruction_splitter_1_rt,
       multiplexer_4_out, multiplexer_5_out;
  wire [5:0] instruction_splitter_1_func, instruction_splitter_1_opcode;
  wire [15:0] instruction_splitter_1_out_3;
  wire [23:0] shifter_1_out;
  wire [25:0] instruction_splitter_1_out_4;
  wire [31:0] adder_1_out, adder_2_out, bit_extender_1_out, jump_address_maker_1_out_3, multiplexer_1_out,
       multiplexer_2_out, multiplexer_3_out, multiplexer_6_out, multiplexer_7_out, multiplexer_8_out,
       n32bit_alu_1_out_5, n32x32register_1_out_8, n32x32register_1_out_9, ram_1_data, register_1_q,
       rom_1_data, shifter_2_out;

  Multiplexer #(.width(32)) multiplexer_1 (
    .in0(adder_1_out), .in1(adder_2_out), .out(multiplexer_1_out), .sel(and_1_out));  // open: en
  or or_1 (or_1_out, main_decoder_ultimate_1_jump, jal);
  Multiplexer #(.width(32)) multiplexer_2 (
    .in0(multiplexer_3_out), .in1(n32x32register_1_out_8), .out(multiplexer_2_out),
    .sel(main_decoder_ultimate_1_jr));  // open: en
  Multiplexer #(.width(32)) multiplexer_3 (
    .in0(multiplexer_1_out), .in1(jump_address_maker_1_out_3), .out(multiplexer_3_out), .sel(or_1_out));  // open: en
  Button button_1 (.out(button_1_out));
  Register #(.width(32)) register_1 (
    .D(multiplexer_2_out), .Q(register_1_q), .clk(button_1_out), .clr(clr));  // open: en
  Shifter #(.width(24), .shift("lr")) shifter_1 (.in(register_1_q[23:0]), .\dist (5'b00010), .out(shifter_1_out));
  Adder #(.width(32)) adder_1 (.a(register_1_q), .b(32'h4), .out(adder_1_out));  // open: cin, cout
  Jump_Address_Maker jump_address_maker_1 (
    .in_1(instruction_splitter_1_out_4), .in_2(register_1_q), .out_3(jump_address_maker_1_out_3));
  ROM #(.addrWidth(24), .dataWidth(32)) rom_1 (.addr(shifter_1_out), .data(rom_1_data));  // open: sel
  Instruction_Splitter instruction_splitter_1 (
    .in_1(rom_1_data), .Func(instruction_splitter_1_func), .out_3(instruction_splitter_1_out_3),
    .out_4(instruction_splitter_1_out_4), .rd(instruction_splitter_1_rd), .rt(instruction_splitter_1_rt),
    .rs(instruction_splitter_1_rs), .opCode(instruction_splitter_1_opcode));
  main_decoder_ultimate main_decoder_ultimate_1 (
    .OpCode(instruction_splitter_1_opcode), .jr(main_decoder_ultimate_1_jr),
    .Funct(instruction_splitter_1_func), .RegWrite(main_decoder_ultimate_1_regwrite),
    .RegDst(main_decoder_ultimate_1_regdst), .ALUSrc(main_decoder_ultimate_1_alusrc),
    .Branch(main_decoder_ultimate_1_branch), .MemWrite(main_decoder_ultimate_1_memwrite),
    .MemToReg(main_decoder_ultimate_1_memtoreg), .Jump(main_decoder_ultimate_1_jump), .Jal(jal),
    .ALU_Control(main_decoder_ultimate_1_alu_control));
  Multiplexer #(.width(5)) multiplexer_4 (
    .in0(instruction_splitter_1_rt), .in1(instruction_splitter_1_rd), .out(multiplexer_4_out),
    .sel(main_decoder_ultimate_1_regdst));  // open: en
  Multiplexer #(.width(5)) multiplexer_5 (
    .in0(multiplexer_4_out), .in1({5{1'b1}}), .out(multiplexer_5_out), .sel(jal));  // open: en
  Multiplexer #(.width(32)) multiplexer_6 (
    .in0(multiplexer_8_out), .in1(adder_1_out), .out(multiplexer_6_out), .sel(jal));  // open: en
  _32x32Register u_32x32register_1 (
    .Read_B(instruction_splitter_1_rt), .Read_A(instruction_splitter_1_rs),
    .in_3(main_decoder_ultimate_1_regwrite), .out_8(n32x32register_1_out_8), .out_9(n32x32register_1_out_9),
    .in_7(multiplexer_6_out), .in_6(button_1_out), .in_5(clr), .Selection(multiplexer_5_out));
  assign bit_extender_1_out = {{16{instruction_splitter_1_out_3[15]}}, instruction_splitter_1_out_3};  // Bit_Extender bit_extender_1
  Multiplexer #(.width(32)) multiplexer_7 (
    .in0(n32x32register_1_out_9), .in1(bit_extender_1_out), .out(multiplexer_7_out),
    .sel(main_decoder_ultimate_1_alusrc));  // open: en
  and and_1 (and_1_out, main_decoder_ultimate_1_branch, n32bit_alu_1_iszero);
  _32bit_ALU u_32bit_alu_1 (
    .in_1(n32x32register_1_out_8), .in_2(multiplexer_7_out), .out_5(n32bit_alu_1_out_5),
    .OpCode(main_decoder_ultimate_1_alu_control), .isZero(n32bit_alu_1_iszero));
  Shifter #(.width(32)) shifter_2 (.in(bit_extender_1_out), .\dist (5'b00010), .out(shifter_2_out));
  Adder #(.width(32)) adder_2 (.a(shifter_2_out), .b(adder_1_out), .out(adder_2_out));  // open: cin, cout
  RAM #(.addrWidth(24), .dataWidth(32), .bus("separate")) ram_1 (
    .addr(n32bit_alu_1_out_5[23:0]), .din(n32x32register_1_out_9), .data(ram_1_data),
    .str(main_decoder_ultimate_1_memwrite), .clk(button_1_out), .clr(clr));  // open: sel, ld
  Multiplexer #(.width(32)) multiplexer_8 (
    .in0(n32bit_alu_1_out_5), .in1(ram_1_data), .out(multiplexer_8_out),
    .sel(main_decoder_ultimate_1_memtoreg));  // open: en

  // Notes on the sheet:
  //   contents of rom_1 (hex, n*v repeats v):
  //   20080005 2009000a 200a0014 200b0028 1098020 20a8822 ac110040 8c120040 2499820
  //   ANJNEY LAWANIYA - 2402CS11
  //   ANJNEY LAWANIYA - 2402CS11
  //   Wish I could rotate
endmodule

module main_decoder_ultimate (
  input  [5:0] OpCode,
  input  [5:0] Funct,
  output RegWrite,
  output RegDst,
  output ALUSrc,
  output Branch,
  output jr,
  output MemWrite,
  output MemToReg,
  output Jump,
  output Jal,
  output [2:0] ALU_Control
);

  wire and_3_out, and_4_out, comparator_1_eq, comparator_2_eq, not_1_out, not_2_out, not_3_out, not_4_out,
       not_5_out, not_6_out, not_7_out, not_8_out, not_9_out, not_10_out;
  wire [1:1] and_7_out;

  Comparator #(.width(6)) comparator_1 (.a(OpCode), .b({6{1'b0}}), .eq(comparator_1_eq));  // open: gt, lt
  and and_1 (jr, comparator_1_eq, comparator_2_eq);
  Comparator #(.width(6)) comparator_2 (.a(Funct), .b(6'b001000), .eq(comparator_2_eq));  // open: gt, lt
  not not_1 (not_1_out, OpCode[2]);
  not not_2 (not_2_out, OpCode[1]);
  not not_3 (not_3_out, OpCode[3]);
  not not_4 (not_4_out, OpCode[3]);
  not not_5 (not_5_out, OpCode[2]);
  not not_6 (not_6_out, OpCode[1]);
  or or_1 (ALUSrc, OpCode[3], OpCode[5]);
  and and_2 (MemWrite, OpCode[5], OpCode[3]);
  not not_7 (not_7_out, OpCode[3]);
  not not_8 (not_8_out, OpCode[3]);
  not not_9 (not_9_out, OpCode[2]);
  not not_10 (not_10_out, OpCode[1]);
  and and_3 (and_3_out, not_1_out, not_2_out);
  and and_4 (and_4_out, not_3_out, OpCode[0]);
  and and_5 (RegDst, not_4_out, not_5_out, not_6_out);
  and and_6 (MemToReg, OpCode[5], not_7_out);
  and and_7 (and_7_out[1], not_8_out, not_9_out, not_10_out);
  or or_2 (RegWrite, and_3_out, and_4_out);
  Comparator #(.width(6), .mode("unsigned")) comparator_3 (.a(6'b000010), .b(OpCode), .eq(Jump));  // open: gt, lt
  Comparator #(.width(6)) comparator_4 (.a(OpCode), .b(6'b000011), .eq(Jal));  // open: gt, lt
  ALU_Decoder_ultimate alu_decoder_ultimate_1 (
    .ALUOp({and_7_out[1], OpCode[2]}), .Funct(Funct), .ALUControl(ALU_Control));

  assign Branch = OpCode[2];
endmodule

module ALU_Decoder_ultimate (
  input  [1:0] ALUOp,
  input  [5:0] Funct,
  output [2:0] ALUControl
);

  wire and_1_out, and_2_out, and_3_out, not_1_out, not_2_out;

  and and_1 (and_1_out, ALUOp[1], Funct[1]);
  not not_1 (not_1_out, ALUOp[1]);
  not not_2 (not_2_out, Funct[2]);
  and and_2 (and_2_out, ALUOp[1], Funct[0]);
  and and_3 (and_3_out, ALUOp[1], Funct[3]);
  or or_1 (ALUControl[2], ALUOp[0], and_1_out);
  or or_2 (ALUControl[1], not_1_out, not_2_out);
  or or_3 (ALUControl[0], and_2_out, and_3_out);
endmodule
