// Logisim project Logisim MIPS Piple Line Datapath.circ as structural Verilog: 9 circuits, main circuit main
module main (
);

  wire ALUSrc, ALUSrc_EX, Branch, Branch_EX, Branch_MEM, clk, Jump, MemRead, MemRead_EX, MemRead_MEM,
       MemToReg, MemToReg_EX, MemToReg_MEM, MemToReg_WB, MemWrite, MemWrite_EX, MemWrite_MEM, PCSrc_MEM,
       RegDest, RegDest_EX, RegWrite, RegWrite_EX, RegWrite_MEM, RegWrite_WB, Zero, Zero_MEM;
  wire [2:0] ALUOp, ALUOp_EX;
  wire [3:0] ALUControl;
  wire [4:0] _16_20, _21_25, ex_mem_1_writereg_2, id_ex_1_rd_2, id_ex_1_rt_2, mem_wb_1_writereg_2,
       multiplexer_4_out;
  wire [5:0] _0_5, _26_31;
  wire [15:0] _0_15;
  wire [31:0] _0_15_Extended, _0_25_Extended, adder_1_out, adder_2_out, ALUResult, ALUResult_MEM,
       ALUResult_WB, bit_extender_1_out, DMemOutput, DMemOutput_WB, ex_mem_1_branchaddress_2, Increment_PC,
       Increment_PC_EX, multiplexer_1_out, multiplexer_2_out, multiplexer_3_out, PC_q, ram_1_data, ReadData1,
       ReadData1_EX, ReadData2, ReadData2_EX, ReadData2_MEM, WriteData;
  wire [31:6] _0_15_Extended_EX;

  Multiplexer #(.width(32), .enable("false")) multiplexer_1 (
    .in0(adder_1_out), .in1(ex_mem_1_branchaddress_2), .out(multiplexer_1_out), .sel(PCSrc_MEM));
  Multiplexer #(.width(32), .enable("false")) multiplexer_2 (
    .in0(multiplexer_1_out), .in1(_0_25_Extended), .out(multiplexer_2_out), .sel(Jump));
  Register_part #(.width(32)) PC (.D(multiplexer_2_out), .Q(PC_q), .clk(clk));  // open: en, clr
  Clock clock_1 (.out(clk));
  Adder #(.width(32)) adder_1 (.a(PC_q), .b(32'h1), .out(adder_1_out));  // open: cin, cout
  RAM #(.addrWidth(24), .dataWidth(32)) ram_1 (
    .addr(PC_q[23:0]), .data(ram_1_data), .clk(clk), .ld(1'b1));  // open: sel, clr
  IF_ID if_id_1 (
    .Incremented_PC(adder_1_out), .Instuction(ram_1_data), .Incremented_PC_2(Increment_PC),
    .Instruction({_26_31, _21_25, _16_20, _0_15}));
  assign bit_extender_1_out = {{6{1'b0}}, {_21_25, _16_20, _0_15}};  // Bit_Extender bit_extender_1
  Shifter #(.width(32)) shifter_1 (.in(bit_extender_1_out), .\dist (5'b00010), .out(_0_25_Extended));
  Control control_1 (
    .IM(_26_31), .RegDest(RegDest), .Branch(Branch), .MemRead(MemRead), .MemtoReg(MemToReg), .ALUOp(ALUOp),
    .MemWrite(MemWrite), .ALUSrc(ALUSrc), .RegWrite(RegWrite), .jump(Jump));
  Register register_1 (
    .Write_Data(WriteData), .RegWrite(RegWrite_WB), .Read_Data_1(ReadData1), .Read_Data_2(ReadData2),
    .Read_Register_1(_21_25), .Read_Register_2(_16_20), .Write_Register(mem_wb_1_writereg_2));
  assign _0_15_Extended = {{16{1'b0}}, _0_15};  // Bit_Extender bit_extender_2
  ID_Ex id_ex_1 (
    .MemtoReg(MemToReg), .RegWrite(RegWrite), .RegDest(RegDest), .ALUOp(ALUOp), .ALUSrc(ALUSrc),
    .Branch(Branch), .MemWrite(MemWrite), .MemRead(MemRead), .IncrementedPC(Increment_PC),
    .ReadReg1(ReadData1), .ReadReg2(ReadData2), .SignExtendOffset(_0_15_Extended), .RT(_16_20),
    .RD(_0_15[15:11]), .MemtoReg_2(MemToReg_EX), .RegWrite_2(RegWrite_EX), .RegDest_2(RegDest_EX),
    .ALUOp_2(ALUOp_EX), .ALUSrc_2(ALUSrc_EX), .Branch_2(Branch_EX), .MemWrite_2(MemWrite_EX),
    .MemRead_2(MemRead_EX), .IncrementedPC_2(Increment_PC_EX), .ReadReg1_2(ReadData1_EX),
    .ReadReg2_2(ReadData2_EX), .SignExtendOffset_2({_0_15_Extended_EX, _0_5}), .RT_2(id_ex_1_rt_2),
    .RD_2(id_ex_1_rd_2));
  Multiplexer #(.width(32), .enable("false")) multiplexer_3 (
    .in0(ReadData2_EX), .in1({_0_15_Extended_EX, _0_5}), .out(multiplexer_3_out), .sel(ALUSrc_EX));
  ALU_Control alu_control_1 (.ALUop(ALUOp_EX), .\function (_0_5), .ALU_control(ALUControl));
  Multiplexer #(.width(5), .enable("false")) multiplexer_4 (
    .in0(id_ex_1_rt_2), .in1(id_ex_1_rd_2), .out(multiplexer_4_out), .sel(RegDest_EX));
  ALU alu_1 (
    .Input1(ReadData1_EX), .Input2(multiplexer_3_out), .Output(ALUResult), .ALU_control(ALUControl),
    .ZeroFlag(Zero), .Input3({_0_15_Extended_EX, _0_5}));
  Adder #(.width(32)) adder_2 (
    .a(Increment_PC_EX), .b({_0_15_Extended_EX, _0_5}), .out(adder_2_out));  // open: cin, cout
  Ex_Mem ex_mem_1 (
    .MemtoReg(MemToReg_EX), .RegWrite(RegWrite_EX), .Branch(Branch_EX), .MemWrite(MemWrite_EX),
    .MemRead(MemRead_EX), .BranchAddress(adder_2_out), .ZeroFlag(Zero), .ALUresult(ALUResult),
    .ValueMemWrite(ReadData2_EX), .WriteReg(multiplexer_4_out), .MemtoReg_2(MemToReg_MEM),
    .RegWrite_2(RegWrite_MEM), .Branch_2(Branch_MEM), .MemWrite_2(MemWrite_MEM), .MemRead_2(MemRead_MEM),
    .BranchAddress_2(ex_mem_1_branchaddress_2), .ZeroFlag_2(Zero_MEM), .ALUresult_2(ALUResult_MEM),
    .ValueMemWrite_2(ReadData2_MEM), .WriteReg_2(ex_mem_1_writereg_2));
  and and_1 (PCSrc_MEM, Zero_MEM, Branch_MEM);
  RAM #(.addrWidth(24), .dataWidth(32), .bus("separate")) ram_2 (
    .addr(ALUResult_MEM[23:0]), .din(ReadData2_MEM), .data(DMemOutput), .str(MemWrite_MEM), .clk(clk),
    .ld(MemRead_MEM));  // open: sel, clr
  Mem_WB mem_wb_1 (
    .MemtoReg(MemToReg_MEM), .RegWrite(RegWrite_MEM), .MemReadData(DMemOutput), .ALUresult(ALUResult_MEM),
    .WriteReg(ex_mem_1_writereg_2), .MemtoReg_2(MemToReg_WB), .RegWrite_2(RegWrite_WB),
    .MemReadData_2(DMemOutput_WB), .ALUresult_2(ALUResult_WB), .WriteReg_2(mem_wb_1_writereg_2));
  Multiplexer #(.width(32), .enable("false")) multiplexer_5 (
    .in0(ALUResult_WB), .in1(DMemOutput_WB), .out(WriteData), .sel(MemToReg_WB));

  // Other names for the same wires on the sheet: _11_15[4:0] = _0_15[15:11]; _0_15_Extended_EX[5:0] = _0_5
endmodule

module ALU (
  input  [31:0] Input1,
  input  [31:0] Input2,
  input  [31:0] Input3,
  input  [3:0] ALU_control,
  output [31:0] Output,
  output ZeroFlag
);

  wire and_2_out, and_3_out, comparator_1_lt, comparator_2_eq, comparator_3_eq, not_1_out, zero;
  wire [31:0] adder_1_out, AND_out, bit_extender_1_out, OR_out, shifter_1_out, shifter_2_out, shifter_3_out,
       subtractor_1_out;

  assign AND_out = Input1 & Input2;  // AND_Gate AND, 32 bits wide
  assign OR_out = Input1 | Input2;  // OR_Gate OR, 32 bits wide
  Adder #(.width(32)) adder_1 (.a(Input1), .b(Input2), .out(adder_1_out));  // open: cin, cout
  Shifter #(.width(32)) shifter_1 (.in(Input2), .\dist (Input3[10:6]), .out(shifter_1_out));
  Shifter #(.width(32), .shift("lr")) shifter_2 (.in(Input2), .\dist (Input3[10:6]), .out(shifter_2_out));
  Subtractor #(.width(32)) subtractor_1 (.a(Input1), .b(Input2), .out(subtractor_1_out));  // open: bin, bout
  Comparator #(.width(32)) comparator_1 (.a(Input1), .b(Input2), .eq(zero), .lt(comparator_1_lt));  // open: gt
  Shifter #(.width(32)) shifter_3 (.in(Input2), .\dist (5'b10000), .out(shifter_3_out));
  assign bit_extender_1_out = {{31{1'b0}}, comparator_1_lt};  // Bit_Extender bit_extender_1
  Multiplexer #(.select(4), .width(32), .enable("false")) multiplexer_1 (
    .in0(AND_out), .in1(OR_out), .in2(adder_1_out), .in3(shifter_1_out), .in4(shifter_2_out),
    .in5(subtractor_1_out), .in6(subtractor_1_out), .in7(bit_extender_1_out), .in8(shifter_3_out),
    .out(Output), .sel(ALU_control));  // open: in9, in10, in11, in12, in13, in14, in15
  Comparator #(.width(4)) comparator_2 (.a(ALU_control), .b(4'b0101), .eq(comparator_2_eq));  // open: gt, lt
  Comparator #(.width(4)) comparator_3 (.a(ALU_control), .b(4'b0110), .eq(comparator_3_eq));  // open: gt, lt
  not not_1 (not_1_out, zero);
  and and_2 (and_2_out, comparator_3_eq, zero);
  and and_3 (and_3_out, comparator_2_eq, not_1_out);
  or or_2 (ZeroFlag, and_3_out, and_2_out);
endmodule

module Register (
  input  [4:0] Read_Register_1,
  input  [4:0] Read_Register_2,
  input  [31:0] Write_Data,
  input  RegWrite,
  input  [4:0] Write_Register,
  output [31:0] Read_Data_1,
  output [31:0] Read_Data_2
);

  wire Clk, En0, En1, En2, En3, En4, En5, En6, En7, En8, En9, En10, En11, En12, En13, En14, En15, En16, En17,
       En18, En19, En20, En21, En22, En23, En24, En25, En26, En27, En28, En29, En30, En31;
  wire [31:0] Reg0, Reg1, Reg2, Reg3, Reg4, Reg5, Reg6, Reg7, Reg8, Reg9, Reg10, Reg11, Reg12, Reg13, Reg14,
       Reg15, Reg16, Reg17, Reg18, Reg19, Reg20, Reg21, Reg22, Reg23, Reg24, Reg25, Reg26, Reg27, Reg28,
       Reg29, Reg30, Reg31;

  Clock clock_1 (.out(Clk));
  Register_part #(.width(32)) register_1 (.D({32{1'b0}}), .Q(Reg0), .clk(Clk));  // open: en, clr
  Register_part #(.width(32)) register_2 (.D(Write_Data), .en(En1), .Q(Reg1), .clk(Clk));  // open: clr
  Register_part #(.width(32)) register_3 (.D(Write_Data), .en(En2), .Q(Reg2), .clk(Clk));  // open: clr
  Register_part #(.width(32)) register_4 (.D(Write_Data), .en(En3), .Q(Reg3), .clk(Clk));  // open: clr
  Register_part #(.width(32)) register_5 (.D(Write_Data), .en(En4), .Q(Reg4), .clk(Clk));  // open: clr
  Register_part #(.width(32)) register_6 (.D(Write_Data), .en(En5), .Q(Reg5), .clk(Clk));  // open: clr
  Register_part #(.width(32)) register_7 (.D(Write_Data), .en(En6), .Q(Reg6), .clk(Clk));  // open: clr
  Register_part #(.width(32)) register_8 (.D(Write_Data), .en(En7), .Q(Reg7), .clk(Clk));  // open: clr
  Register_part #(.width(32)) register_9 (.D(Write_Data), .en(En8), .Q(Reg8), .clk(Clk));  // open: clr
  Register_part #(.width(32)) register_10 (.D(Write_Data), .en(En9), .Q(Reg9), .clk(Clk));  // open: clr
  Register_part #(.width(32)) register_11 (.D(Write_Data), .en(En10), .Q(Reg10), .clk(Clk));  // open: clr
  Register_part #(.width(32)) register_12 (.D(Write_Data), .en(En11), .Q(Reg11), .clk(Clk));  // open: clr
  Register_part #(.width(32)) register_13 (.D(Write_Data), .en(En12), .Q(Reg12), .clk(Clk));  // open: clr
  Register_part #(.width(32)) register_14 (.D(Write_Data), .en(En13), .Q(Reg13), .clk(Clk));  // open: clr
  Register_part #(.width(32)) register_15 (.D(Write_Data), .en(En14), .Q(Reg14), .clk(Clk));  // open: clr
  Register_part #(.width(32)) register_16 (.D(Write_Data), .en(En15), .Q(Reg15), .clk(Clk));  // open: clr
  Decoder #(.select(5), .disabled(0)) decoder_1 (
    .out0(En0), .out1(En1), .out2(En2), .out3(En3), .out4(En4), .out5(En5), .out6(En6), .out7(En7),
    .out8(En8), .out9(En9), .out10(En10), .out11(En11), .out12(En12), .out13(En13), .out14(En14),
    .out15(En15), .out16(En16), .out17(En17), .out18(En18), .out19(En19), .out20(En20), .out21(En21),
    .out22(En22), .out23(En23), .out24(En24), .out25(En25), .out26(En26), .out27(En27), .out28(En28),
    .out29(En29), .out30(En30), .out31(En31), .sel(Write_Register), .en(RegWrite));
  Multiplexer #(.select(5), .width(32), .enable("false")) multiplexer_1 (
    .in0(Reg0), .in1(Reg1), .in2(Reg2), .in3(Reg3), .in4(Reg4), .in5(Reg5), .in6(Reg6), .in7(Reg7),
    .in8(Reg8), .in9(Reg9), .in10(Reg10), .in11(Reg11), .in12(Reg12), .in13(Reg13), .in14(Reg14),
    .in15(Reg15), .in16(Reg16), .in17(Reg17), .in18(Reg18), .in19(Reg19), .in20(Reg20), .in21(Reg21),
    .in22(Reg22), .in23(Reg23), .in24(Reg24), .in25(Reg25), .in26(Reg26), .in27(Reg27), .in28(Reg28),
    .in29(Reg29), .in30(Reg30), .in31(Reg31), .out(Read_Data_1), .sel(Read_Register_1));
  Multiplexer #(.select(5), .width(32), .enable("false")) multiplexer_2 (
    .in0(Reg0), .in1(Reg1), .in2(Reg2), .in3(Reg3), .in4(Reg4), .in5(Reg5), .in6(Reg6), .in7(Reg7),
    .in8(Reg8), .in9(Reg9), .in10(Reg10), .in11(Reg11), .in12(Reg12), .in13(Reg13), .in14(Reg14),
    .in15(Reg15), .in16(Reg16), .in17(Reg17), .in18(Reg18), .in19(Reg19), .in20(Reg20), .in21(Reg21),
    .in22(Reg22), .in23(Reg23), .in24(Reg24), .in25(Reg25), .in26(Reg26), .in27(Reg27), .in28(Reg28),
    .in29(Reg29), .in30(Reg30), .in31(Reg31), .out(Read_Data_2), .sel(Read_Register_2));
  Register_part #(.width(32)) register_17 (.D(Write_Data), .en(En16), .Q(Reg16), .clk(Clk));  // open: clr
  Register_part #(.width(32)) register_18 (.D(Write_Data), .en(En17), .Q(Reg17), .clk(Clk));  // open: clr
  Register_part #(.width(32)) register_19 (.D(Write_Data), .en(En18), .Q(Reg18), .clk(Clk));  // open: clr
  Register_part #(.width(32)) register_20 (.D(Write_Data), .en(En19), .Q(Reg19), .clk(Clk));  // open: clr
  Register_part #(.width(32)) register_21 (.D(Write_Data), .en(En20), .Q(Reg20), .clk(Clk));  // open: clr
  Register_part #(.width(32)) register_22 (.D(Write_Data), .en(En21), .Q(Reg21), .clk(Clk));  // open: clr
  Register_part #(.width(32)) register_23 (.D(Write_Data), .en(En22), .Q(Reg22), .clk(Clk));  // open: clr
  Register_part #(.width(32)) register_24 (.D(Write_Data), .en(En23), .Q(Reg23), .clk(Clk));  // open: clr
  Register_part #(.width(32)) register_25 (.D(Write_Data), .en(En24), .Q(Reg24), .clk(Clk));  // open: clr
  Register_part #(.width(32)) register_26 (.D(Write_Data), .en(En25), .Q(Reg25), .clk(Clk));  // open: clr
  Register_part #(.width(32)) register_27 (.D(Write_Data), .en(En26), .Q(Reg26), .clk(Clk));  // open: clr
  Register_part #(.width(32)) register_28 (.D(Write_Data), .en(En27), .Q(Reg27), .clk(Clk));  // open: clr
  Register_part #(.width(32)) register_29 (.D(Write_Data), .en(En28), .Q(Reg28), .clk(Clk));  // open: clr
  Register_part #(.width(32)) register_30 (.D(Write_Data), .en(En29), .Q(Reg29), .clk(Clk));  // open: clr
  Register_part #(.width(32)) register_31 (.D(Write_Data), .en(En30), .Q(Reg30), .clk(Clk));  // open: clr
  Register_part #(.width(32)) register_32 (.D(Write_Data), .en(En31), .Q(Reg31), .clk(Clk));  // open: clr

  // Other names for the same wires on the sheet: WData[31:0] = Write_Data
endmodule

module ALU_Control (
  input  [2:0] ALUop,
  input  [5:0] \function ,
  output [3:0] ALU_control
);

  wire add_out, and_out, beq_out, bne_out, lui_out, lw_sw_out, not_1_out, not_2_out, not_3_out, not_4_out,
       not_5_out, not_6_out, not_7_out, not_8_out, not_9_out, not_10_out, not_11_out, not_12_out, not_13_out,
       not_14_out, not_15_out, not_16_out, not_17_out, not_18_out, not_19_out, not_20_out, not_21_out,
       not_22_out, not_23_out, not_24_out, not_25_out, not_26_out, not_27_out, not_28_out, not_29_out,
       not_30_out, not_31_out, not_32_out, not_33_out, not_34_out, not_35_out, not_36_out, not_37_out,
       not_38_out, not_39_out, not_40_out, or_out, R_out, sll_out, slr_out, slti_out, sub_out;
  wire [3:0] controlled_buffer_5_out;

  not not_1 (not_1_out, ALUop[1]);
  not not_2 (not_2_out, ALUop[2]);
  not not_3 (not_3_out, ALUop[1]);
  not not_4 (not_4_out, ALUop[2]);
  not not_5 (not_5_out, ALUop[2]);
  not not_6 (not_6_out, ALUop[0]);
  not not_7 (not_7_out, ALUop[1]);
  not not_8 (not_8_out, ALUop[2]);
  not not_9 (not_9_out, \function [0]);
  not not_10 (not_10_out, \function [1]);
  not not_11 (not_11_out, \function [0]);
  not not_12 (not_12_out, \function [0]);
  not not_13 (not_13_out, \function [1]);
  not not_14 (not_14_out, \function [1]);
  not not_15 (not_15_out, \function [0]);
  not not_16 (not_16_out, \function [0]);
  not not_17 (not_17_out, \function [1]);
  not not_18 (not_18_out, \function [2]);
  not not_19 (not_19_out, \function [0]);
  not not_20 (not_20_out, \function [2]);
  not not_21 (not_21_out, ALUop[0]);
  and lw_sw (lw_sw_out, not_21_out, not_1_out, not_2_out);
  and beq (beq_out, ALUop[0], not_3_out, not_4_out);
  and bne (bne_out, ALUop[0], ALUop[1], not_5_out);
  and lui (lui_out, not_6_out, not_7_out, ALUop[2]);
  not not_22 (not_22_out, ALUop[0]);
  and R (R_out, not_22_out, ALUop[1], not_8_out);
  not not_23 (not_23_out, \function [2]);
  not not_24 (not_24_out, \function [3]);
  not not_25 (not_25_out, \function [2]);
  not not_26 (not_26_out, \function [3]);
  not not_27 (not_27_out, \function [3]);
  not not_28 (not_28_out, \function [3]);
  not not_29 (not_29_out, \function [2]);
  not not_30 (not_30_out, \function [3]);
  not not_31 (not_31_out, \function [4]);
  not not_32 (not_32_out, \function [5]);
  not not_33 (not_33_out, \function [3]);
  not not_34 (not_34_out, \function [4]);
  not not_35 (not_35_out, \function [5]);
  and add (add_out, not_9_out, not_10_out, not_23_out, not_24_out, not_36_out, \function [5]);
  not not_36 (not_36_out, \function [4]);
  and sub (sub_out, not_11_out, \function [1], not_25_out, not_26_out, not_37_out, \function [5]);
  not not_37 (not_37_out, \function [4]);
  and \and  (and_out, not_12_out, not_13_out, \function [2], not_27_out, not_38_out, \function [5]);
  not not_38 (not_38_out, \function [4]);
  and \or  (or_out, \function [0], not_14_out, \function [2], not_28_out, not_39_out, \function [5]);
  not not_39 (not_39_out, \function [4]);
  and slti (slti_out, not_15_out, \function [1], not_29_out, \function [3], not_40_out, \function [5]);
  not not_40 (not_40_out, \function [4]);
  and sll (sll_out, not_16_out, not_17_out, not_18_out, not_30_out, not_31_out, not_32_out);
  and slr (slr_out, not_19_out, \function [1], not_20_out, not_33_out, not_34_out, not_35_out);
  assign ALU_control = lw_sw_out ? 4'b0010 : 4'bz;  // Controlled_Buffer controlled_buffer_1
  assign ALU_control = beq_out ? 4'b0110 : 4'bz;  // Controlled_Buffer controlled_buffer_2
  assign ALU_control = bne_out ? 4'b0101 : 4'bz;  // Controlled_Buffer controlled_buffer_3
  assign ALU_control = lui_out ? 4'b1000 : 4'bz;  // Controlled_Buffer controlled_buffer_4
  assign controlled_buffer_5_out = add_out ? 4'b0010 : 4'bz;  // Controlled_Buffer controlled_buffer_5
  assign controlled_buffer_5_out = sub_out ? 4'b0110 : 4'bz;  // Controlled_Buffer controlled_buffer_6
  assign controlled_buffer_5_out = and_out ? 4'b0000 : 4'bz;  // Controlled_Buffer controlled_buffer_7
  assign controlled_buffer_5_out = or_out ? 4'b0001 : 4'bz;  // Controlled_Buffer controlled_buffer_8
  assign controlled_buffer_5_out = slti_out ? 4'b0111 : 4'bz;  // Controlled_Buffer controlled_buffer_9
  assign controlled_buffer_5_out = sll_out ? 4'b0011 : 4'bz;  // Controlled_Buffer controlled_buffer_10
  assign controlled_buffer_5_out = slr_out ? 4'b0100 : 4'bz;  // Controlled_Buffer controlled_buffer_11
  assign ALU_control = R_out ? controlled_buffer_5_out : 4'bz;  // Controlled_Buffer controlled_buffer_12

  // Other names for the same wires on the sheet: fnction[5:0] = \function 
endmodule

module Control (
  input  [5:0] IM,
  output RegDest,
  output Branch,
  output MemRead,
  output MemtoReg,
  output [2:0] ALUOp,
  output MemWrite,
  output ALUSrc,
  output RegWrite,
  output jump
);

  wire addi, beq, bne, lui, or_2_out;

  Comparator #(.width(6)) comparator_1 (.a(IM), .b({6{1'b0}}), .eq(RegDest));  // open: gt, lt
  Comparator #(.width(6)) comparator_2 (.a(IM), .b(6'b100011), .eq(MemRead));  // open: gt, lt
  Comparator #(.width(6)) comparator_3 (.a(IM), .b(6'b101011), .eq(MemWrite));  // open: gt, lt
  Comparator #(.width(6)) comparator_4 (.a(IM), .b(6'b000101), .eq(bne));  // open: gt, lt
  Comparator #(.width(6)) comparator_5 (.a(IM), .b(6'b000100), .eq(beq));  // open: gt, lt
  Comparator #(.width(6)) comparator_6 (.a(IM), .b(6'b000010), .eq(jump));  // open: gt, lt
  Comparator #(.width(6)) comparator_7 (.a(IM), .b(6'b001000), .eq(addi));  // open: gt, lt
  Comparator #(.width(6)) comparator_8 (.a(IM), .b(6'b001111), .eq(lui));  // open: gt, lt
  or or_1 (Branch, beq, bne);
  assign ALUOp = RegDest ? 3'b010 : 3'bz;  // Controlled_Buffer controlled_buffer_1
  assign ALUOp = or_2_out ? 3'b000 : 3'bz;  // Controlled_Buffer controlled_buffer_2
  or or_2 (or_2_out, MemRead, addi, MemWrite);
  assign ALUOp = beq ? 3'b001 : 3'bz;  // Controlled_Buffer controlled_buffer_3
  assign ALUOp = bne ? 3'b011 : 3'bz;  // Controlled_Buffer controlled_buffer_4
  assign ALUOp = lui ? 3'b100 : 3'bz;  // Controlled_Buffer controlled_buffer_5
  or or_3 (ALUSrc, MemRead, MemWrite, addi, lui);
  or or_4 (RegWrite, MemRead, RegDest, addi, lui);

  assign MemtoReg = MemRead;

  // Other names for the same wires on the sheet: j = jump; lw = MemRead; R = RegDest; sw = MemWrite
endmodule

module Ex_Mem (
  input  MemtoReg,
  input  RegWrite,
  input  Branch,
  input  MemWrite,
  input  MemRead,
  input  [31:0] BranchAddress,
  input  ZeroFlag,
  input  [31:0] ALUresult,
  input  [31:0] ValueMemWrite,
  input  [4:0] WriteReg,
  output MemtoReg_2,
  output RegWrite_2,
  output Branch_2,
  output MemWrite_2,
  output MemRead_2,
  output [31:0] BranchAddress_2,
  output ZeroFlag_2,
  output [31:0] ALUresult_2,
  output [31:0] ValueMemWrite_2,
  output [4:0] WriteReg_2
);

  wire clock_1_out;

  Clock clock_1 (.out(clock_1_out));
  Register_part #(.width(1)) WriteBack (.D(MemtoReg), .Q(MemtoReg_2), .clk(clock_1_out));  // open: en, clr
  Register_part #(.width(1)) WriteBack_2 (.D(RegWrite), .Q(RegWrite_2), .clk(clock_1_out));  // open: en, clr
  Register_part #(.width(1)) Mem (.D(Branch), .Q(Branch_2), .clk(clock_1_out));  // open: en, clr
  Register_part #(.width(1)) Mem_2 (.D(MemWrite), .Q(MemWrite_2), .clk(clock_1_out));  // open: en, clr
  Register_part #(.width(1)) Mem_3 (.D(MemRead), .Q(MemRead_2), .clk(clock_1_out));  // open: en, clr
  Register_part #(.width(32)) u_BranchAddress (
    .D(BranchAddress), .Q(BranchAddress_2), .clk(clock_1_out));  // open: en, clr
  Register_part #(.width(1)) u_ZeroFlag (.D(ZeroFlag), .Q(ZeroFlag_2), .clk(clock_1_out));  // open: en, clr
  Register_part #(.width(32)) u_ALUresult (.D(ALUresult), .Q(ALUresult_2), .clk(clock_1_out));  // open: en, clr
  Register_part #(.width(32)) u_ValueMemWrite (
    .D(ValueMemWrite), .Q(ValueMemWrite_2), .clk(clock_1_out));  // open: en, clr
  Register_part #(.width(5)) RT (.D(WriteReg), .Q(WriteReg_2), .clk(clock_1_out));  // open: en, clr
endmodule

module ID_Ex (
  input  MemtoReg,
  input  RegWrite,
  input  RegDest,
  input  [2:0] ALUOp,
  input  ALUSrc,
  input  Branch,
  input  MemWrite,
  input  MemRead,
  input  [31:0] IncrementedPC,
  input  [31:0] ReadReg1,
  input  [31:0] ReadReg2,
  input  [31:0] SignExtendOffset,
  input  [4:0] RT,
  input  [4:0] RD,
  output MemtoReg_2,
  output RegWrite_2,
  output RegDest_2,
  output [2:0] ALUOp_2,
  output ALUSrc_2,
  output Branch_2,
  output MemWrite_2,
  output MemRead_2,
  output [31:0] IncrementedPC_2,
  output [31:0] ReadReg1_2,
  output [31:0] ReadReg2_2,
  output [31:0] SignExtendOffset_2,
  output [4:0] RT_2,
  output [4:0] RD_2
);

  wire clock_1_out;

  Clock clock_1 (.out(clock_1_out));
  Register_part #(.width(1)) WriteBack (.D(MemtoReg), .Q(MemtoReg_2), .clk(clock_1_out));  // open: en, clr
  Register_part #(.width(1)) WriteBack_2 (.D(RegWrite), .Q(RegWrite_2), .clk(clock_1_out));  // open: en, clr
  Register_part #(.width(1)) Execute (.D(RegDest), .Q(RegDest_2), .clk(clock_1_out));  // open: en, clr
  Register_part #(.width(3)) Execute_2 (.D(ALUOp), .Q(ALUOp_2), .clk(clock_1_out));  // open: en, clr
  Register_part #(.width(1)) Execute_3 (.D(ALUSrc), .Q(ALUSrc_2), .clk(clock_1_out));  // open: en, clr
  Register_part #(.width(1)) Mem (.D(Branch), .Q(Branch_2), .clk(clock_1_out));  // open: en, clr
  Register_part #(.width(1)) Mem_2 (.D(MemWrite), .Q(MemWrite_2), .clk(clock_1_out));  // open: en, clr
  Register_part #(.width(1)) Mem_3 (.D(MemRead), .Q(MemRead_2), .clk(clock_1_out));  // open: en, clr
  Register_part #(.width(32)) Incremented_PC (
    .D(IncrementedPC), .Q(IncrementedPC_2), .clk(clock_1_out));  // open: en, clr
  Register_part #(.width(32)) u_ReadReg1 (.D(ReadReg1), .Q(ReadReg1_2), .clk(clock_1_out));  // open: en, clr
  Register_part #(.width(32)) u_ReadReg2 (.D(ReadReg2), .Q(ReadReg2_2), .clk(clock_1_out));  // open: en, clr
  Register_part #(.width(32)) u_SignExtendOffset (
    .D(SignExtendOffset), .Q(SignExtendOffset_2), .clk(clock_1_out));  // open: en, clr
  Register_part #(.width(5)) u_RT (.D(RT), .Q(RT_2), .clk(clock_1_out));  // open: en, clr
  Register_part #(.width(5)) u_RD (.D(RD), .Q(RD_2), .clk(clock_1_out));  // open: en, clr
endmodule

module IF_ID (
  input  [31:0] Incremented_PC,
  input  [31:0] Instuction,
  output [31:0] Incremented_PC_2,
  output [31:0] Instruction
);

  wire clock_1_out;

  Register_part #(.width(32)) u_Incremented_PC (
    .D(Incremented_PC), .Q(Incremented_PC_2), .clk(clock_1_out));  // open: en, clr
  Register_part #(.width(32)) u_Instruction (.D(Instuction), .Q(Instruction), .clk(clock_1_out));  // open: en, clr
  Clock clock_1 (.out(clock_1_out));
endmodule

module Mem_WB (
  input  MemtoReg,
  input  RegWrite,
  input  [31:0] MemReadData,
  input  [31:0] ALUresult,
  input  [4:0] WriteReg,
  output MemtoReg_2,
  output RegWrite_2,
  output [31:0] MemReadData_2,
  output [31:0] ALUresult_2,
  output [4:0] WriteReg_2
);

  wire clock_1_out;

  Clock clock_1 (.out(clock_1_out));
  Register_part #(.width(1)) WriteBack (.D(MemtoReg), .Q(MemtoReg_2), .clk(clock_1_out));  // open: en, clr
  Register_part #(.width(1)) WriteBack_2 (.D(RegWrite), .Q(RegWrite_2), .clk(clock_1_out));  // open: en, clr
  Register_part #(.width(32)) u_MemReadData (.D(MemReadData), .Q(MemReadData_2), .clk(clock_1_out));  // open: en, clr
  Register_part #(.width(32)) u_ALUresult (.D(ALUresult), .Q(ALUresult_2), .clk(clock_1_out));  // open: en, clr
  Register_part #(.width(5)) RT (.D(WriteReg), .Q(WriteReg_2), .clk(clock_1_out));  // open: en, clr
endmodule
